// Digital circuit Template-04.dig as structural Verilog
module Template_04 (
  input  [6:0] In,
  output [6:0] Output
);

  wire not_1_out, not_2_out, not_3_out, xor_1_out, xor_2_out, xor_3_out;
  wire [6:0] and_1_out;

  xor xor_1 (xor_1_out, In[3], In[4], In[5], In[6]);
  xor xor_2 (xor_2_out, In[1], In[2], In[5], In[6]);
  xor xor_3 (xor_3_out, In[0], In[2], In[4], In[6]);
  not not_1 (not_1_out, xor_1_out);
  not not_2 (not_2_out, xor_2_out);
  not not_3 (not_3_out, xor_3_out);
  and and_1 (and_1_out[0], not_1_out, not_2_out, xor_3_out);
  and and_2 (and_1_out[1], not_1_out, xor_2_out, not_3_out);
  and and_3 (and_1_out[2], not_1_out, xor_2_out, xor_3_out);
  and and_4 (and_1_out[3], xor_1_out, not_2_out, not_3_out);
  and and_5 (and_1_out[4], xor_1_out, not_2_out, xor_3_out);
  and and_6 (and_1_out[5], xor_1_out, xor_2_out, not_3_out);
  and and_7 (and_1_out[6], xor_1_out, xor_2_out, xor_3_out);
  assign Output = In ^ and_1_out;  // XOr xor_4, 7 bits wide
endmodule
