// Digital circuit item.dig as structural Verilog
module item (
  input  [3:0] In,
  output out_2,
  output out_3,
  output out_4,
  output out_5,
  output out_6,
  output out_7,
  output out_8
);

  wire and_1_out, and_2_out, and_3_out, and_4_out, and_5_out, and_6_out, and_7_out, and_8_out, and_9_out,
       not_1_out, not_2_out, not_3_out, not_4_out;

  not not_1 (not_1_out, In[3]);
  not not_2 (not_2_out, In[2]);
  not not_3 (not_3_out, In[0]);
  not not_4 (not_4_out, In[1]);
  and and_1 (and_1_out, not_2_out, not_3_out);
  and and_2 (and_2_out, not_4_out, not_3_out);
  and and_3 (and_3_out, not_2_out, In[1]);
  and and_4 (and_4_out, In[2], not_4_out);
  and and_5 (and_5_out, In[2], In[0]);
  and and_6 (and_6_out, In[1], In[0]);
  and and_7 (and_7_out, In[1], not_3_out);
  and and_8 (and_8_out, In[2], not_3_out);
  and and_9 (and_9_out, In[2], not_4_out, In[0]);
  or or_1 (out_2, In[3], In[1], and_1_out, and_5_out);
  or or_2 (out_3, not_2_out, and_2_out, and_6_out);
  or or_3 (out_4, not_4_out, In[0], In[2]);
  or or_4 (out_5, In[3], and_1_out, and_3_out, and_9_out, and_7_out);
  or or_5 (out_6, and_1_out, and_7_out);
  or or_6 (out_7, and_2_out, and_4_out, and_8_out, In[3]);
  or or_7 (out_8, and_3_out, and_4_out, In[3], and_7_out);
  Seven_Seg seven_seg_1 (.a(out_2), .b(out_3), .c(out_4), .d(out_5), .e(out_6), .f(out_7), .g(out_8), .dp(1'b0));
endmodule
