// Digital circuit main.dig as structural Verilog
module main (
  input  [2:0] In,
  output [7:0] Z
);

  wire and_1_out, and_2_out, and_3_out, and_4_out, and_5_out, and_6_out, and_7_out, and_8_out, and_9_out,
       and_10_out, and_11_out, not_1_out, not_2_out, not_3_out;

  not not_1 (not_1_out, In[2]);
  not not_2 (not_2_out, In[1]);
  not not_3 (not_3_out, In[0]);
  and and_1 (and_1_out, not_1_out, In[1], not_3_out);
  and and_2 (and_2_out, In[2], not_3_out);
  and and_3 (and_3_out, not_1_out, not_2_out, In[0]);
  and and_4 (and_4_out, In[2], In[1], In[0]);
  and and_5 (and_5_out, not_1_out, In[0]);
  and and_6 (and_6_out, In[2], not_2_out);
  and and_7 (and_7_out, not_1_out, In[1]);
  and and_8 (and_8_out, not_1_out, not_3_out);
  and and_9 (and_9_out, In[2], not_2_out, not_3_out);
  and and_10 (and_10_out, In[2], not_3_out);
  and and_11 (and_11_out, In[1], not_3_out);
  or or_1 (Z[5], and_1_out, and_2_out, and_3_out, and_4_out);
  or or_2 (Z[3], and_5_out, and_6_out);
  or or_3 (Z[2], and_7_out, and_6_out, and_8_out);
  or or_4 (Z[1], and_1_out, and_9_out, and_4_out);
  or or_5 (Z[0], and_10_out, and_11_out, and_3_out);

  assign {Z[7:6], Z[4]} = 3'b010;

  // Other names for the same wires on the sheet: b0 = Z[0]; b1 = Z[1]; b2 = Z[2]; b3 = Z[3]; b5 = Z[5]
endmodule
