// Digital circuit main.dig as structural Verilog
module main (
  input  [3:0] In,
  input  [1:0] Selector,
  output [3:0] out_3
);

  wire add_2_c_o, add_3_c_o, add_4_c_o, add_5_c_o, add_6_c_o, add_7_c_o, add_8_c_o, and_1_out, and_2_out,
       and_3_out, and_4_out, and_5_out, and_6_out, and_7_out, and_8_out, and_9_out, and_10_out,
       comparator_1_lt, not_1_out, not_2_out, not_3_out, not_4_out;
  wire [2:0] cyclic;
  wire [3:0] _2_4_2_1, _6_4_2__3, add_1_s, excess_3;

  Add add_1 (.a(In[3]), .b(1'b0), .c_i(add_4_c_o), .s(add_1_s[3]));  // open: c_o
  Add add_2 (.a(In[3]), .b(1'b0), .c_i(add_3_c_o), .s(excess_3[3]), .c_o(add_2_c_o));
  Add add_3 (.a(In[2]), .b(1'b0), .c_i(add_5_c_o), .s(excess_3[2]), .c_o(add_3_c_o));
  xor xor_1 (cyclic[2], In[3], In[2]);
  Add add_4 (.a(In[2]), .b(1'b1), .c_i(add_6_c_o), .s(add_1_s[2]), .c_o(add_4_c_o));
  Add add_5 (.a(In[1]), .b(1'b1), .c_i(add_7_c_o), .s(excess_3[1]), .c_o(add_5_c_o));
  xor xor_2 (cyclic[1], In[2], In[1]);
  xor xor_3 (cyclic[0], In[1], In[0]);
  Add add_6 (.a(In[1]), .b(1'b1), .c_i(add_8_c_o), .s(add_1_s[1]), .c_o(add_6_c_o));
  Add add_7 (.a(In[0]), .b(1'b1), .c_i(1'b0), .s(excess_3[0]), .c_o(add_7_c_o));
  Add add_8 (.a(In[0]), .b(1'b0), .c_i(1'b0), .s(add_1_s[0]), .c_o(add_8_c_o));
  Comparator #(.Bits(4)) comparator_1 (.a(In), .b(4'b0101), .lt(comparator_1_lt));  // open: gt, eq
  Multiplexer #(.Bits(4)) multiplexer_1 (.sel(comparator_1_lt), .in_0(add_1_s), .in_1(In), .out(_2_4_2_1));
  Multiplexer #(.Bits(4), .Selector_Bits(2)) multiplexer_2 (
    .sel(Selector), .in_0(excess_3), .in_1({In[3], cyclic}), .in_2(_2_4_2_1), .in_3(_6_4_2__3), .out(out_3));
  not not_1 (not_1_out, In[3]);
  not not_2 (not_2_out, In[2]);
  not not_3 (not_3_out, In[1]);
  not not_4 (not_4_out, In[0]);
  and and_1 (and_1_out, not_1_out, In[1], In[0]);
  and and_2 (and_2_out, In[3], not_2_out, not_3_out);
  and and_3 (and_3_out, not_1_out, In[2], not_3_out, In[0]);
  and and_4 (and_4_out, In[3], not_2_out, not_3_out, In[0]);
  and and_5 (and_5_out, not_1_out, In[2], not_4_out);
  and and_6 (and_6_out, not_1_out, In[2], In[1]);
  and and_7 (and_7_out, not_2_out, not_3_out, In[0]);
  and and_8 (and_8_out, In[3], not_2_out, not_3_out);
  and and_9 (and_9_out, not_1_out, In[1], not_4_out);
  and and_10 (and_10_out, not_1_out, In[0]);
  or or_1 (_6_4_2__3[3], and_1_out, and_2_out, and_3_out, and_4_out);
  or or_2 (_6_4_2__3[2], and_5_out, and_6_out, and_7_out);
  or or_3 (_6_4_2__3[1], and_8_out, and_9_out, and_3_out);
  or or_4 (_6_4_2__3[0], and_7_out, and_10_out);
  // also tied to GND on the sheet: add_2_c_o

  // Other names for the same wires on the sheet: b0 = In[0]; b1 = In[1]; b2 = In[2]; b3 = In[3]; cyclic[3] = In[3];
  //   sel[1:0] = Selector
endmodule
