// Digital circuit adv_gcd.dig as structural Verilog
module adv_gcd (
  input  [7:0] A,
  input  [7:0] B,
  input  start,
  input  clear,
  input  clk,
  output busy,
  output [7:0] \output 
);

  wire A0, A1, A2, A3, a_eq_b, a_gt_b, a_lt_b, and_1_out, and_2_out, multiplexer_1_out, multiplexer_2_out,
       not_2_out, or_1_out, or_2_out, Qa, Qb;
  wire [7:0] a_t, b_t, multiplexer_3_out, multiplexer_4_out, sub_1_s, sub_2_s;

  Multiplexer #(.Selector_Bits(2)) multiplexer_1 (
    .sel({Qa, Qb}), .in_0(start), .in_1(1'b1), .in_2(a_lt_b), .in_3(1'b1), .out(multiplexer_1_out));
  and and_1 (and_1_out, ~clear, multiplexer_1_out);  // And
  Decoder #(.Selector_Bits(2)) decoder_1 (.sel({Qa, Qb}), .out_0(A0), .out_1(A2), .out_2(A1), .out_3(A3));
  D_FF d_ff_1 (.D(and_1_out), .C(clk), .Q(Qa));  // open: nQ
  not not_1 (busy, A0);
  not not_2 (not_2_out, a_eq_b);
  Comparator #(.Bits(8)) comp (.a(a_t), .b(b_t), .gt(a_gt_b), .eq(a_eq_b), .lt(a_lt_b));
  Multiplexer #(.Selector_Bits(2)) multiplexer_2 (
    .sel({Qa, Qb}), .in_0(1'b0), .in_1(1'b0), .in_2(not_2_out), .in_3(1'b0), .out(multiplexer_2_out));
  or or_1 (or_1_out, A0, A2);
  and and_2 (and_2_out, ~clear, multiplexer_2_out);  // And
  Sub #(.Bits(8)) sub_1 (.a(a_t), .b(b_t), .c_i(1'b0), .s(sub_1_s));  // open: c_o
  Multiplexer #(.Bits(8)) multiplexer_3 (.sel(A2), .in_0(A), .in_1(sub_1_s), .out(multiplexer_3_out));
  Register #(.Bits(8)) RegA (.D(multiplexer_3_out), .C(clk), .en(or_1_out), .Q(a_t));
  D_FF d_ff_2 (.D(and_2_out), .C(clk), .Q(Qb));  // open: nQ
  Register #(.Bits(8)) RegOutput (.D(a_t), .C(clk), .en(A1), .Q(\output ));
  or or_2 (or_2_out, A0, A3);
  Sub #(.Bits(8)) sub_2 (.a(b_t), .b(a_t), .c_i(1'b0), .s(sub_2_s));  // open: c_o
  Register #(.Bits(8)) RegB (.D(multiplexer_4_out), .C(clk), .en(or_2_out), .Q(b_t));
  Multiplexer #(.Bits(8)) multiplexer_4 (.sel(A3), .in_0(B), .in_1(sub_2_s), .out(multiplexer_4_out));
  Seven_Seg_Hex seven_seg_hex_1 (.d(\output [7:4]), .dp(1'b0));
  Seven_Seg_Hex seven_seg_hex_2 (.d(\output [3:0]), .dp(1'b0));
endmodule

/* Test case:
A B start clear clk busy output
0xF 0x6 0 0 0 0 0
0xF 0x6 0 0 1 X 0
0xF 0x6 1 0 0 X 0
0xF 0x6 1 0 1 X 0
0xF 0x6 1 0 0 X 0
loop(x,1000)
0xF 0x6 0 0 1 X X
0xF 0x6 0 0 0 X X
end loop
0xF 0x6 0 0 0 0 0x3
*/
