// Digital circuit gcd_template.dig as structural Verilog
module gcd_template (
  input  [7:0] A,
  input  [7:0] B,
  input  start,
  input  clear,
  input  clk,
  output busy,
  output [7:0] \output 
);

  wire cl, comparator_1_eq, driverinvsel_1_out, gt, lt, or_1_out;
  wire [7:0] A_B, a_t, B_A, b_t, d_ff_1_q, d_ff_2_q, d_ff_3_q, d_ff_4_q, multiplexer_1_out,
       multiplexer_2_out, multiplexer_3_out, multiplexer_4_out, multiplexer_5_out, multiplexer_6_out;

  Multiplexer #(.Bits(8)) multiplexer_1 (.sel(clear), .in_0(B), .in_1({8{1'b0}}), .out(multiplexer_1_out));
  Multiplexer #(.Bits(8)) multiplexer_2 (.sel(clear), .in_0(A), .in_1({8{1'b0}}), .out(multiplexer_2_out));
  assign driverinvsel_1_out = ~busy ? start : 1'bz;  // DriverInvSel driverinvsel_1
  D_FF #(.Bits(8)) d_ff_1 (.D(multiplexer_2_out), .C(driverinvsel_1_out), .Q(d_ff_1_q));  // open: nQ
  D_FF #(.Bits(8)) d_ff_2 (.D(multiplexer_1_out), .C(driverinvsel_1_out), .Q(d_ff_2_q));  // open: nQ
  Multiplexer #(.Bits(8)) multiplexer_3 (.sel(gt), .in_0(a_t), .in_1(A_B), .out(multiplexer_3_out));
  Multiplexer #(.Bits(8)) multiplexer_4 (.sel(lt), .in_0(b_t), .in_1(B_A), .out(multiplexer_4_out));
  D_FF #(.Bits(8)) d_ff_3 (.D(multiplexer_3_out), .C(cl), .Q(d_ff_3_q));  // open: nQ
  D_FF #(.Bits(8)) d_ff_4 (.D(multiplexer_4_out), .C(cl), .Q(d_ff_4_q));  // open: nQ
  Multiplexer #(.Bits(8)) multiplexer_5 (.sel(busy), .in_0(d_ff_1_q), .in_1(d_ff_3_q), .out(multiplexer_5_out));
  Multiplexer #(.Bits(8)) multiplexer_6 (.sel(busy), .in_0(d_ff_2_q), .in_1(d_ff_4_q), .out(multiplexer_6_out));
  Multiplexer #(.Bits(8)) multiplexer_7 (.sel(busy), .in_0(b_t), .in_1({8{1'b0}}), .out(\output ));
  D_FF #(.Bits(8)) d_ff_5 (.D(multiplexer_5_out), .C(~cl), .Q(a_t));  // open: nQ
  D_FF #(.Bits(8)) d_ff_6 (.D(multiplexer_6_out), .C(~cl), .Q(b_t));  // open: nQ
  or or_1 (or_1_out, start, busy);
  Comparator #(.Bits(8)) comparator_1 (.a(a_t), .b(b_t), .gt(gt), .eq(comparator_1_eq), .lt(lt));
  and and_1 (cl, or_1_out, clk);
  not not_1 (busy, comparator_1_eq);
  Sub #(.Bits(8)) sub_1 (.a(a_t), .b(b_t), .c_i(1'b0), .s(A_B));  // open: c_o
  Sub #(.Bits(8)) sub_2 (.a(b_t), .b(a_t), .c_i(1'b0), .s(B_A));  // open: c_o

  // Other names for the same wires on the sheet: on = busy
endmodule

/* Test case:
A B start clear clk busy output
0xF 0x6 0 0 0 0 0
0xF 0x6 0 0 1 X 0
0xF 0x6 1 0 0 X 0
0xF 0x6 1 0 1 X 0
0xF 0x6 1 0 0 X 0
loop(x,1000)
0xF 0x6 0 0 1 X X
0xF 0x6 0 0 0 X X
end loop
0xF 0x6 0 0 0 0 0x3
*/
