// Digital circuit template.dig as structural Verilog
module template (
  input  reset,
  input  clk,
  output A,
  output B,
  output C
);

  wire and_1_out, and_2_out, and_3_out, and_4_out, and_5_out, and_6_out, and_7_out, not_1_out, or_1_out,
       or_2_out;

  not not_1 (not_1_out, reset);
  and and_1 (and_1_out, or_1_out, not_1_out);
  and and_2 (and_2_out, or_2_out, not_1_out);
  and and_3 (and_3_out, and_7_out, not_1_out);
  D_FF d_ff_1 (.D(and_1_out), .C(clk), .Q(C));  // open: nQ
  D_FF d_ff_2 (.D(and_2_out), .C(clk), .Q(B));  // open: nQ
  D_FF d_ff_3 (.D(and_3_out), .C(clk), .Q(A));  // open: nQ
  and and_4 (and_4_out, C, ~B, A);  // And
  and and_5 (and_5_out, ~C, B, A);  // And
  and and_6 (and_6_out, ~C, ~A);  // And
  and and_7 (and_7_out, ~C, B);  // And
  or or_1 (or_1_out, and_4_out, and_5_out);
  or or_2 (or_2_out, and_4_out, and_6_out);
endmodule

/* Test case:
clk reset C B A
0 0 0 0 0 
0 1 0 0 0
1 1 0 0 0
0 0 0 0 0
1 0 0 1 0
0 0 0 1 0
1 0 0 1 1
0 0 0 1 1
1 0 1 0 1
0 0 1 0 1
1 0 1 1 0
0 0 1 1 0
1 0 0 0 0
0 0 0 0 0
1 0 0 1 0
0 0 0 1 0
1 0 0 1 1
0 0 0 1 1
1 0 1 0 1
0 0 1 0 1
1 0 1 1 0
0 0 1 1 0
1 0 0 0 0
0 0 0 0 0
*/
