// Digital circuit ALU.dig as structural Verilog
module ALU (
  input  [7:0] accA,
  input  [7:0] accB,
  input  [3:0] opcode,
  output [7:0] ALU
);

  wire or_1_out;
  wire [7:0] A, A_B, A_lt__lt_B, AND, barrelshifter_1_out, DIFF, DIV, MOD, MUL, OR, SUM, XOR;

  or or_1 (or_1_out, accB[4], accB[5], accB[6], accB[7]);
  assign AND = accA & accB;  // And and_1, 8 bits wide
  assign OR = accA | accB;  // Or or_2, 8 bits wide
  assign XOR = accA ^ accB;  // XOr xor_1, 8 bits wide
  Add #(.Bits(8)) add_1 (.a(accA), .b(accB), .c_i(1'b0), .s(SUM));  // open: c_o
  Sub #(.Bits(8)) sub_1 (.a(accA), .b(accB), .c_i(1'b0), .s(DIFF));  // open: c_o
  Mul #(.Bits(4)) mul_1 (.a(accA[3:0]), .b(accB[3:0]), .mul(MUL));
  Div #(.Bits(8)) divide (.a(accA), .b(accB), .q(DIV));  // open: r
  Div #(.Bits(8)) u_mod (.a(accA), .b(accB), .q(MOD));  // open: r
  exponent exponent_1 (.B(accB[2:0]), .A(accA[2:0]), .A_B(A_B));
  assign A = ~accA;  // Not not_1, 8 bits wide
  BarrelShifter #(.Bits(8), .barrelShifterMode("arithmetic")) barrelshifter_1 (
    .in(accA), .shift(accB[3:0]), .out(barrelshifter_1_out));
  Multiplexer #(.Bits(8)) multiplexer_1 (
    .sel(or_1_out), .in_0(barrelshifter_1_out), .in_1({8{1'b0}}), .out(A_lt__lt_B));
  Multiplexer #(.Selector_Bits(4), .Bits(8)) multiplexer_2 (
    .sel(opcode), .in_0({8{1'b0}}), .in_1(SUM), .in_2(DIFF), .in_3(MUL), .in_4(DIV), .in_5(MOD), .in_6(A_B),
    .in_7({8{1'b0}}), .in_8(A), .in_9(AND), .in_10(OR), .in_11(XOR), .in_12(A_lt__lt_B), .in_13({8{1'b0}}),
    .in_14({8{1'b0}}), .in_15({8{1'b0}}), .out(ALU));
endmodule
