// Digital circuit DigLo67_Project_Full-150925 (1).dig as structural Verilog
module DigLo67_Project_Full_150925__1 (
  input  [7:0] M,
  input  [7:0] N,
  input  [12:0] progIN,
  input  reset,
  input  progLoad,
  input  start,
  input  result,
  input  clk,
  output valid,
  output done,
  output [7:0] \output ,
  output [12:0] out_12,
  output [7:0] out_13,
  output [7:0] out_14,
  output [7:0] out_15,
  output [7:0] out_16,
  output [7:0] out_17,
  output busy,
  output [15:0] out_19,
  output [15:0] out_20,
  output [7:0] _8
);

  wire _00000, _00001, _00010, _00011, _00100, _00101, _00110, _00111, _01000, _01001, _01010, _01011,
       _01100, _01101, _01110, _01111, _10000, _10001, _10010, _10011, _10100, _10101, _10110, _10111,
       _10111__11101__re, _10111__re, _11000, _11001, _11010, _11011, _11100, _11101, _11110, _11110__reset,
       _11110__stop, _11110_process, _11110_process__re, _11111, add1, add2, addpRAMAd, addrRAMAd, and_4_out,
       and_5_out, and_6_out, and_10_out, and_13_out, and_14_out, and_15_out, and_16_out, and_17_out,
       and_18_out, and_19_out, and_20_out, CanLoadA, CanloadA__re, CanLoadB, CanloadB__re, CanLoadC,
       CanloadC__re, clearpRAMAd, clearrRAMAd, CMP_eq, comparator_4_eq, d_ff_7_nq, d_ff_8_nq, d_ff_8_q,
       Data_Process, Done_Qa, Done_Qc, driverinvsel_1_out, endswap, equal, equal_flag, greater, greater_flag,
       Idle, jump, jump__11111, ldpRAM, ldrRAM, lesser, lesser_flag, LongProcess, multiplexer_1_out,
       multiplexer_3_out, multiplexer_4_out, multiplexer_5_out, not_1_out, not_2_out, not_3_out, not_4_out,
       not_5_out, not_6_out, not_7_out, notAnyInput, opCode_eq__eq_11111, or_1_out, or_7_out, or_26_out,
       or_27_out, or_28_out, or_29_out, or_31_out, Outputing, Outputing__re, pRAMAd_eq__eq_255, prime_check,
       process__re, Qa, Qb, Qc, reset__result, Reseting, result__valid__done, rRAMAd_eq__eq_16, setpRAMad,
       stop, strpRAM, strrRAM, timetoreset, togreater_flag, tolesser_flag, torequal_flag, Valid_ed;
  wire [4:0] opCode;
  wire [7:0] _1ArRAM, _2ArRAM, a, accA____accB, accA____accB_t, accA____accB_t_t, accA___accB,
       accA__lt__lt__accB, accA__plus__accB, accA_AND_accB, accA_OR_accB, accA_XOR_accB, and_21_out,
       and_22_out, and_23_out, and_24_out, b, dataA, dataB, dataC, DatapRAM, DatarRAM, DatarRAM1D,
       multiplexer_13_out, multiplexer_14_out, multiplexer_15_out, multiplexer_16_out, multiplexer_18_out,
       multiplexer_23_out, multiplexer_30_out, multiplexer_31_out, NOT_accA, operand, pRAM_Adress_1A,
       presetto, reg0x00, register_1_q, register_2_q, regoperand, rRAMData, sub_2_s, sub_3_s, toaccA, toaccB,
       tooutput, toregC, toswap0x00, toswapoperand;
  wire [7:7] a__gt__b, a__lt__b;
  wire [12:0] _2D;
  wire [12:8] pRAM_d1;
  wire [15:0] mul_1_mul;

  Multiplexer multiplexer_1 (.sel(_01011), .in_0(clk), .in_1(not_1_out), .out(multiplexer_1_out));
  not not_1 (not_1_out, clk);
  Decoder #(.Selector_Bits(3)) decoder_1 (
    .sel({Qa, Qb, Qc}), .out_0(Idle), .out_1(setpRAMad), .out_2(Data_Process), .out_3(Valid_ed),
    .out_4(Outputing), .out_5(done), .out_6(Reseting), .out_7(LongProcess));
  Multiplexer #(.Bits(8)) multiplexer_2 (.sel(Data_Process), .in_0(out_13), .in_1(operand), .out(pRAM_Adress_1A));
  RAMDualAccess #(.AddrBits(8), .Bits(13)) pRAM (
    .str(strpRAM), .C(clk), .ld(ldpRAM), .A1(pRAM_Adress_1A), .Din1(progIN), .A2(out_13),
    .D1({pRAM_d1, DatapRAM}), .D2(_2D));
  Register #(.Bits(13)) Operate (.D(out_12), .C(clk), .en(process__re), .Q({opCode, operand}));
  RAMDualAccess #(.AddrBits(8), .Bits(8)) rRAM (
    .str(strrRAM), .C(multiplexer_1_out), .ld(ldrRAM), .A1(_1ArRAM), .Din1(rRAMData), .A2(_2ArRAM),
    .D1(DatarRAM1D), .D2(DatarRAM));
  not not_2 (not_2_out, rRAMAd_eq__eq_16);
  not not_3 (not_3_out, endswap);
  Multiplexer #(.Selector_Bits(3)) multiplexer_3 (
    .sel({Qa, Qb, Qc}), .in_0(reset), .in_1(reset), .in_2(_11110__reset), .in_3(reset__result), .in_4(1'b1),
    .in_5(Done_Qa), .in_6(not_2_out), .in_7(not_3_out), .out(multiplexer_3_out));
  or or_1 (or_1_out, Valid_ed, done);
  or or_2 (stop, opCode_eq__eq_11111, pRAMAd_eq__eq_255);
  or or_3 (reset__result, result, reset);
  or or_4 (Done_Qa, result, notAnyInput, reset);
  D_FF d_ff_1 (.D(multiplexer_3_out), .C(clk), .Q(Qa));  // open: nQ
  and and_1 (strpRAM, progLoad, Idle);
  or or_5 (ldpRAM, Data_Process, setpRAMad);
  or or_6 (addpRAMAd, strpRAM, Data_Process);
  and and_2 (result__valid__done, or_1_out, result);
  or or_7 (or_7_out, add1, add2);
  and and_3 (notAnyInput, ~progLoad, ~start, ~result, ~reset);  // And
  or or_8 (Done_Qc, notAnyInput, start);
  or or_9 (_11110__reset, _11110, reset);
  Multiplexer #(.Selector_Bits(3)) multiplexer_4 (
    .sel({Qa, Qb, Qc}), .in_0(reset), .in_1(1'b1), .in_2(1'b1), .in_3(not_4_out), .in_4(reset), .in_5(reset),
    .in_6(not_5_out), .in_7(1'b1), .out(multiplexer_4_out));
  not not_4 (not_4_out, result);
  not not_5 (not_5_out, rRAMAd_eq__eq_16);
  and and_4 (and_4_out, LongProcess, or_7_out);
  and and_5 (and_5_out, Outputing, reset);
  or or_10 (_11110__stop, _11110, stop);
  D_FF d_ff_2 (.D(multiplexer_4_out), .C(clk), .Q(Qb));  // open: nQ
  or or_11 (clearpRAMAd, setpRAMad, done, Reseting);
  or or_12 (clearrRAMAd, and_5_out, rRAMAd_eq__eq_16);
  or or_13 (strrRAM, timetoreset, and_4_out, _01011);
  or or_14 (timetoreset, Reseting, reset);
  CounterPreset #(.maxValue(255), .Bits(8)) pRAM_Adress (
    .en(addpRAMAd), .C(~clk), .dir(1'b0), .in(presetto), .ld(jump__11111), .clr(clearpRAMAd), .out(out_13));  // open: ovf
  CounterPreset #(.maxValue(255), .Bits(8)) rRAM_Adress (
    .en(addrRAMAd), .C(~clk), .dir(1'b0), .in({8{1'b0}}), .ld(1'b0), .clr(clearrRAMAd), .out(out_14));  // open: ovf
  not not_6 (not_6_out, reset__result);
  Multiplexer #(.Selector_Bits(3)) multiplexer_5 (
    .sel({Qa, Qb, Qc}), .in_0(start), .in_1(1'b0), .in_2(_11110__stop), .in_3(not_6_out),
    .in_4(rRAMAd_eq__eq_16), .in_5(Done_Qc), .in_6(1'b0), .in_7(not_7_out), .out(multiplexer_5_out));
  not not_7 (not_7_out, endswap);
  Comparator #(.Bits(5)) comparator_1 (.a(opCode), .b({5{1'b1}}), .eq(opCode_eq__eq_11111));  // open: gt, lt
  Comparator #(.Bits(8)) comparator_2 (.a(out_13), .b({8{1'b1}}), .eq(pRAMAd_eq__eq_255));  // open: gt, lt
  Comparator #(.Bits(8)) comparator_3 (.a(out_14), .b(8'h10), .eq(rRAMAd_eq__eq_16));  // open: gt, lt
  or or_15 (ldrRAM, result__valid__done, Outputing, _01010, _11110);
  or or_16 (valid, done, Outputing, Valid_ed);
  or or_17 (addrRAMAd, Outputing, timetoreset);
  D_FF d_ff_3 (.D(multiplexer_5_out), .C(clk), .Q(Qc));  // open: nQ
  and and_6 (and_6_out, setpRAMad, ~clk);  // And
  or or_18 (_10111__re, _10111, timetoreset);
  Multiplexer #(.Bits(13)) multiplexer_6 (.sel(timetoreset), .in_0(_2D), .in_1({13{1'b0}}), .out(out_12));
  or or_19 (CanloadA__re, CanLoadA, timetoreset);
  Multiplexer #(.Bits(8)) multiplexer_7 (.sel(timetoreset), .in_0(dataA), .in_1({8{1'b0}}), .out(toaccA));
  Multiplexer multiplexer_8 (.sel(timetoreset), .in_0(greater), .in_1(1'b0), .out(togreater_flag));
  or or_20 (process__re, and_6_out, Data_Process, timetoreset);
  Multiplexer multiplexer_9 (.sel(timetoreset), .in_0(lesser), .in_1(1'b0), .out(tolesser_flag));
  or or_21 (_10111__11101__re, _11101, timetoreset, _10111);
  or or_22 (Outputing__re, Outputing, result__valid__done, timetoreset);
  Multiplexer #(.Bits(8)) multiplexer_10 (.sel(timetoreset), .in_0(DatarRAM), .in_1({8{1'b0}}), .out(tooutput));
  or or_23 (CanloadB__re, CanLoadB, timetoreset);
  Multiplexer #(.Bits(8)) multiplexer_11 (.sel(timetoreset), .in_0(dataB), .in_1({8{1'b0}}), .out(toaccB));
  Multiplexer multiplexer_12 (.sel(timetoreset), .in_0(equal), .in_1(1'b0), .out(torequal_flag));
  Register #(.Bits(8)) out (.D(tooutput), .C(clk), .en(Outputing__re), .Q(\output ));
  Multiplexer #(.Bits(8)) multiplexer_13 (.sel(timetoreset), .in_0(operand), .in_1(out_14), .out(multiplexer_13_out));
  Seven_Seg_Hex seven_seg_hex_1 (.d(\output [7:4]), .dp(1'b0));
  Multiplexer #(.Bits(8)) multiplexer_14 (.sel(timetoreset), .in_0(out_15), .in_1({8{1'b0}}), .out(multiplexer_14_out));
  Multiplexer #(.Bits(8)) multiplexer_15 (
    .sel(add1), .in_0(multiplexer_14_out), .in_1(out_20[15:8]), .out(multiplexer_15_out));
  Multiplexer #(.Bits(8)) multiplexer_16 (
    .sel(_11110), .in_0(multiplexer_13_out), .in_1({4'b0000, operand[7:4]}), .out(multiplexer_16_out));
  Multiplexer #(.Bits(8)) multiplexer_17 (.sel(add2), .in_0(multiplexer_15_out), .in_1(out_20[7:0]), .out(rRAMData));
  Multiplexer #(.Bits(8)) multiplexer_18 (.sel(add1), .in_0(multiplexer_16_out), .in_1(8'he), .out(multiplexer_18_out));
  or or_24 (CanloadC__re, CanLoadC, timetoreset);
  Multiplexer #(.Bits(8)) multiplexer_19 (.sel(timetoreset), .in_0(dataC), .in_1({8{1'b0}}), .out(toregC));
  or or_25 (_11110_process__re, _11110_process, timetoreset);
  and and_7 (_11110_process, _11110, Data_Process);
  Multiplexer #(.Bits(8)) multiplexer_20 (.sel(timetoreset), .in_0(DatarRAM1D), .in_1({8{1'b0}}), .out(toswap0x00));
  Seven_Seg_Hex seven_seg_hex_2 (.d(\output [3:0]), .dp(1'b0));
  Multiplexer #(.Bits(8)) multiplexer_21 (.sel(add2), .in_0(multiplexer_18_out), .in_1(8'hf), .out(_1ArRAM));
  Multiplexer #(.Bits(8)) multiplexer_22 (.sel(timetoreset), .in_0(DatarRAM), .in_1({8{1'b0}}), .out(toswapoperand));
  Multiplexer #(.Bits(8)) multiplexer_23 (.sel(or_26_out), .in_0(operand), .in_1(out_14), .out(multiplexer_23_out));
  or or_26 (or_26_out, result__valid__done, Outputing);
  Multiplexer #(.Bits(8)) multiplexer_24 (
    .sel(_11110), .in_0(multiplexer_23_out), .in_1({4'b0000, operand[3:0]}), .out(_2ArRAM));
  or or_27 (or_27_out, _00101, _00111, _01000);
  Decoder #(.Selector_Bits(5)) decoder_2 (
    .sel(opCode), .out_0(_00000), .out_1(_00001), .out_2(_00010), .out_3(_00011), .out_4(_00100),
    .out_5(_00101), .out_6(_00110), .out_7(_00111), .out_8(_01000), .out_9(_01001), .out_10(_01010),
    .out_11(_01011), .out_12(_01100), .out_13(_01101), .out_14(_01110), .out_15(_01111), .out_16(_10000),
    .out_17(_10001), .out_18(_10010), .out_19(_10011), .out_20(_10100), .out_21(_10101), .out_22(_10110),
    .out_23(_10111), .out_24(_11000), .out_25(_11001), .out_26(_11010), .out_27(_11011), .out_28(_11100),
    .out_29(_11101), .out_30(_11110), .out_31(_11111));
  Register #(.Bits(8)) regC (.D(toregC), .C(~clk), .en(CanloadC__re), .Q(out_17));
  and and_8 (CanLoadC, or_27_out, Data_Process);
  Multiplexer #(.Selector_Bits(3), .Bits(8)) multiplexer_25 (
    .sel({_01000, _00111, _00101}), .in_0({8{1'b0}}), .in_1(out_15), .in_2(M), .in_3({8{1'b0}}), .in_4(N),
    .in_5({8{1'b0}}), .in_6({8{1'b0}}), .in_7({8{1'b0}}), .out(dataC));
  or or_28 (or_28_out, _00010, _00100);
  Multiplexer #(.Bits(8)) multiplexer_26 (.sel(_00100), .in_0(operand), .in_1(out_15), .out(dataB));
  and and_9 (CanLoadB, or_28_out, Data_Process);
  ROM #(.AddrBits(8)) PrimeCheck (.A(out_15), .sel(_11101), .D(prime_check));
  Register #(.Bits(8)) accB (.D(toaccB), .C(~clk), .en(CanloadB__re), .Q(out_16));
  Multiplexer #(.Selector_Bits(5), .Bits(8)) multiplexer_27 (
    .sel(opCode), .in_0({8{1'b0}}), .in_1(operand), .in_2({8{1'b0}}), .in_3(out_16), .in_4({8{1'b0}}),
    .in_5({8{1'b0}}), .in_6(out_17), .in_7({8{1'b0}}), .in_8({8{1'b0}}), .in_9(DatapRAM), .in_10(DatarRAM),
    .in_11({8{1'b0}}), .in_12({8{1'b0}}), .in_13({8{1'b0}}), .in_14({8{1'b0}}), .in_15({8{1'b0}}),
    .in_16({8{1'b0}}), .in_17(accA__plus__accB), .in_18(accA___accB), .in_19(accA____accB_t),
    .in_20(accA____accB_t_t), .in_21(accA____accB), .in_22(_8), .in_23({8{1'b0}}), .in_24(NOT_accA),
    .in_25(accA_AND_accB), .in_26(accA_OR_accB), .in_27(accA_XOR_accB), .in_28(accA__lt__lt__accB),
    .in_29({8{1'b0}}), .in_30({8{1'b0}}), .in_31({8{1'b0}}), .out(dataA));
  and and_10 (and_10_out, ~busy, LongProcess);  // And
  Register #(.Bits(8)) accA (.D(toaccA), .C(~clk), .en(CanloadA__re), .Q(out_15));
  D_FF d_ff_4 (.D(and_10_out), .C(clk), .Q(add1));  // open: nQ
  D_FF d_ff_5 (.D(add1), .C(clk), .Q(add2));  // open: nQ
  Register #(.Bits(8)) _0x00 (.D(toswap0x00), .C(~clk), .en(_11110_process__re), .Q(reg0x00));
  Register #(.Bits(8)) u_operand (.D(toswapoperand), .C(~clk), .en(_11110_process__re), .Q(regoperand));
  D_FF d_ff_6 (.D(add2), .C(clk), .Q(endswap));  // open: nQ
  or or_29 (or_29_out, _00001, _00011, _00110, _01001, _01010, _10001, _10010, _10011, _10100, _10101, _10110, _11000, _11001, _11010, _11011, _11100);
  Add #(.Bits(8)) Plus (.a(out_15), .b(out_16), .c_i(1'b0), .s(accA__plus__accB));  // open: c_o
  Sub #(.Bits(8)) Sub (.a(out_15), .b(out_16), .c_i(1'b0), .s(accA___accB));  // open: c_o
  assign NOT_accA = ~out_15;  // Not not_8, 8 bits wide
  assign accA_AND_accB = out_15 & out_16;  // And and_11, 8 bits wide
  assign accA_OR_accB = out_15 | out_16;  // Or or_30, 8 bits wide
  and and_12 (CanLoadA, or_29_out, Data_Process);
  or or_31 (or_31_out, greater_flag, equal_flag);
  Comparator #(.Bits(8)) CMP (.a(out_15), .b(out_16), .gt(greater), .eq(CMP_eq), .lt(lesser));
  Register u_Lesser (.D(tolesser_flag), .C(~clk), .en(_10111__re), .Q(lesser_flag));
  Register u_Greater (.D(togreater_flag), .C(~clk), .en(_10111__re), .Q(greater_flag));
  and and_13 (and_13_out, _01101, equal_flag);
  and and_14 (and_14_out, _01110, greater_flag);
  and and_15 (and_15_out, _01111, lesser_flag);
  and and_16 (and_16_out, _10000, or_31_out);
  Mul #(.Bits(4)) Multi (.a(out_15[3:0]), .b(out_16[3:0]), .mul(accA____accB_t));
  Div #(.Bits(8)) Divi (.a(out_15), .b(out_16), .q(accA____accB_t_t), .r(accA____accB));
  assign accA_XOR_accB = out_15 ^ out_16;  // XOr xor_1, 8 bits wide
  BarrelShifter #(.Bits(8)) Shift (.in(out_15), .shift({1'b0, out_16[2:0]}), .out(accA__lt__lt__accB));
  or or_32 (jump, _01100, and_13_out, and_14_out, and_15_out, and_16_out);
  Multiplexer #(.Selector_Bits(2)) multiplexer_28 (
    .sel({_10111, _11101}), .in_0(equal_flag), .in_1(prime_check), .in_2(CMP_eq), .in_3(1'b0), .out(equal));
  Register u_Equal (.D(torequal_flag), .C(~clk), .en(_10111__11101__re), .Q(equal_flag));
  LookUpTable #(.Bits(8)) Power (
    .in0(out_15[0]), .in1(out_15[1]), .in2(out_15[2]), .in3(out_16[0]), .in4(out_16[1]), .in5(out_16[2]),
    .out(_8));
  or or_33 (jump__11111, _11111, jump);
  Multiplexer #(.Bits(8)) multiplexer_29 (.sel(_11111), .in_0(operand), .in_1(out_13), .out(presetto));
  Multiplexer #(.Bits(8)) multiplexer_30 (.sel(busy), .in_0(reg0x00), .in_1(a), .out(multiplexer_30_out));
  Multiplexer #(.Bits(8)) multiplexer_31 (.sel(busy), .in_0(regoperand), .in_1(b), .out(multiplexer_31_out));
  D_FF d_ff_7 (.D(LongProcess), .C(clk), .nQ(d_ff_7_nq));  // open: Q
  Register #(.Bits(8)) register_1 (.D(multiplexer_30_out), .C(clk), .en(1'b1), .Q(register_1_q));
  Register #(.Bits(8)) register_2 (.D(multiplexer_31_out), .C(clk), .en(1'b1), .Q(register_2_q));
  and and_17 (and_17_out, d_ff_7_nq, LongProcess);
  Comparator #(.Bits(8)) comparator_4 (
    .a(register_1_q), .b(register_2_q), .gt(a__gt__b[7]), .eq(comparator_4_eq), .lt(a__lt__b[7]));
  assign driverinvsel_1_out = ~busy ? and_17_out : 1'bz;  // DriverInvSel driverinvsel_1
  and and_18 (and_18_out, d_ff_8_q, ~reset, ~comparator_4_eq);  // And
  and and_19 (and_19_out, ~reset, driverinvsel_1_out, ~comparator_4_eq);  // And
  and and_20 (and_20_out, driverinvsel_1_out, ~reset, d_ff_8_nq);  // And
  Sub #(.Bits(8)) sub_2 (.a(register_1_q), .b(register_2_q), .c_i(1'b0), .s(sub_2_s));  // open: c_o
  Sub #(.Bits(8)) sub_3 (.a(register_2_q), .b(register_1_q), .c_i(1'b0), .s(sub_3_s));  // open: c_o
  or or_34 (busy, and_18_out, and_19_out, and_20_out);
  Mul #(.Bits(8)) mul_1 (.a(reg0x00), .b(regoperand), .mul(mul_1_mul));
  Div #(.Bits(16)) div_1 (.a(mul_1_mul), .b({{8{1'b0}}, out_19[7:0]}), .q(out_20));  // open: r
  assign and_21_out = sub_2_s & {8{a__gt__b[7]}};  // And and_21, 8 bits wide
  assign and_22_out = sub_3_s & {8{a__lt__b[7]}};  // And and_22, 8 bits wide
  assign and_23_out = {8{a__gt__b[7]}} & register_2_q;  // And and_23, 8 bits wide
  assign and_24_out = register_1_q & {8{a__lt__b[7]}};  // And and_24, 8 bits wide
  D_FF d_ff_8 (.D(busy), .C(clk), .Q(d_ff_8_q), .nQ(d_ff_8_nq));
  assign a = and_21_out | and_22_out;  // Or or_35, 8 bits wide
  assign b = and_23_out | and_24_out;  // Or or_36, 8 bits wide
  Register #(.Bits(8)) register_3 (.D(register_2_q), .C(clk), .en(comparator_4_eq), .Q(out_19[7:0]));

  assign out_19[15:8] = {8{1'b0}};

  // Other names for the same wires on the sheet: a__lt__b[6:0] = {7{a__lt__b[7]}}; a__gt__b[6:0] = {7{a__gt__b[7]}};
  //   gcd[7:0] = out_19[7:0]; accA[7:0] = out_15; accA___accB_t[7:0] = _8; accB[7:0] = out_16; Done_ed = done;
  //   lcm[15:0] = out_20; pRAM_Ad[7:0] = out_13; process = Data_Process; processpRAM[12:0] = out_12;
  //   select_state[2:0] = {Qa, Qb, Qc}; regC[7:0] = out_17; rRAM_Ad[7:0] = out_14; Swaping = LongProcess

  // Notes on the sheet:
  //   RAM
  //   Control-Unit
  //   Logic-for-State
  //   Testcase
  //   CMP-for-State
  //   Reset
  //   Input & Output
  //   command
  //   accA
  //   Flag
  //   Output
  //   accB
  //   6733021521 นายกีรติ เศรษฐสุข (ต่อวงจร)
  //   6733154321 นายปุญญพัฒน์ ผิวขำ (ผู้ช่วยต่อวงจรและพัฒนาdata path)
  //   6733213721 นายยศสรัล ไชยภักดี (ผู้ช่วยและทำเอกสาร)
  //   6733152021 นายปิยากร สุธีโรจน์ตระกูล (ผู้ช่วยและทำสไลด์)
  //   rRAM
  //   Swap
  //   regC
  //   ALU
  //   PrimeCheck
  //   contents of PrimeCheck (hex, n*v repeats v):
  //   0,0,1,1,0,1,0,1,0,0,0,1,0,1,0,0,0,1,0,1,0,0,0,1,5*0,1,0,1,5*0
  //   ,1,0,0,0,1,0,1,0,0,0,1,5*0,1,5*0,1,0,1,5*0,1,0,0,0,1,0,1,0,0,0
  //   ,1,5*0,1,5*0,1,0,1,4*0,1,6*0,1,0,0,0,1,0,1,0,0,1,14*0,1,0,0,0
  //   ,1,5*0,1,0,1,9*0,1,0,1,5*0,1,5*0,1,0,0,0,1,5*0,1,5*0,1,0,1,9*0
  //   ,1,0,1,0,0,0,1,0,1,11*0,1,11*0,1,0,0,0,1,0,1,0,0,0,1,7*0,1,9*0,1
  //   accA-process-before-collect
  //   Jump
  //   Comparator
  //   STOP
  //   contents of Power (hex, n*v repeats v):
  //   1,7*0,9*1,2,4,8,10,20,40,80,1,3,9,1b,51,f3,0,0,1,4,10,40,100,0,0,0
  //   ,1,5,19,7d,4*0,1,6,24,d8,4*0,1,7,31,0,0,2d
endmodule

/* Test case 01_P01T1:
M N progIN reset progLoad start result clk valid done output
0 0 0 0 0 0 0 0 x x x
0 0 0 0 0 0 0 1 x x x
0 0 0 1 0 0 0 0 x x x
0 0 0 1 0 0 0 1 0 0 x
0 0 0 0 0 0 0 0 0 0 x
0 0 0 0 0 0 0 1 0 0 x
0 0 0 0 0 0 0 0 0 0 x
0 0 0 0 0 0 0 1 0 0 x
0 0 0 0 0 0 0 0 0 0 x
0 0 0 0 0 0 0 1 0 0 x
0 0 0 0 0 0 0 0 0 0 x
0 0 0 0 0 0 0 1 0 0 x
0 0 0 0 0 0 0 0 0 0 x
0 0 0 0 0 0 0 1 0 0 x
0 0 0 0 0 0 0 0 0 0 x
0 0 0 0 0 0 0 1 0 0 x
0 0 0 0 0 0 0 0 0 0 x
0 0 0 0 0 0 0 1 0 0 x
0 0 0 0 0 0 0 0 0 0 x
0 0 0 0 0 0 0 1 0 0 x
0 0 0 0 0 0 0 0 0 0 x
0 0 0 0 0 0 0 1 0 0 x
0 0 0 0 0 0 0 0 0 0 x
0 0 0 0 0 0 0 1 0 0 x
0 0 0 0 0 0 0 0 0 0 x
0 0 0 0 0 0 0 1 0 0 x
0 0 0 0 0 0 0 0 0 0 x
0 0 0 0 0 0 0 1 0 0 x
0 0 0 0 0 0 0 0 0 0 x
0 0 0 0 0 0 0 1 0 0 x
0 0 0 0 0 0 0 0 0 0 x
0 0 0 0 0 0 0 1 0 0 x
0 0 0 0 0 0 0 0 0 0 x
0 0 0 0 0 0 0 1 0 0 x
0 0 0 0 0 0 0 0 0 0 x
0 0 0 0 0 0 0 1 0 0 x
0 0 0 0 0 0 0 0 0 0 x
0 0 0 0 0 0 0 1 0 0 x
0 0 0 0 0 0 0 0 0 0 x
0 0 0 0 0 0 0 1 0 0 x
0 0 0 0 0 0 0 0 0 0 x
0 0 0 0 0 0 0 1 0 0 x
0 0 271 0 1 0 0 0 0 0 x
0 0 271 0 1 0 0 1 0 0 x
0 0 565 0 1 0 0 0 0 0 x
0 0 565 0 1 0 0 1 0 0 x
0 0 4352 0 1 0 0 0 0 0 x
0 0 4352 0 1 0 0 1 0 0 x
0 0 2819 0 1 0 0 0 0 0 x
0 0 2819 0 1 0 0 1 0 0 x
0 0 7936 0 1 0 0 0 0 0 x
0 0 7936 0 1 0 0 1 0 0 x
0 0 0 0 0 1 0 0 0 0 x
0 0 0 0 0 1 0 1 0 0 x
0 0 0 0 0 0 0 0 x 0 x
0 0 0 0 0 0 0 1 x 0 x
0 0 0 0 0 0 0 0 x 0 x
0 0 0 0 0 0 0 1 x 0 x
0 0 0 0 0 0 0 0 x 0 x
0 0 0 0 0 0 0 1 x 0 x
0 0 0 0 0 0 0 0 x 0 x
0 0 0 0 0 0 0 1 x 0 x
0 0 0 0 0 0 0 0 x 0 x
0 0 0 0 0 0 0 1 x 0 x
0 0 0 0 0 0 0 0 x 0 x
0 0 0 0 0 0 0 1 x 0 x
0 0 0 0 0 0 0 0 x 0 x
0 0 0 0 0 0 0 1 x 0 x
0 0 0 0 0 0 0 0 x 0 x
0 0 0 0 0 0 0 1 x 0 x
0 0 0 0 0 0 0 0 x 0 x
0 0 0 0 0 0 0 1 x 0 x
0 0 0 0 0 0 0 0 x 0 x
0 0 0 0 0 0 0 1 x 0 x
0 0 0 0 0 0 0 0 x 0 x
0 0 0 0 0 0 0 1 x 0 x
0 0 0 0 0 0 0 0 x 0 x
0 0 0 0 0 0 0 1 x 0 x
0 0 0 0 0 0 0 0 x 0 x
0 0 0 0 0 0 0 1 x 0 x
0 0 0 0 0 0 0 0 x 0 x
0 0 0 0 0 0 0 1 x 0 x
0 0 0 0 0 0 0 0 x 0 x
0 0 0 0 0 0 0 1 x 0 x
0 0 0 0 0 0 0 0 x 0 x
0 0 0 0 0 0 0 1 x 0 x
0 0 0 0 0 0 0 0 x 0 x
0 0 0 0 0 0 0 1 x 0 x
0 0 0 0 0 0 0 0 x 0 x
0 0 0 0 0 0 0 1 x 0 x
0 0 0 0 0 0 0 0 x 0 x
0 0 0 0 0 0 0 1 x 0 x
0 0 0 0 0 0 0 0 x 0 x
0 0 0 0 0 0 0 1 x 0 x
0 0 0 0 0 0 0 0 x 0 x
0 0 0 0 0 0 0 1 x 0 x
0 0 0 0 0 0 0 0 x 0 x
0 0 0 0 0 0 0 1 x 0 x
0 0 0 0 0 0 0 0 x 0 x
0 0 0 0 0 0 0 1 x 0 x
0 0 0 0 0 0 0 0 x 0 x
0 0 0 0 0 0 0 1 x 0 x
0 0 0 0 0 0 0 0 x 0 x
0 0 0 0 0 0 0 1 x 0 x
0 0 0 0 0 0 0 0 x 0 x
0 0 0 0 0 0 0 1 1 0 x
0 0 0 0 0 0 1 0 1 0 x
0 0 0 0 0 0 1 1 1 0 0
0 0 0 0 0 0 0 0 1 0 0
0 0 0 0 0 0 0 1 1 0 0
0 0 0 0 0 0 0 0 1 0 0
0 0 0 0 0 0 0 1 1 0 0
0 0 0 0 0 0 0 0 1 0 0
0 0 0 0 0 0 0 1 1 0 68
0 0 0 0 0 0 0 0 1 0 68
0 0 0 0 0 0 0 1 1 0 0
0 0 0 0 0 0 0 0 1 0 0
0 0 0 0 0 0 0 1 1 0 0
0 0 0 0 0 0 0 0 1 0 0
0 0 0 0 0 0 0 1 1 0 0
0 0 0 0 0 0 0 0 1 0 0
0 0 0 0 0 0 0 1 1 0 0
0 0 0 0 0 0 0 0 1 0 0
0 0 0 0 0 0 0 1 1 0 0
0 0 0 0 0 0 0 0 1 0 0
0 0 0 0 0 0 0 1 1 0 0
0 0 0 0 0 0 0 0 1 0 0
0 0 0 0 0 0 0 1 1 0 0
0 0 0 0 0 0 0 0 1 0 0
0 0 0 0 0 0 0 1 1 0 0
0 0 0 0 0 0 0 0 1 0 0
0 0 0 0 0 0 0 1 1 0 0
0 0 0 0 0 0 0 0 1 0 0
0 0 0 0 0 0 0 1 1 0 0
0 0 0 0 0 0 0 0 1 0 0
0 0 0 0 0 0 0 1 1 0 0
0 0 0 0 0 0 0 0 1 0 0
0 0 0 0 0 0 0 1 1 0 0
0 0 0 0 0 0 0 0 1 0 0
0 0 0 0 0 0 0 1 1 1 x
0 0 0 0 0 0 0 0 1 1 x
0 0 0 0 0 0 0 1 1 1 x
0 0 0 0 0 0 0 0 1 1 x
*/

/* Test case 01_P01T2:
M N progIN reset progLoad start result clk valid done output
0 0 0 0 0 0 0 0 x x x
0 0 0 0 0 0 0 1 x x x
0 0 0 1 0 0 0 0 x x x
0 0 0 1 0 0 0 1 0 0 x
0 0 0 0 0 0 0 0 0 0 x
0 0 0 0 0 0 0 1 0 0 x
0 0 0 0 0 0 0 0 0 0 x
0 0 0 0 0 0 0 1 0 0 x
0 0 0 0 0 0 0 0 0 0 x
0 0 0 0 0 0 0 1 0 0 x
0 0 0 0 0 0 0 0 0 0 x
0 0 0 0 0 0 0 1 0 0 x
0 0 0 0 0 0 0 0 0 0 x
0 0 0 0 0 0 0 1 0 0 x
0 0 0 0 0 0 0 0 0 0 x
0 0 0 0 0 0 0 1 0 0 x
0 0 0 0 0 0 0 0 0 0 x
0 0 0 0 0 0 0 1 0 0 x
0 0 0 0 0 0 0 0 0 0 x
0 0 0 0 0 0 0 1 0 0 x
0 0 0 0 0 0 0 0 0 0 x
0 0 0 0 0 0 0 1 0 0 x
0 0 0 0 0 0 0 0 0 0 x
0 0 0 0 0 0 0 1 0 0 x
0 0 0 0 0 0 0 0 0 0 x
0 0 0 0 0 0 0 1 0 0 x
0 0 0 0 0 0 0 0 0 0 x
0 0 0 0 0 0 0 1 0 0 x
0 0 0 0 0 0 0 0 0 0 x
0 0 0 0 0 0 0 1 0 0 x
0 0 0 0 0 0 0 0 0 0 x
0 0 0 0 0 0 0 1 0 0 x
0 0 0 0 0 0 0 0 0 0 x
0 0 0 0 0 0 0 1 0 0 x
0 0 0 0 0 0 0 0 0 0 x
0 0 0 0 0 0 0 1 0 0 x
0 0 0 0 0 0 0 0 0 0 x
0 0 0 0 0 0 0 1 0 0 x
0 0 0 0 0 0 0 0 0 0 x
0 0 0 0 0 0 0 1 0 0 x
0 0 0 0 0 0 0 0 0 0 x
0 0 0 0 0 0 0 1 0 0 x
0 0 271 0 1 0 0 0 0 0 x
0 0 271 0 1 0 0 1 0 0 x
0 0 565 0 1 0 0 0 0 0 x
0 0 565 0 1 0 0 1 0 0 x
0 0 4352 0 1 0 0 0 0 0 x
0 0 4352 0 1 0 0 1 0 0 x
0 0 2819 0 1 0 0 0 0 0 x
0 0 2819 0 1 0 0 1 0 0 x
0 0 7936 0 1 0 0 0 0 0 x
0 0 7936 0 1 0 0 1 0 0 x
0 0 0 0 0 1 0 0 0 0 x
0 0 0 0 0 1 0 1 0 0 x
0 0 0 0 0 0 0 0 x 0 x
0 0 0 0 0 0 0 1 x 0 x
0 0 0 0 0 0 0 0 x 0 x
0 0 0 0 0 0 0 1 x 0 x
0 0 0 0 0 0 0 0 x 0 x
0 0 0 0 0 0 0 1 x 0 x
0 0 0 0 0 0 0 0 x 0 x
0 0 0 0 0 0 0 1 x 0 x
0 0 0 0 0 0 0 0 x 0 x
0 0 0 0 0 0 0 1 x 0 x
0 0 0 0 0 0 0 0 x 0 x
0 0 0 0 0 0 0 1 x 0 x
0 0 0 0 0 0 0 0 x 0 x
0 0 0 0 0 0 0 1 x 0 x
0 0 0 0 0 0 0 0 x 0 x
0 0 0 0 0 0 0 1 x 0 x
0 0 0 0 0 0 0 0 x 0 x
0 0 0 0 0 0 0 1 x 0 x
0 0 0 0 0 0 0 0 x 0 x
0 0 0 0 0 0 0 1 x 0 x
0 0 0 0 0 0 0 0 x 0 x
0 0 0 0 0 0 0 1 x 0 x
0 0 0 0 0 0 0 0 x 0 x
0 0 0 0 0 0 0 1 x 0 x
0 0 0 0 0 0 0 0 x 0 x
0 0 0 0 0 0 0 1 x 0 x
0 0 0 0 0 0 0 0 x 0 x
0 0 0 0 0 0 0 1 x 0 x
0 0 0 0 0 0 0 0 x 0 x
0 0 0 0 0 0 0 1 x 0 x
0 0 0 0 0 0 0 0 x 0 x
0 0 0 0 0 0 0 1 x 0 x
0 0 0 0 0 0 0 0 x 0 x
0 0 0 0 0 0 0 1 x 0 x
0 0 0 0 0 0 0 0 x 0 x
0 0 0 0 0 0 0 1 x 0 x
0 0 0 0 0 0 0 0 x 0 x
0 0 0 0 0 0 0 1 x 0 x
0 0 0 0 0 0 0 0 x 0 x
0 0 0 0 0 0 0 1 x 0 x
0 0 0 0 0 0 0 0 x 0 x
0 0 0 0 0 0 0 1 x 0 x
0 0 0 0 0 0 0 0 x 0 x
0 0 0 0 0 0 0 1 x 0 x
0 0 0 0 0 0 0 0 x 0 x
0 0 0 0 0 0 0 1 x 0 x
0 0 0 0 0 0 0 0 x 0 x
0 0 0 0 0 0 0 1 x 0 x
0 0 0 0 0 0 0 0 x 0 x
0 0 0 0 0 0 0 1 x 0 x
0 0 0 0 0 0 0 0 x 0 x
0 0 0 0 0 0 0 1 1 0 x
0 0 0 0 0 0 1 0 1 0 x
0 0 0 0 0 0 1 1 1 0 0
0 0 0 0 0 0 0 0 1 0 0
0 0 0 0 0 0 0 1 1 0 0
0 0 0 0 0 0 0 0 1 0 0
0 0 0 0 0 0 0 1 1 0 0
0 0 0 0 0 0 0 0 1 0 0
0 0 0 0 0 0 0 1 1 0 68
0 0 0 0 0 0 0 0 1 0 68
0 0 0 0 0 0 0 1 1 0 0
0 0 0 0 0 0 0 0 1 0 0
0 0 0 0 0 0 0 1 1 0 0
0 0 0 0 0 0 0 0 1 0 0
0 0 0 0 0 0 0 1 1 0 0
0 0 0 0 0 0 0 0 1 0 0
0 0 0 0 0 0 0 1 1 0 0
0 0 0 0 0 0 0 0 1 0 0
0 0 0 0 0 0 0 1 1 0 0
0 0 0 0 0 0 0 0 1 0 0
0 0 0 0 0 0 0 1 1 0 0
0 0 0 0 0 0 0 0 1 0 0
0 0 0 0 0 0 0 1 1 0 0
0 0 0 0 0 0 0 0 1 0 0
0 0 0 0 0 0 0 1 1 0 0
0 0 0 0 0 0 0 0 1 0 0
0 0 0 0 0 0 0 1 1 0 0
0 0 0 0 0 0 0 0 1 0 0
0 0 0 0 0 0 0 1 1 0 0
0 0 0 0 0 0 0 0 1 0 0
0 0 0 0 0 0 0 1 1 0 0
0 0 0 0 0 0 0 0 1 0 0
0 0 0 0 0 0 0 1 1 0 0
0 0 0 0 0 0 0 0 1 0 0
0 0 0 0 0 0 0 1 1 1 x
0 0 0 0 0 0 0 0 1 1 x
0 0 0 0 0 0 0 1 1 1 x
0 0 0 0 0 0 0 0 1 1 x
0 0 0 0 0 0 0 1 1 1 x
0 0 0 0 0 0 1 0 1 X x
0 0 0 0 0 0 1 1 1 X 0
0 0 0 0 0 0 0 0 1 0 0
0 0 0 0 0 0 0 1 1 0 0
0 0 0 0 0 0 0 0 1 0 0
0 0 0 0 0 0 0 1 1 0 0
0 0 0 0 0 0 0 0 1 0 0
0 0 0 0 0 0 0 1 1 0 68
0 0 0 0 0 0 0 0 1 0 68
0 0 0 0 0 0 0 1 1 0 0
0 0 0 0 0 0 0 0 1 0 0
0 0 0 0 0 0 0 1 1 0 0
0 0 0 0 0 0 0 0 1 0 0
0 0 0 0 0 0 0 1 1 0 0
0 0 0 0 0 0 0 0 1 0 0
0 0 0 0 0 0 0 1 1 0 0
0 0 0 0 0 0 0 0 1 0 0
0 0 0 0 0 0 0 1 1 0 0
0 0 0 0 0 0 0 0 1 0 0
0 0 0 0 0 0 0 1 1 0 0
0 0 0 0 0 0 0 0 1 0 0
0 0 0 0 0 0 0 1 1 0 0
0 0 0 0 0 0 0 0 1 0 0
0 0 0 0 0 0 0 1 1 0 0
0 0 0 0 0 0 0 0 1 0 0
0 0 0 0 0 0 0 1 1 0 0
0 0 0 0 0 0 0 0 1 0 0
0 0 0 0 0 0 0 1 1 0 0
0 0 0 0 0 0 0 0 1 0 0
0 0 0 0 0 0 0 1 1 0 0
0 0 0 0 0 0 0 0 1 0 0
0 0 0 0 0 0 0 1 1 0 0
0 0 0 0 0 0 0 0 1 0 0
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*/

/* Test case 01_P01T3:
M N progIN reset progLoad start result clk valid done output
0 0 0 0 0 0 0 0 x x x
0 0 0 0 0 0 0 1 x x x
0 0 0 1 0 0 0 0 x x x
0 0 0 1 0 0 0 1 0 0 x
0 0 0 0 0 0 0 0 0 0 x
0 0 0 0 0 0 0 1 0 0 x
0 0 0 0 0 0 0 0 0 0 x
0 0 0 0 0 0 0 1 0 0 x
0 0 0 0 0 0 0 0 0 0 x
0 0 0 0 0 0 0 1 0 0 x
0 0 0 0 0 0 0 0 0 0 x
0 0 0 0 0 0 0 1 0 0 x
0 0 0 0 0 0 0 0 0 0 x
0 0 0 0 0 0 0 1 0 0 x
0 0 0 0 0 0 0 0 0 0 x
0 0 0 0 0 0 0 1 0 0 x
0 0 0 0 0 0 0 0 0 0 x
0 0 0 0 0 0 0 1 0 0 x
0 0 0 0 0 0 0 0 0 0 x
0 0 0 0 0 0 0 1 0 0 x
0 0 0 0 0 0 0 0 0 0 x
0 0 0 0 0 0 0 1 0 0 x
0 0 0 0 0 0 0 0 0 0 x
0 0 0 0 0 0 0 1 0 0 x
0 0 0 0 0 0 0 0 0 0 x
0 0 0 0 0 0 0 1 0 0 x
0 0 0 0 0 0 0 0 0 0 x
0 0 0 0 0 0 0 1 0 0 x
0 0 0 0 0 0 0 0 0 0 x
0 0 0 0 0 0 0 1 0 0 x
0 0 0 0 0 0 0 0 0 0 x
0 0 0 0 0 0 0 1 0 0 x
0 0 0 0 0 0 0 0 0 0 x
0 0 0 0 0 0 0 1 0 0 x
0 0 0 0 0 0 0 0 0 0 x
0 0 0 0 0 0 0 1 0 0 x
0 0 0 0 0 0 0 0 0 0 x
0 0 0 0 0 0 0 1 0 0 x
0 0 0 0 0 0 0 0 0 0 x
0 0 0 0 0 0 0 1 0 0 x
0 0 0 0 0 0 0 0 0 0 x
0 0 0 0 0 0 0 1 0 0 x
0 0 271 0 1 0 0 0 0 0 x
0 0 271 0 1 0 0 1 0 0 x
0 0 566 0 1 0 0 0 0 0 x
0 0 566 0 1 0 0 1 0 0 x
0 0 5888 0 1 0 0 0 0 0 x
0 0 5888 0 1 0 0 1 0 0 x
0 0 3599 0 1 0 0 0 0 0 x
0 0 3599 0 1 0 0 1 0 0 x
0 0 4110 0 1 0 0 0 0 0 x
0 0 4110 0 1 0 0 1 0 0 x
0 0 3856 0 1 0 0 0 0 0 x
0 0 3856 0 1 0 0 1 0 0 x
0 0 7936 0 1 0 0 0 0 0 x
0 0 7936 0 1 0 0 1 0 0 x
0 0 0 0 1 0 0 0 0 0 x
0 0 0 0 1 0 0 1 0 0 x
0 0 0 0 1 0 0 0 0 0 x
0 0 0 0 1 0 0 1 0 0 x
0 0 0 0 1 0 0 0 0 0 x
0 0 0 0 1 0 0 1 0 0 x
0 0 0 0 1 0 0 0 0 0 x
0 0 0 0 1 0 0 1 0 0 x
0 0 0 0 1 0 0 0 0 0 x
0 0 0 0 1 0 0 1 0 0 x
0 0 0 0 1 0 0 0 0 0 x
0 0 0 0 1 0 0 1 0 0 x
0 0 0 0 1 0 0 0 0 0 x
0 0 0 0 1 0 0 1 0 0 x
0 0 0 0 1 0 0 0 0 0 x
0 0 0 0 1 0 0 1 0 0 x
0 0 0 0 1 0 0 0 0 0 x
0 0 0 0 1 0 0 1 0 0 x
0 0 4352 0 1 0 0 0 0 0 x
0 0 4352 0 1 0 0 1 0 0 x
0 0 2819 0 1 0 0 0 0 0 x
0 0 2819 0 1 0 0 1 0 0 x
0 0 7936 0 1 0 0 0 0 0 x
0 0 7936 0 1 0 0 1 0 0 x
0 0 0 0 1 0 0 0 0 0 x
0 0 0 0 1 0 0 1 0 0 x
0 0 0 0 0 0 0 0 0 0 x
0 0 0 0 0 0 0 1 0 0 x
0 0 0 0 0 0 0 0 0 0 x
0 0 0 0 0 0 0 1 0 0 x
0 0 0 0 0 0 0 0 0 0 x
0 0 0 0 0 0 0 1 0 0 x
0 0 0 0 0 1 0 0 0 0 x
0 0 0 0 0 1 0 1 0 0 x
0 0 0 0 0 0 0 0 x 0 x
0 0 0 0 0 0 0 1 x 0 x
0 0 0 0 0 0 0 0 x 0 x
0 0 0 0 0 0 0 1 x 0 x
0 0 0 0 0 0 0 0 x 0 x
0 0 0 0 0 0 0 1 x 0 x
0 0 0 0 0 0 0 0 x 0 x
0 0 0 0 0 0 0 1 x 0 x
0 0 0 0 0 0 0 0 x 0 x
0 0 0 0 0 0 0 1 x 0 x
0 0 0 0 0 0 0 0 x 0 x
0 0 0 0 0 0 0 1 x 0 x
0 0 0 0 0 0 0 0 x 0 x
0 0 0 0 0 0 0 1 x 0 x
0 0 0 0 0 0 0 0 x 0 x
0 0 0 0 0 0 0 1 x 0 x
0 0 0 0 0 0 0 0 x 0 x
0 0 0 0 0 0 0 1 x 0 x
0 0 0 0 0 0 0 0 x 0 x
0 0 0 0 0 0 0 1 x 0 x
0 0 0 0 0 0 0 0 x 0 x
0 0 0 0 0 0 0 1 x 0 x
0 0 0 0 0 0 0 0 x 0 x
0 0 0 0 0 0 0 1 x 0 x
0 0 0 0 0 0 0 0 x 0 x
0 0 0 0 0 0 0 1 x 0 x
0 0 0 0 0 0 0 0 x 0 x
0 0 0 0 0 0 0 1 x 0 x
0 0 0 0 0 0 0 0 x 0 x
0 0 0 0 0 0 0 1 x 0 x
0 0 0 0 0 0 0 0 x 0 x
0 0 0 0 0 0 0 1 x 0 x
0 0 0 0 0 0 0 0 x 0 x
0 0 0 0 0 0 0 1 x 0 x
0 0 0 0 0 0 0 0 x 0 x
0 0 0 0 0 0 0 1 x 0 x
0 0 0 0 0 0 0 0 x 0 x
0 0 0 0 0 0 0 1 x 0 x
0 0 0 0 0 0 0 0 x 0 x
0 0 0 0 0 0 0 1 x 0 x
0 0 0 0 0 0 0 0 x 0 x
0 0 0 0 0 0 0 1 x 0 x
0 0 0 0 0 0 0 0 x 0 x
0 0 0 0 0 0 0 1 x 0 x
0 0 0 0 0 0 0 0 x 0 x
0 0 0 0 0 0 0 1 x 0 x
0 0 0 0 0 0 0 0 x 0 x
0 0 0 0 0 0 0 1 x 0 x
0 0 0 0 0 0 0 0 x 0 x
0 0 0 0 0 0 0 1 x 0 x
0 0 0 0 0 0 0 0 x 0 x
0 0 0 0 0 0 0 1 1 0 x
0 0 0 0 0 0 1 0 1 0 x
0 0 0 0 0 0 1 1 1 0 0
0 0 0 0 0 0 0 0 1 0 0
0 0 0 0 0 0 0 1 1 0 0
0 0 0 0 0 0 0 0 1 0 0
0 0 0 0 0 0 0 1 1 0 0
0 0 0 0 0 0 0 0 1 0 0
0 0 0 0 0 0 0 1 1 0 69
0 0 0 0 0 0 0 0 1 0 69
0 0 0 0 0 0 0 1 1 0 0
0 0 0 0 0 0 0 0 1 0 0
0 0 0 0 0 0 0 1 1 0 0
0 0 0 0 0 0 0 0 1 0 0
0 0 0 0 0 0 0 1 1 0 0
0 0 0 0 0 0 0 0 1 0 0
0 0 0 0 0 0 0 1 1 0 0
0 0 0 0 0 0 0 0 1 0 0
0 0 0 0 0 0 0 1 1 0 0
0 0 0 0 0 0 0 0 1 0 0
0 0 0 0 0 0 0 1 1 0 0
0 0 0 0 0 0 0 0 1 0 0
0 0 0 0 0 0 0 1 1 0 0
0 0 0 0 0 0 0 0 1 0 0
0 0 0 0 0 0 0 1 1 0 0
0 0 0 0 0 0 0 0 1 0 0
0 0 0 0 0 0 0 1 1 0 0
0 0 0 0 0 0 0 0 1 0 0
0 0 0 0 0 0 0 1 1 0 0
0 0 0 0 0 0 0 0 1 0 0
0 0 0 0 0 0 0 1 1 0 0
0 0 0 0 0 0 0 0 1 0 0
0 0 0 0 0 0 0 1 1 0 0
0 0 0 0 0 0 0 0 1 0 0
0 0 0 0 0 0 0 1 1 1 x
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*/

/* Test case 01_P01T4:
M N progIN reset progLoad start result clk valid done output
0 0 0 0 0 0 0 0 x x x
0 0 0 0 0 0 0 1 x x x
0 0 0 1 0 0 0 0 x x x
0 0 0 1 0 0 0 1 0 0 x
0 0 0 0 0 0 0 0 0 0 x
0 0 0 0 0 0 0 1 0 0 x
0 0 0 0 0 0 0 0 0 0 x
0 0 0 0 0 0 0 1 0 0 x
0 0 0 0 0 0 0 0 0 0 x
0 0 0 0 0 0 0 1 0 0 x
0 0 0 0 0 0 0 0 0 0 x
0 0 0 0 0 0 0 1 0 0 x
0 0 0 0 0 0 0 0 0 0 x
0 0 0 0 0 0 0 1 0 0 x
0 0 0 0 0 0 0 0 0 0 x
0 0 0 0 0 0 0 1 0 0 x
0 0 0 0 0 0 0 0 0 0 x
0 0 0 0 0 0 0 1 0 0 x
0 0 0 0 0 0 0 0 0 0 x
0 0 0 0 0 0 0 1 0 0 x
0 0 0 0 0 0 0 0 0 0 x
0 0 0 0 0 0 0 1 0 0 x
0 0 0 0 0 0 0 0 0 0 x
0 0 0 0 0 0 0 1 0 0 x
0 0 0 0 0 0 0 0 0 0 x
0 0 0 0 0 0 0 1 0 0 x
0 0 0 0 0 0 0 0 0 0 x
0 0 0 0 0 0 0 1 0 0 x
0 0 0 0 0 0 0 0 0 0 x
0 0 0 0 0 0 0 1 0 0 x
0 0 0 0 0 0 0 0 0 0 x
0 0 0 0 0 0 0 1 0 0 x
0 0 0 0 0 0 0 0 0 0 x
0 0 0 0 0 0 0 1 0 0 x
0 0 0 0 0 0 0 0 0 0 x
0 0 0 0 0 0 0 1 0 0 x
0 0 0 0 0 0 0 0 0 0 x
0 0 0 0 0 0 0 1 0 0 x
0 0 0 0 0 0 0 0 0 0 x
0 0 0 0 0 0 0 1 0 0 x
0 0 0 0 0 0 0 0 0 0 x
0 0 0 0 0 0 0 1 0 0 x
0 0 0 0 0 0 0 0 0 0 x
0 0 0 0 0 0 0 1 0 0 x
0 0 271 0 1 0 0 0 0 0 x
0 0 271 0 1 0 0 1 0 0 x
0 0 565 0 1 0 0 0 0 0 x
0 0 565 0 1 0 0 1 0 0 x
0 0 2309 0 1 0 0 0 0 0 x
0 0 2309 0 1 0 0 1 0 0 x
0 0 4352 0 1 0 0 0 0 0 x
0 0 4352 0 1 0 0 1 0 0 x
0 0 2818 0 1 0 0 0 0 0 x
0 0 2818 0 1 0 0 1 0 0 x
0 0 2311 0 1 0 0 0 0 0 x
0 0 2311 0 1 0 0 1 0 0 x
0 0 4366 0 1 0 0 0 0 0 x
0 0 4366 0 1 0 0 1 0 0 x
0 0 12 0 1 0 0 0 0 0 x
0 0 12 0 1 0 0 1 0 0 x
0 0 4359 0 1 0 0 0 0 0 x
0 0 4359 0 1 0 0 1 0 0 x
0 0 2819 0 1 0 0 0 0 0 x
0 0 2819 0 1 0 0 1 0 0 x
0 0 7936 0 1 0 0 0 0 0 x
0 0 7936 0 1 0 0 1 0 0 x
0 0 0 0 0 0 0 0 0 0 x
0 0 0 0 0 0 0 1 0 0 x
0 0 0 0 0 0 0 0 0 0 x
0 0 0 0 0 0 0 1 0 0 x
0 0 0 0 0 0 0 0 0 0 x
0 0 0 0 0 0 0 1 0 0 x
0 0 0 0 0 0 0 0 0 0 x
0 0 0 0 0 0 0 1 0 0 x
0 0 0 0 0 0 0 0 0 0 x
0 0 0 0 0 0 0 1 0 0 x
0 0 0 0 0 0 0 0 0 0 x
0 0 0 0 0 0 0 1 0 0 x
0 0 0 0 0 0 0 0 0 0 x
0 0 0 0 0 0 0 1 0 0 x
0 0 0 0 0 0 0 0 0 0 x
0 0 0 0 0 0 0 1 0 0 x
0 0 0 0 0 0 0 0 0 0 x
0 0 0 0 0 0 0 1 0 0 x
0 0 0 0 0 0 0 0 0 0 x
0 0 0 0 0 0 0 1 0 0 x
0 0 0 0 0 0 0 0 0 0 x
0 0 0 0 0 0 0 1 0 0 x
0 0 0 0 0 0 0 0 0 0 x
0 0 0 0 0 0 0 1 0 0 x
0 0 0 0 0 1 0 0 0 0 x
0 0 0 0 0 1 0 1 0 0 x
0 0 0 0 0 0 0 0 x 0 x
0 0 0 0 0 0 0 1 x 0 x
0 0 0 0 0 0 0 0 x 0 x
0 0 0 0 0 0 0 1 x 0 x
0 0 0 0 0 0 0 0 x 0 x
0 0 0 0 0 0 0 1 x 0 x
0 0 0 0 0 0 0 0 x 0 x
0 0 0 0 0 0 0 1 x 0 x
0 0 0 0 0 0 0 0 x 0 x
0 0 0 0 0 0 0 1 x 0 x
0 0 0 0 0 0 0 0 x 0 x
0 0 0 0 0 0 0 1 x 0 x
0 0 0 0 0 0 0 0 x 0 x
0 0 0 0 0 0 0 1 x 0 x
0 0 0 0 0 0 0 0 x 0 x
0 0 0 0 0 0 0 1 x 0 x
0 0 0 0 0 0 0 0 x 0 x
0 0 0 0 0 0 0 1 x 0 x
0 0 0 0 0 0 0 0 x 0 x
0 0 0 0 0 0 0 1 x 0 x
0 0 0 0 0 0 0 0 x 0 x
0 0 0 0 0 0 0 1 x 0 x
0 0 0 0 0 0 0 0 x 0 x
0 0 0 0 0 0 0 1 x 0 x
0 0 0 0 0 0 0 0 x 0 x
0 0 0 0 0 0 0 1 x 0 x
0 0 0 0 0 0 0 0 x 0 x
0 0 0 0 0 0 0 1 x 0 x
0 0 0 0 0 0 0 0 x 0 x
0 0 0 0 0 0 0 1 x 0 x
0 0 0 0 0 0 0 0 x 0 x
0 0 0 0 0 0 0 1 x 0 x
0 0 0 0 0 0 0 0 x 0 x
0 0 0 0 0 0 0 1 x 0 x
0 0 0 0 0 0 0 0 x 0 x
0 0 0 0 0 0 0 1 x 0 x
0 0 0 0 0 0 0 0 x 0 x
0 0 0 0 0 0 0 1 x 0 x
0 0 0 0 0 0 0 0 x 0 x
0 0 0 0 0 0 0 1 x 0 x
0 0 0 0 0 0 0 0 x 0 x
0 0 0 0 0 0 0 1 x 0 x
0 0 0 0 0 0 0 0 x 0 x
0 0 0 0 0 0 0 1 x 0 x
0 0 0 0 0 0 0 0 x 0 x
0 0 0 0 0 0 0 1 x 0 x
0 0 0 0 0 0 0 0 x 0 x
0 0 0 0 0 0 0 1 x 0 x
0 0 0 0 0 0 0 0 x 0 x
0 0 0 0 0 0 0 1 x 0 x
0 0 0 0 0 0 0 0 x 0 x
0 0 0 0 0 0 0 1 1 0 x
0 0 0 0 0 0 1 0 1 0 x
0 0 0 0 0 0 1 1 1 0 0
0 0 0 0 0 0 0 0 1 0 0
0 0 0 0 0 0 0 1 1 0 0
0 0 0 0 0 0 0 0 1 0 0
0 0 0 0 0 0 0 1 1 0 60
0 0 0 0 0 0 0 0 1 0 60
0 0 0 0 0 0 0 1 1 0 118
0 0 0 0 0 0 0 0 1 0 118
0 0 0 0 0 0 0 1 1 0 0
0 0 0 0 0 0 0 0 1 0 0
0 0 0 0 0 0 0 1 1 0 0
0 0 0 0 0 0 0 0 1 0 0
0 0 0 0 0 0 0 1 1 0 0
0 0 0 0 0 0 0 0 1 0 0
0 0 0 0 0 0 0 1 1 0 0
0 0 0 0 0 0 0 0 1 0 0
0 0 0 0 0 0 0 1 1 0 0
0 0 0 0 0 0 0 0 1 0 0
0 0 0 0 0 0 0 1 1 0 0
0 0 0 0 0 0 0 0 1 0 0
0 0 0 0 0 0 0 1 1 0 0
0 0 0 0 0 0 0 0 1 0 0
0 0 0 0 0 0 0 1 1 0 0
0 0 0 0 0 0 0 0 1 0 0
0 0 0 0 0 0 0 1 1 0 0
0 0 0 0 0 0 0 0 1 0 0
0 0 0 0 0 0 0 1 1 0 0
0 0 0 0 0 0 0 0 1 0 0
0 0 0 0 0 0 0 1 1 0 0
0 0 0 0 0 0 0 0 1 0 0
0 0 0 0 0 0 0 1 1 0 0
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*/

/* Test case 01_P01T5:
M N progIN reset progLoad start result clk valid done output
0 0 0 0 0 0 0 0 x x x
0 0 0 0 0 0 0 1 x x x
0 0 0 1 0 0 0 0 x x x
0 0 0 1 0 0 0 1 0 0 x
0 0 0 0 0 0 0 0 0 0 x
0 0 0 0 0 0 0 1 0 0 x
0 0 0 0 0 0 0 0 0 0 x
0 0 0 0 0 0 0 1 0 0 x
0 0 0 0 0 0 0 0 0 0 x
0 0 0 0 0 0 0 1 0 0 x
0 0 0 0 0 0 0 0 0 0 x
0 0 0 0 0 0 0 1 0 0 x
0 0 0 0 0 0 0 0 0 0 x
0 0 0 0 0 0 0 1 0 0 x
0 0 0 0 0 0 0 0 0 0 x
0 0 0 0 0 0 0 1 0 0 x
0 0 0 0 0 0 0 0 0 0 x
0 0 0 0 0 0 0 1 0 0 x
0 0 0 0 0 0 0 0 0 0 x
0 0 0 0 0 0 0 1 0 0 x
0 0 0 0 0 0 0 0 0 0 x
0 0 0 0 0 0 0 1 0 0 x
0 0 0 0 0 0 0 0 0 0 x
0 0 0 0 0 0 0 1 0 0 x
0 0 0 0 0 0 0 0 0 0 x
0 0 0 0 0 0 0 1 0 0 x
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*/

/* Test case 01_P01T6:
M N progIN reset progLoad start result clk valid done output
0 0 0 0 0 0 0 0 x x x
0 0 0 0 0 0 0 1 x x x
0 0 0 1 0 0 0 0 x x x
0 0 0 1 0 0 0 1 0 0 x
0 0 0 0 0 0 0 0 0 0 x
0 0 0 0 0 0 0 1 0 0 x
0 0 0 0 0 0 0 0 0 0 x
0 0 0 0 0 0 0 1 0 0 x
0 0 0 0 0 0 0 0 0 0 x
0 0 0 0 0 0 0 1 0 0 x
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*/

/* Test case 01_P01T7:
M N progIN reset progLoad start result clk valid done output
0 0 0 0 0 0 0 0 x x x
0 0 0 0 0 0 0 1 x x x
0 0 0 1 0 0 0 0 x x x
0 0 0 1 0 0 0 1 0 0 x
0 0 0 0 0 0 0 0 0 0 x
0 0 0 0 0 0 0 1 0 0 x
0 0 0 0 0 0 0 0 0 0 x
0 0 0 0 0 0 0 1 0 0 x
0 0 0 0 0 0 0 0 0 0 x
0 0 0 0 0 0 0 1 0 0 x
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*/

/* Test case 01_P01T8:
M N progIN reset progLoad start result clk valid done output
0 0 0 0 0 0 0 0 x x x
0 0 0 0 0 0 0 1 x x x
0 0 0 1 0 0 0 0 x x x
0 0 0 1 0 0 0 1 0 0 x
0 0 0 0 0 0 0 0 0 0 x
0 0 0 0 0 0 0 1 0 0 x
0 0 0 0 0 0 0 0 0 0 x
0 0 0 0 0 0 0 1 0 0 x
0 0 0 0 0 0 0 0 0 0 x
0 0 0 0 0 0 0 1 0 0 x
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*/

/* Test case super-testcase:
M N progIN reset progLoad start result clk valid done output
0 0 0 0 0 0 0 0 0 0 0
0 0 0 0 0 0 0 1 0 0 0
0 0 0 1 0 0 0 0 0 0 0
0 0 0 1 0 0 0 1 0 0 0
0 0 0 0 0 0 0 0 0 0 0
0 0 0 0 0 0 0 1 0 0 0
0 0 0 0 0 0 0 0 0 0 0
0 0 0 0 0 0 0 1 0 0 0
0 0 0 0 0 0 0 0 0 0 0
0 0 0 0 0 0 0 1 0 0 0
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*/

/* Test case Primetest:
M N progIN reset progLoad start result clk valid done output
0 0 0 0 0 0 0 0 x x x
0 0 0 0 0 0 0 1 x x x
0 0 0 1 0 0 0 0 x x x
0 0 0 1 0 0 0 1 0 0 0
0 0 0 0 0 0 0 0 0 0 0
0 0 0 0 0 0 0 1 0 0 0
0 0 0 0 0 0 0 0 0 0 0
0 0 0 0 0 0 0 1 0 0 0
0 0 0 0 0 0 0 0 0 0 0
0 0 0 0 0 0 0 1 0 0 0
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*/

/* Test case JUMP:
M N progIN reset progLoad start result clk valid done output
0 0 0 0 0 0 0 0 x x x	
0 0 0 0 0 0 0 1 x x x	
0 0 0 1 0 0 0 0 x x x	
0 0 0 1 0 0 0 1 0 0 0	
0 0 0 0 0 0 0 0 0 0 0	
0 0 0 0 0 0 0 1 0 0 0	
0 0 0 0 0 0 0 0 0 0 0	
0 0 0 0 0 0 0 1 0 0 0	
0 0 0 0 0 0 0 0 0 0 0	
0 0 0 0 0 0 0 1 0 0 0	
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*/

/* Test case comment19:
M N progIN reset progLoad start result clk valid done output
0 0 0 0 0 0 0 0 0 0 0
0 0 0 0 0 0 0 1 0 0 0
0 0 0 1 0 0 0 0 0 0 0
0 0 0 1 0 0 0 1 0 0 0
0 0 0 0 0 0 0 0 0 0 0
0 0 0 0 0 0 0 1 0 0 0
0 0 0 0 0 0 0 0 0 0 0
0 0 0 0 0 0 0 1 0 0 0
0 0 0 0 0 0 0 0 0 0 0
0 0 0 0 0 0 0 1 0 0 0
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*/

/* Test case Triple_JUMP:
M N progIN reset progLoad start result clk valid done output
0 0 0 0 0 0 0 0 x x x
0 0 0 0 0 0 0 1 x x x
0 0 0 1 0 0 0 0 x x x
0 0 0 1 0 0 0 1 0 0 0
0 0 0 0 0 0 0 0 0 0 0
0 0 0 0 0 0 0 1 0 0 0
0 0 0 0 0 0 0 0 0 0 0
0 0 0 0 0 0 0 1 0 0 0
0 0 0 0 0 0 0 0 0 0 0
0 0 0 0 0 0 0 1 0 0 0
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*/

/* Test case reset_test:
M N progIN reset progLoad start result clk valid done output
0 0 0 0 0 0 0 0 x x x
0 0 0 0 0 0 0 1 x x x
0 0 0 1 0 0 0 0 x x x
0 0 0 1 0 0 0 1 x x x
0 0 0 0 0 0 0 0 x x x
0 0 0 0 0 0 0 1 x x x
0 0 0 0 0 0 0 0 x x x
0 0 0 0 0 0 0 1 x x x
0 0 0 0 0 0 0 0 x x x
0 0 0 0 0 0 0 1 x x x
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*/

/* Test case rRAM_test:
M N progIN reset progLoad start result clk valid done output
0 0 0 0 0 0 0 0 0 0 0
0 0 0 0 0 0 0 1 0 0 0
0 0 0 1 0 0 0 0 0 0 0
0 0 0 1 0 0 0 1 0 0 0
0 0 0 0 0 0 0 0 0 0 0
0 0 0 0 0 0 0 1 0 0 0
0 0 0 0 0 0 0 0 0 0 0
0 0 0 0 0 0 0 1 0 0 0
0 0 0 0 0 0 0 0 0 0 0
0 0 0 0 0 0 0 1 0 0 0
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*/

/* Test case tworoundprocess:
M N progIN reset progLoad start result clk valid done output
0 0 0 0 0 0 0 0 x x x
0 0 0 0 0 0 0 1 x x x
0 0 0 1 0 0 0 0 x x x
0 0 0 1 0 0 0 1 x x x
0 0 0 0 0 0 0 0 x x x
0 0 0 0 0 0 0 1 x x x
0 0 0 0 0 0 0 0 x x x
0 0 0 0 0 0 0 1 x x x
0 0 0 0 0 0 0 0 x x x
0 0 0 0 0 0 0 1 x x x
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*/

/* Test case reset-during-test:
M N progIN reset progLoad start result clk valid done output
0 0 0 0 0 0 0 0 x x x
0 0 0 0 0 0 0 1 x x x
0 0 0b0000100001111 0 1 0 0 0 0 0 x
0 0 0b0000100001111 0 1 0 0 1 0 0 x
0 0 0b0001000101111 1 1 0 0 0 0 0 x
0 0 0b0001000101111 1 1 0 0 1 0 0 x
0 0 0b1111100001111 0 1 0 0 0 0 0 x
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*/

/* Test case pRamLoad:
M N progIN reset progLoad start result clk valid done output	
0 0 0 0 0 0 0 0 x x x	
0 0 0 0 0 0 0 1 x x x	
0 0 0 1 0 0 0 0 x x x	
0 0 0 1 0 0 0 1 0 0 0	
0 0 0 0 0 0 0 0 0 0 0	
0 0 0 0 0 0 0 1 0 0 0	
0 0 0 0 0 0 0 0 0 0 0	
0 0 0 0 0 0 0 1 0 0 0	
0 0 0 0 0 0 0 0 0 0 0	
0 0 0 0 0 0 0 1 0 0 0	
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*/

/* Test case result-again:
M N progIN reset progLoad start result clk valid done output
0 0 0 0 0 0 0 0 x x x
0 0 0 0 0 0 0 1 x x x
0 0 0 1 0 0 0 0 x x x
0 0 0 1 0 0 0 1 0 0 0
0 0 0 0 0 0 0 0 0 0 0
0 0 0 0 0 0 0 1 0 0 0
0 0 0 0 0 0 0 0 0 0 0
0 0 0 0 0 0 0 1 0 0 0
0 0 0 0 0 0 0 0 0 0 0
0 0 0 0 0 0 0 1 0 0 0
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*/

/* Test case start-again:
M N progIN reset progLoad start result clk valid done output
0 0 0 0 0 0 0 0 x x x
0 0 0 0 0 0 0 1 x x x
0 0 0 1 0 0 0 0 x x x
0 0 0 1 0 0 0 1 0 0 0
0 0 0 0 0 0 0 0 0 0 0
0 0 0 0 0 0 0 1 0 0 0
0 0 0 0 0 0 0 0 0 0 0
0 0 0 0 0 0 0 1 0 0 0
0 0 0 0 0 0 0 0 0 0 0
0 0 0 0 0 0 0 1 0 0 0
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*/

/* Test case newworld:
M N progIN reset progLoad start result clk valid done output
0 0 0 0 0 0 0 0 x x x
0 0 0 0 0 0 0 1 x x x
0 0 0 1 0 0 0 0 x x x
0 0 0 1 0 0 0 1 0 0 0
0 0 0 0 0 0 0 0 0 0 0
0 0 0 0 0 0 0 1 0 0 0
0 0 0 0 0 0 0 0 0 0 0
0 0 0 0 0 0 0 1 0 0 0
0 0 0 0 0 0 0 0 0 0 0
0 0 0 0 0 0 0 1 0 0 0
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*/

/* Test case check0x00aftereset:
M N progIN reset progLoad start result clk valid done output
0 0 0 0 0 0 0 0 x x x
0 0 0 0 0 0 0 1 x x x
0 0 0 1 0 0 0 0 x x x
0 0 0 1 0 0 0 1 x x x
0 0 0 0 0 0 0 0 x x x
0 0 0 0 0 0 0 1 x x x
0 0 0 0 0 0 0 0 x x x
0 0 0 0 0 0 0 1 x x x
0 0 0 0 0 0 0 0 x x x
0 0 0 0 0 0 0 1 x x x
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*/

/* Test case swaptest:
M N progIN reset progLoad start result clk valid done output
0 0 0 0 0 0 0 0 x x x
0 0 0 0 0 0 0 1 x x x
0 0 0 1 0 0 0 0 x x x
0 0 0 1 0 0 0 1 x x x
0 0 0 0 0 0 0 0 x x x
0 0 0 0 0 0 0 1 x x x
0 0 0 0 0 0 0 0 x x x
0 0 0 0 0 0 0 1 x x x
0 0 0 0 0 0 0 0 x x x
0 0 0 0 0 0 0 1 x x x
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*/

/* Test case lcmtest:
M N progIN reset progLoad start result clk valid done output
0 0 0 0 0 0 0 0 x x x
0 0 0 0 0 0 0 1 x x x
0 0 0 1 0 0 0 0 x x x
0 0 0 1 0 0 0 1 x x x
0 0 0 0 0 0 0 0 x x x
0 0 0 0 0 0 0 1 x x x
0 0 0 0 0 0 0 0 x x x
0 0 0 0 0 0 0 1 x x x
0 0 0 0 0 0 0 0 x x x
0 0 0 0 0 0 0 1 x x x
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*/

/* Test case lcmtest2:
M N progIN reset progLoad start result clk valid done output
0 0 0 0 0 0 0 0 x x x
0 0 0 0 0 0 0 1 x x x
0 0 0 1 0 0 0 0 x x x
0 0 0 1 0 0 0 1 x x x
0 0 0 0 0 0 0 0 x x x
0 0 0 0 0 0 0 1 x x x
0 0 0 0 0 0 0 0 x x x
0 0 0 0 0 0 0 1 x x x
0 0 0 0 0 0 0 0 x x x
0 0 0 0 0 0 0 1 x x x
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*/

/* Test case lcmtest3:
M N progIN reset progLoad start result clk valid done output
0 0 0 0 0 0 0 0 x x x
0 0 0 0 0 0 0 1 x x x
0 0 0 1 0 0 0 0 x x x
0 0 0 1 0 0 0 1 x x x
0 0 0 0 0 0 0 0 x x x
0 0 0 0 0 0 0 1 x x x
0 0 0 0 0 0 0 0 x x x
0 0 0 0 0 0 0 1 x x x
0 0 0 0 0 0 0 0 x x x
0 0 0 0 0 0 0 1 x x x
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*/

/* Test case lcmtest4:
M N progIN reset progLoad start result clk valid done output
0 0 0 0 0 0 0 0 x x x
0 0 0 0 0 0 0 1 x x x
0 0 0 1 0 0 0 0 x x x
0 0 0 1 0 0 0 1 0 0 x
0 0 0 0 0 0 0 0 0 0 x
0 0 0 0 0 0 0 1 0 0 x
0 0 0 0 0 0 0 0 0 0 x
0 0 0 0 0 0 0 1 0 0 x
0 0 0 0 0 0 0 0 0 0 x
0 0 0 0 0 0 0 1 0 0 x
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*/
