// Digital circuit TEMPLATE V1.dig as structural Verilog
module TEMPLATE_V1 (
  input  [7:0] M,
  input  [7:0] N,
  input  [12:0] progIN,
  input  reset,
  input  progLoad,
  input  start,
  input  result,
  input  clk,
  output valid,
  output done,
  output [7:0] \output ,
  output [7:0] cnt,
  output [7:0] r_cnt,
  output [12:0] out_14,
  output [7:0] out_15,
  output [7:0] out_16,
  output [7:0] out_17,
  output [7:0] out_18
);

  wire _00, _00000, _00000op, _00001, _01, _00001op, _00010, _10, _00010op, _00011, _11, _00011op, _00100,
       _00100op, _00101, _00101op, _00110, _00110op, _00111, _00111op, _01000, _01000op, _01001, _01001op,
       _01010, _01010op, _01011, _01011op, _01100, _01100op, _01101, _01101op, _01110, _01110op, _01111,
       _01111op, _10000, _10000op, _10001, _10001op, _10010, _10010op, _10011, _10011op, _10100, _10100op,
       _10101, _10101op, _10110, _10110op, _10111, _10111op, _11000, _11000op, _11001, _11001op, _11010,
       _11010op, _11011, _11011op, _11100, _11100op, _11101, _11101op, _11110, _11110op, _11111, _11111op,
       and_1_out, and_2_out, and_3_out, and_4_out, and_5_out, and_6_out, and_7_out, and_8_out, and_9_out,
       and_10_out, and_11_out, and_12_out, and_13_out, and_14_out, and_15_out, and_16_out, and_17_out,
       and_18_out, and_19_out, and_20_out, and_21_out, and_22_out, and_23_out, and_24_out, and_25_out,
       and_26_out, and_27_out, and_28_out, and_29_out, driver_3_out, driver_4_out, driver_5_out, eq, eq_t,
       gr, gt, isprimefinal_1_p2, le, lt, multiplexer_11_out, multiplexer_15_out, multiplexer_16_out,
       multiplexer_17_out, multiplexer_18_out, multiplexer_19_out, multiplexer_20_out, multiplexer_21_out,
       not_1_out, not_2_out, not_3_out, not_4_out, not_5_out, not_6_out, not_7_out, or_1_out, or_2_out,
       or_3_out, or_4_out, or_5_out, or_6_out, or_7_out, or_8_out, or_9_out, or_15_out, or_16_out, P_a, P_b,
       priorityencoder_2_num, Q_a, Q_a_plus__op, Q_b, Q_b_plus__op, Q_c, Q_c_plus__op, Q_d, Q_d_plus__op,
       Q_e, Q_e_plus__op, r_cnt_eq_16, r_cnt_eq_cnt, r_cnt_gt_16, r_cnt_gt_cnt, r_cnt_lt_16, r_cnt_lt_cnt,
       result_cnt_eq_16, result_cnt_gt_16, result_cnt_lt_16, result_t, start_t;
  wire [1:0] priorityencoder_3_num;
  wire [2:0] priorityencoder_1_num;
  wire [7:0] alu_1_alu, d_ff_3_q, driver_1_out, driver_2_out, multiplexer_2_out, multiplexer_3_out,
       multiplexer_4_out, multiplexer_8_out, multiplexer_9_out, multiplexer_10_out, multiplexer_12_out,
       multiplexer_13_out, multiplexer_14_out, pc, pRAM_operand, result_cnt, rRAM_operand;
  wire [12:0] multiplexer_1_out, multiplexer_7_out;
  wire [12:8] pRAM_reserve_d2;

  or or_1 (or_1_out, _00010, _00100);
  not not_1 (not_1_out, _00010);
  or or_2 (or_2_out, _00000, _11100);
  and and_1 (and_1_out, not_1_out, _00011);
  assign driver_1_out = _11011 ? out_14[7:0] : 8'bz;  // Driver driver_1
  CounterPreset #(.maxValue(256), .Bits(8)) u_cnt (
    .en(progLoad), .C(clk), .dir(1'b0), .in({8{1'b0}}), .ld(1'b0), .clr(and_1_out), .out(cnt));  // open: ovf
  CounterPreset #(.maxValue(256), .Bits(8)) u_r_cnt (
    .en(or_1_out), .C(clk), .dir(1'b0), .in({8{1'b0}}), .ld(1'b0), .clr(or_2_out), .out(r_cnt));  // open: ovf
  Comparator #(.Bits(8)) u_r_cnt_eq_16 (.a(r_cnt), .b(8'h10), .gt(r_cnt_gt_16), .eq(r_cnt_eq_16), .lt(r_cnt_lt_16));
  Comparator #(.Bits(8)) u_r_cnt_eq_cnt (.a(r_cnt), .b(cnt), .gt(r_cnt_gt_cnt), .eq(r_cnt_eq_cnt), .lt(r_cnt_lt_cnt));
  CounterPreset #(.maxValue(256), .Bits(8)) u_pc (
    .en(_11010), .C(clk), .dir(1'b0), .in(driver_1_out), .ld(_11011), .clr(_00000), .out(pc));  // open: ovf
  CounterPreset #(.maxValue(256), .Bits(8)) u_result_cnt (
    .en(_01), .C(clk), .dir(1'b0), .in({8{1'b0}}), .ld(1'b0), .clr(_00), .out(result_cnt));  // open: ovf
  Comparator #(.Bits(8)) comparator_1 (
    .a(result_cnt), .b(8'h10), .gt(result_cnt_gt_16), .eq(result_cnt_eq_16), .lt(result_cnt_lt_16));
  D_FF d_ff_1 (.D(start), .C(clk), .Q(start_t));  // open: nQ
  D_FF d_ff_2 (.D(result), .C(clk), .Q(result_t));  // open: nQ
  Multiplexer #(.Bits(13)) multiplexer_1 (.sel(_00010), .in_0(progIN), .in_1({13{1'b0}}), .out(multiplexer_1_out));
  Multiplexer #(.Bits(8)) multiplexer_2 (.sel(_00100), .in_0(out_14[7:0]), .in_1(r_cnt), .out(multiplexer_2_out));
  or or_3 (or_3_out, _00001, _00010);
  or or_4 (or_4_out, _00100, _10000);
  Multiplexer #(.Bits(8)) multiplexer_3 (.sel(_00100), .in_0(out_15), .in_1({8{1'b0}}), .out(multiplexer_3_out));
  Multiplexer #(.Bits(8)) multiplexer_4 (.sel(_00010), .in_0(cnt), .in_1(r_cnt), .out(multiplexer_4_out));
  D_FF #(.Bits(8)) d_ff_3 (.D(out_14[7:0]), .C(clk), .Q(d_ff_3_q));  // open: nQ
  RAMDualAccess #(.AddrBits(8), .Bits(13)) pRAM_reserve (
    .str(or_3_out), .C(clk), .ld(1'b0), .A1(multiplexer_4_out), .Din1(multiplexer_1_out), .A2(out_14[7:0]),
    .D2({pRAM_reserve_d2, pRAM_operand}));  // open: D1
  RAMDualAccess #(.AddrBits(8), .Bits(8)) rRAM_reserve (
    .str(or_4_out), .C(clk), .ld(1'b0), .A1(multiplexer_2_out), .Din1(multiplexer_3_out), .A2(out_14[7:0]),
    .D2(rRAM_operand));  // open: D1
  Multiplexer multiplexer_5 (.sel(_00011), .in_0(_11100), .in_1(1'b0), .out(valid));
  Multiplexer multiplexer_6 (.sel(_00011), .in_0(_10), .in_1(1'b0), .out(done));
  Multiplexer #(.Bits(13)) multiplexer_7 (.sel(_00010), .in_0(progIN), .in_1({13{1'b0}}), .out(multiplexer_7_out));
  Multiplexer #(.Bits(8)) multiplexer_8 (.sel(_00100), .in_0(d_ff_3_q), .in_1(r_cnt), .out(multiplexer_8_out));
  or or_5 (or_5_out, progLoad, _00010);
  Multiplexer #(.Bits(8)) multiplexer_9 (.sel(_00010), .in_0(cnt), .in_1(r_cnt), .out(multiplexer_9_out));
  assign driver_2_out = _00101 ? pc : 8'bz;  // Driver driver_2
  or or_6 (or_6_out, _00100, _10000);
  Multiplexer #(.Bits(8)) multiplexer_10 (.sel(_00100), .in_0(out_15), .in_1({8{1'b0}}), .out(multiplexer_10_out));
  RAMDualAccess #(.AddrBits(8), .Bits(13)) pRAM (
    .str(or_5_out), .C(clk), .ld(1'b0), .A1(multiplexer_9_out), .Din1(multiplexer_7_out), .A2(driver_2_out),
    .D2(out_14));  // open: D1
  RAMDualAccess #(.AddrBits(8), .Bits(8)) rRAM (
    .str(or_6_out), .C(clk), .ld(1'b0), .A1(multiplexer_8_out), .Din1(multiplexer_10_out), .A2(result_cnt),
    .D2(\output ));  // open: D1
  Seven_Seg_Hex seven_seg_hex_1 (.d(\output [7:4]), .dp(1'b0));
  Seven_Seg_Hex seven_seg_hex_2 (.d(\output [3:0]), .dp(1'b0));
  // isprimeFinal isprimefinal_1: pin names not known; wires that end beside it: out_15, isprimefinal_1_p2
  assign driver_3_out = _10110 ? eq : 1'bz;  // Driver driver_3
  Comparator #(.Bits(8)) comparator_2 (.a(out_15), .b(out_16), .gt(gt), .eq(eq), .lt(lt));
  Multiplexer multiplexer_11 (.sel(_11000), .in_0(driver_3_out), .in_1(isprimefinal_1_p2), .out(multiplexer_11_out));
  assign driver_4_out = _10110 ? gt : 1'bz;  // Driver driver_4
  assign driver_5_out = _10110 ? lt : 1'bz;  // Driver driver_5
  D_FF u_gr (.D(driver_4_out), .C(clk), .Q(gr));  // open: nQ
  D_FF u_eq (.D(multiplexer_11_out), .C(clk), .Q(eq_t));  // open: nQ
  D_FF u_le (.D(driver_5_out), .C(clk), .Q(le));  // open: nQ
  Multiplexer #(.Selector_Bits(3), .Bits(8)) multiplexer_12 (
    .sel(priorityencoder_1_num), .in_0(out_14[7:0]), .in_1(out_16), .in_2(out_17), .in_3(pRAM_operand),
    .in_4(rRAM_operand), .in_5(out_18), .in_6({8{1'b0}}), .in_7({8{1'b0}}), .out(multiplexer_12_out));
  PriorityEncoder #(.Selector_Bits(3)) priorityencoder_1 (
    .in0(_00110), .in1(_01000), .in2(_01011), .in3(_01110), .in4(_01111), .in5(_11001), .in6(1'b0),
    .in7(1'b0), .num(priorityencoder_1_num));  // open: any
  Multiplexer #(.Bits(8)) multiplexer_13 (
    .sel(priorityencoder_2_num), .in_0(out_14[7:0]), .in_1(out_15), .out(multiplexer_13_out));
  PriorityEncoder priorityencoder_2 (.in0(_00111), .in1(_01001), .num(priorityencoder_2_num));  // open: any
  or or_7 (or_7_out, _00110, _01000, _01011, _01110, _01111, _11001);
  or or_8 (or_8_out, _00111, _01001);
  or or_9 (or_9_out, _01010, _01100, _01101);
  PriorityEncoder #(.Selector_Bits(2)) priorityencoder_3 (
    .in0(_01010), .in1(_01100), .in2(_01101), .in3(1'b0), .num(priorityencoder_3_num));  // open: any
  Multiplexer #(.Selector_Bits(2), .Bits(8)) multiplexer_14 (
    .sel(priorityencoder_3_num), .in_0(out_15), .in_1(M), .in_2(N), .in_3({8{1'b0}}), .out(multiplexer_14_out));
  Register #(.Bits(8)) accA (.D(multiplexer_12_out), .C(clk), .en(or_7_out), .Q(out_15));
  Register #(.Bits(8)) accB (.D(multiplexer_13_out), .C(clk), .en(or_8_out), .Q(out_16));
  Register #(.Bits(8)) regC (.D(multiplexer_14_out), .C(clk), .en(or_9_out), .Q(out_17));
  not not_2 (not_2_out, reset);
  not not_3 (not_3_out, result_cnt_eq_16);
  not not_4 (not_4_out, reset);
  Multiplexer #(.Selector_Bits(5)) multiplexer_15 (
    .sel({Q_a, Q_b, Q_c, Q_d, Q_e}), .in_0(1'b0), .in_1(1'b0), .in_2(1'b0), .in_3(1'b0), .in_4(1'b0),
    .in_5(Q_a_plus__op), .in_6(1'b1), .in_7(1'b1), .in_8(1'b1), .in_9(1'b1), .in_10(1'b1), .in_11(1'b1),
    .in_12(1'b1), .in_13(1'b1), .in_14(1'b1), .in_15(1'b1), .in_16(1'b1), .in_17(1'b1), .in_18(1'b1),
    .in_19(1'b1), .in_20(1'b1), .in_21(1'b1), .in_22(1'b1), .in_23(1'b1), .in_24(1'b1), .in_25(1'b1),
    .in_26(1'b0), .in_27(1'b0), .in_28(not_2_out), .in_29(1'b0), .in_30(1'b0), .in_31(1'b0),
    .out(multiplexer_15_out));
  Multiplexer #(.Selector_Bits(2)) multiplexer_16 (
    .sel({P_a, P_b}), .in_0(1'b0), .in_1(result_cnt_eq_16), .in_2(not_4_out), .in_3(1'b0),
    .out(multiplexer_16_out));
  Multiplexer #(.Selector_Bits(2)) multiplexer_17 (
    .sel({P_a, P_b}), .in_0(result_t), .in_1(not_3_out), .in_2(1'b0), .in_3(1'b0), .out(multiplexer_17_out));
  ALU alu_1 (.accA(out_15), .accB(out_16), .opcode(out_14[11:8]), .ALU(alu_1_alu));
  D_FF d_ff_4 (.D(multiplexer_15_out), .C(clk), .Q(Q_a));  // open: nQ
  D_FF d_ff_5 (.D(multiplexer_16_out), .C(clk), .Q(P_a));  // open: nQ
  D_FF d_ff_6 (.D(multiplexer_17_out), .C(clk), .Q(P_b));  // open: nQ
  D_FF #(.Bits(8)) d_ff_7 (.D(alu_1_alu), .C(clk), .Q(out_18));  // open: nQ
  not not_5 (not_5_out, reset);
  Multiplexer #(.Selector_Bits(5)) multiplexer_18 (
    .sel({Q_a, Q_b, Q_c, Q_d, Q_e}), .in_0(1'b0), .in_1(1'b0), .in_2(1'b0), .in_3(1'b0), .in_4(1'b0),
    .in_5(Q_b_plus__op), .in_6(1'b1), .in_7(1'b1), .in_8(1'b1), .in_9(1'b1), .in_10(1'b1), .in_11(1'b1),
    .in_12(1'b1), .in_13(1'b1), .in_14(1'b1), .in_15(1'b1), .in_16(1'b1), .in_17(1'b1), .in_18(1'b1),
    .in_19(1'b1), .in_20(1'b1), .in_21(1'b1), .in_22(1'b1), .in_23(1'b1), .in_24(1'b1), .in_25(1'b1),
    .in_26(1'b0), .in_27(1'b0), .in_28(not_5_out), .in_29(1'b0), .in_30(1'b0), .in_31(1'b0),
    .out(multiplexer_18_out));
  Decoder #(.Selector_Bits(2)) decoder_1 (.sel({P_a, P_b}), .out_0(_00), .out_1(_01), .out_2(_10), .out_3(_11));
  D_FF d_ff_8 (.D(multiplexer_18_out), .C(clk), .Q(Q_b));  // open: nQ
  and and_2 (and_2_out, ~out_14[11], ~out_14[10], ~out_14[9], ~out_14[8]);  // And
  and and_3 (and_3_out, out_14[11], out_14[9], out_14[8]);
  and and_4 (and_4_out, out_14[11], out_14[10]);
  and and_5 (and_5_out, out_14[11], ~out_14[10], ~out_14[9]);  // And
  and and_6 (and_6_out, out_14[11], ~out_14[10], ~out_14[8]);  // And
  and and_7 (and_7_out, out_14[12], out_14[11], out_14[8]);
  and and_8 (and_8_out, ~out_14[12], ~out_14[11], ~out_14[9], ~out_14[8]);  // And
  and and_9 (and_9_out, ~out_14[12], ~out_14[11], out_14[9], out_14[8]);  // And
  and and_10 (and_10_out, ~out_14[12], ~out_14[11], out_14[10]);  // And
  and and_11 (and_11_out, out_14[12], ~out_14[10], out_14[8]);  // And
  and and_12 (and_12_out, out_14[12], ~out_14[11], out_14[9], ~out_14[8]);  // And
  and and_13 (and_13_out, out_14[12], out_14[10], ~out_14[9]);  // And
  and and_14 (and_14_out, ~out_14[12], ~out_14[10], ~out_14[9], out_14[8]);  // And
  and and_15 (and_15_out, ~out_14[12], ~out_14[10], ~out_14[8], out_14[9]);  // And
  and and_16 (and_16_out, out_14[10], out_14[9], out_14[8]);
  and and_17 (and_17_out, out_14[12], ~out_14[11], ~out_14[10], ~out_14[9], ~out_14[8]);  // And
  and and_18 (and_18_out, out_14[12], out_14[11], out_14[10], out_14[9]);
  and and_19 (and_19_out, ~out_14[12], out_14[11], ~out_14[10], ~out_14[9]);  // And
  and and_20 (and_20_out, ~out_14[12], ~out_14[9], out_14[8]);  // And
  and and_21 (and_21_out, ~out_14[12], ~out_14[8], out_14[9]);  // And
  and and_22 (and_22_out, out_14[12], ~out_14[11], out_14[10], out_14[9], out_14[8]);  // And
  and and_23 (and_23_out, out_14[11], out_14[10], out_14[9], ~out_14[8]);  // And
  and and_24 (and_24_out, ~out_14[12], ~out_14[11], ~out_14[10], ~out_14[9]);  // And
  and and_25 (and_25_out, out_14[9], ~out_14[8]);  // And
  and and_26 (and_26_out, out_14[10], ~out_14[8]);  // And
  and and_27 (and_27_out, out_14[11], ~out_14[8]);  // And
  and and_28 (and_28_out, out_14[12], ~out_14[10]);  // And
  and and_29 (and_29_out, out_14[12], ~out_14[11], ~out_14[9]);  // And
  not not_6 (not_6_out, reset);
  not not_7 (not_7_out, r_cnt_eq_16);
  or or_10 (Q_a_plus__op, and_2_out, and_3_out, and_4_out, out_14[12]);
  or or_11 (Q_d_plus__op, and_20_out, and_21_out, and_22_out, and_23_out, and_24_out);
  or or_12 (Q_e_plus__op, and_25_out, and_26_out, and_27_out, and_28_out, and_29_out);
  Multiplexer #(.Selector_Bits(5)) multiplexer_19 (
    .sel({Q_a, Q_b, Q_c, Q_d, Q_e}), .in_0(start_t), .in_1(1'b0), .in_2(1'b0), .in_3(1'b1), .in_4(not_7_out),
    .in_5(Q_c_plus__op), .in_6(1'b0), .in_7(1'b0), .in_8(1'b0), .in_9(1'b0), .in_10(1'b0), .in_11(1'b0),
    .in_12(1'b0), .in_13(1'b0), .in_14(1'b0), .in_15(1'b0), .in_16(1'b0), .in_17(1'b0), .in_18(1'b0),
    .in_19(1'b0), .in_20(1'b0), .in_21(1'b0), .in_22(1'b0), .in_23(1'b0), .in_24(1'b0), .in_25(1'b0),
    .in_26(1'b1), .in_27(1'b1), .in_28(not_6_out), .in_29(1'b0), .in_30(1'b0), .in_31(1'b0),
    .out(multiplexer_19_out));
  or or_13 (Q_c_plus__op, and_14_out, and_15_out, and_16_out, and_17_out, and_18_out, and_19_out);
  or or_14 (Q_b_plus__op, and_5_out, and_6_out, and_7_out, and_8_out, and_9_out, and_10_out, and_11_out, and_12_out, and_13_out);
  D_FF d_ff_9 (.D(multiplexer_19_out), .C(clk), .Q(Q_c));  // open: nQ
  Multiplexer #(.Selector_Bits(5)) multiplexer_20 (
    .sel({Q_a, Q_b, Q_c, Q_d, Q_e}), .in_0(reset), .in_1(reset), .in_2(1'b1), .in_3(1'b0), .in_4(1'b0),
    .in_5(Q_d_plus__op), .in_6(1'b1), .in_7(1'b1), .in_8(1'b1), .in_9(1'b1), .in_10(1'b1), .in_11(1'b1),
    .in_12(1'b1), .in_13(1'b1), .in_14(1'b1), .in_15(1'b1), .in_16(1'b1), .in_17(1'b1), .in_18(1'b1),
    .in_19(1'b1), .in_20(1'b1), .in_21(1'b1), .in_22(1'b1), .in_23(1'b1), .in_24(1'b1), .in_25(1'b1),
    .in_26(1'b0), .in_27(1'b0), .in_28(reset), .in_29(1'b0), .in_30(1'b0), .in_31(1'b0),
    .out(multiplexer_20_out));
  D_FF d_ff_10 (.D(multiplexer_20_out), .C(clk), .Q(Q_d));  // open: nQ
  or or_15 (or_15_out, start_t, progLoad);
  or or_16 (or_16_out, eq_t, gr);
  Multiplexer #(.Selector_Bits(5)) multiplexer_21 (
    .sel({Q_a, Q_b, Q_c, Q_d, Q_e}), .in_0(or_15_out), .in_1(progLoad), .in_2(r_cnt_eq_cnt), .in_3(1'b0),
    .in_4(1'b0), .in_5(Q_e_plus__op), .in_6(1'b0), .in_7(1'b0), .in_8(1'b0), .in_9(1'b0), .in_10(1'b0),
    .in_11(1'b0), .in_12(1'b0), .in_13(1'b0), .in_14(1'b0), .in_15(1'b0), .in_16(1'b0), .in_17(1'b1),
    .in_18(eq_t), .in_19(gr), .in_20(le), .in_21(or_16_out), .in_22(1'b0), .in_23(1'b0), .in_24(1'b0),
    .in_25(1'b0), .in_26(1'b1), .in_27(1'b1), .in_28(1'b0), .in_29(1'b0), .in_30(1'b0), .in_31(1'b0),
    .out(multiplexer_21_out));
  D_FF d_ff_11 (.D(multiplexer_21_out), .C(clk), .Q(Q_e));  // open: nQ
  Decoder #(.Selector_Bits(5)) decoder_2 (
    .sel({Q_a, Q_b, Q_c, Q_d, Q_e}), .out_0(_00000), .out_1(_00001), .out_2(_00010), .out_3(_00011),
    .out_4(_00100), .out_5(_00101), .out_6(_00110), .out_7(_00111), .out_8(_01000), .out_9(_01001),
    .out_10(_01010), .out_11(_01011), .out_12(_01100), .out_13(_01101), .out_14(_01110), .out_15(_01111),
    .out_16(_10000), .out_17(_10001), .out_18(_10010), .out_19(_10011), .out_20(_10100), .out_21(_10101),
    .out_22(_10110), .out_23(_10111), .out_24(_11000), .out_25(_11001), .out_26(_11010), .out_27(_11011),
    .out_28(_11100), .out_29(_11101), .out_30(_11110), .out_31(_11111));
  Decoder #(.Selector_Bits(5)) decoder_3 (
    .sel(out_14[12:8]), .out_0(_00000op), .out_1(_00001op), .out_2(_00010op), .out_3(_00011op),
    .out_4(_00100op), .out_5(_00101op), .out_6(_00110op), .out_7(_00111op), .out_8(_01000op),
    .out_9(_01001op), .out_10(_01010op), .out_11(_01011op), .out_12(_01100op), .out_13(_01101op),
    .out_14(_01110op), .out_15(_01111op), .out_16(_10000op), .out_17(_10001op), .out_18(_10010op),
    .out_19(_10011op), .out_20(_10100op), .out_21(_10101op), .out_22(_10110op), .out_23(_10111op),
    .out_24(_11000op), .out_25(_11001op), .out_26(_11010op), .out_27(_11011op), .out_28(_11100op),
    .out_29(_11101op), .out_30(_11110op), .out_31(_11111op));

  // Other names for the same wires on the sheet: accA[7:0] = out_15; accB[7:0] = out_16; ALU_result[7:0] = out_18;
  //   operand[7:0] = out_14[7:0]; opcode[4:0] = out_14[12:8]; regC[7:0] = out_17
endmodule

/* Test case 01_P01T01:
M N progIN reset progLoad start result clk valid done output
0 0 0 0 0 0 0 0 0 0 0
0 0 0 0 0 0 0 1 0 0 0
0 0 0 1 0 0 0 0 0 0 0
0 0 0 1 0 0 0 1 0 0 0
0 0 0 0 0 0 0 0 0 0 0
0 0 0 0 0 0 0 1 0 0 0
0 0 0 0 0 0 0 0 0 0 0
0 0 0 0 0 0 0 1 0 0 0
0 0 0 0 0 0 0 0 0 0 0
0 0 0 0 0 0 0 1 0 0 0
0 0 0 0 0 0 0 0 0 0 0
0 0 0 0 0 0 0 1 0 0 0
0 0 0 0 0 0 0 0 0 0 0
0 0 0 0 0 0 0 1 0 0 0
0 0 0 0 0 0 0 0 0 0 0
0 0 0 0 0 0 0 1 0 0 0
0 0 0 0 0 0 0 0 0 0 0
0 0 0 0 0 0 0 1 0 0 0
0 0 0 0 0 0 0 0 0 0 0
0 0 0 0 0 0 0 1 0 0 0
0 0 0 0 0 0 0 0 0 0 0
0 0 0 0 0 0 0 1 0 0 0
0 0 0 0 0 0 0 0 0 0 0
0 0 0 0 0 0 0 1 0 0 0
0 0 0 0 0 0 0 0 0 0 0
0 0 0 0 0 0 0 1 0 0 0
0 0 0 0 0 0 0 0 0 0 0
0 0 0 0 0 0 0 1 0 0 0
0 0 0 0 0 0 0 0 0 0 0
0 0 0 0 0 0 0 1 0 0 0
0 0 0 0 0 0 0 0 0 0 0
0 0 0 0 0 0 0 1 0 0 0
0 0 0 0 0 0 0 0 0 0 0
0 0 0 0 0 0 0 1 0 0 0
0 0 0 0 0 0 0 0 0 0 0
0 0 0 0 0 0 0 1 0 0 0
0 0 0 0 0 0 0 0 0 0 0
0 0 0 0 0 0 0 1 0 0 0
0 0 0 0 0 0 0 0 0 0 0
0 0 0 0 0 0 0 1 0 0 0
0 0 0 0 0 0 0 0 0 0 0
0 0 0 0 0 0 0 1 0 0 0
0 0 271 0 1 0 0 0 0 0 0
0 0 0 0 1 0 0 1 0 0 0
0 0 565 0 1 0 0 0 0 0 0
0 0 0 0 1 0 0 1 0 0 0
0 0 4352 0 1 0 0 0 0 0 0
0 0 0 0 1 0 0 1 0 0 0
0 0 2819 0 1 0 0 0 0 0 0
0 0 0 0 1 0 0 1 0 0 0
0 0 7936 0 1 0 0 0 0 0 0
0 0 0 0 1 0 0 1 0 0 0
0 0 0 0 0 1 0 0 0 0 0
0 0 0 0 0 1 0 1 0 0 0
0 0 0 0 0 0 0 0 x 0 0
0 0 0 0 0 0 0 1 x 0 0
0 0 0 0 0 0 0 0 x 0 0
0 0 0 0 0 0 0 1 x 0 0
0 0 0 0 0 0 0 0 x 0 0
0 0 0 0 0 0 0 1 x 0 0
0 0 0 0 0 0 0 0 x 0 0
0 0 0 0 0 0 0 1 x 0 0
0 0 0 0 0 0 0 0 x 0 0
0 0 0 0 0 0 0 1 x 0 0
0 0 0 0 0 0 0 0 x 0 0
0 0 0 0 0 0 0 1 x 0 0
0 0 0 0 0 0 0 0 x 0 0
0 0 0 0 0 0 0 1 x 0 0
0 0 0 0 0 0 0 0 x 0 0
0 0 0 0 0 0 0 1 x 0 0
0 0 0 0 0 0 0 0 x 0 0
0 0 0 0 0 0 0 1 x 0 0
0 0 0 0 0 0 0 0 x 0 0
0 0 0 0 0 0 0 1 x 0 0
0 0 0 0 0 0 0 0 x 0 0
0 0 0 0 0 0 0 1 x 0 0
0 0 0 0 0 0 0 0 x 0 0
0 0 0 0 0 0 0 1 x 0 0
0 0 0 0 0 0 0 0 x 0 0
0 0 0 0 0 0 0 1 x 0 0
0 0 0 0 0 0 0 0 x 0 0
0 0 0 0 0 0 0 1 x 0 0
0 0 0 0 0 0 0 0 x 0 0
0 0 0 0 0 0 0 1 x 0 0
0 0 0 0 0 0 0 0 x 0 0
0 0 0 0 0 0 0 1 x 0 0
0 0 0 0 0 0 0 0 x 0 0
0 0 0 0 0 0 0 1 x 0 0
0 0 0 0 0 0 0 0 x 0 0
0 0 0 0 0 0 0 1 x 0 0
0 0 0 0 0 0 0 0 x 0 0
0 0 0 0 0 0 0 1 x 0 0
0 0 0 0 0 0 0 0 x 0 0
0 0 0 0 0 0 0 1 x 0 0
0 0 0 0 0 0 0 0 x 0 0
0 0 0 0 0 0 0 1 x 0 0
0 0 0 0 0 0 0 0 x 0 0
0 0 0 0 0 0 0 1 x 0 0
0 0 0 0 0 0 0 0 x 0 0
0 0 0 0 0 0 0 1 x 0 0
0 0 0 0 0 0 0 0 x 0 0
0 0 0 0 0 0 0 1 x 0 0
0 0 0 0 0 0 0 0 x 0 0
0 0 0 0 0 0 0 1 x 0 0
0 0 0 0 0 0 0 0 x 0 0
0 0 0 0 0 0 0 1 1 0 0
0 0 0 0 0 0 1 0 1 0 0
0 0 0 0 0 0 1 1 1 0 0
0 0 0 0 0 0 0 0 1 0 0
0 0 0 0 0 0 0 1 1 0 0
0 0 0 0 0 0 0 0 1 0 0
0 0 0 0 0 0 0 1 1 0 0
0 0 0 0 0 0 0 0 1 0 0
0 0 0 0 0 0 0 1 1 0 68
0 0 0 0 0 0 0 0 1 0 68
0 0 0 0 0 0 0 1 1 0 0
0 0 0 0 0 0 0 0 1 0 0
0 0 0 0 0 0 0 1 1 0 0
0 0 0 0 0 0 0 0 1 0 0
0 0 0 0 0 0 0 1 1 0 0
0 0 0 0 0 0 0 0 1 0 0
0 0 0 0 0 0 0 1 1 0 0
0 0 0 0 0 0 0 0 1 0 0
0 0 0 0 0 0 0 1 1 0 0
0 0 0 0 0 0 0 0 1 0 0
0 0 0 0 0 0 0 1 1 0 0
0 0 0 0 0 0 0 0 1 0 0
0 0 0 0 0 0 0 1 1 0 0
0 0 0 0 0 0 0 0 1 0 0
0 0 0 0 0 0 0 1 1 0 0
0 0 0 0 0 0 0 0 1 0 0
0 0 0 0 0 0 0 1 1 0 0
0 0 0 0 0 0 0 0 1 0 0
0 0 0 0 0 0 0 1 1 0 0
0 0 0 0 0 0 0 0 1 0 0
0 0 0 0 0 0 0 1 1 0 0
0 0 0 0 0 0 0 0 1 0 0
0 0 0 0 0 0 0 1 1 0 0
0 0 0 0 0 0 0 0 1 0 0
0 0 0 0 0 0 0 1 1 1 0
0 0 0 0 0 0 0 0 1 1 0
0 0 0 0 0 0 0 1 1 1 0
0 0 0 0 0 0 0 0 1 1 0
*/

/* Test case 01_P01T2:
M N progIN reset progLoad start result clk valid done output
0 0 0 0 0 0 0 0 0 0 0
0 0 0 0 0 0 0 1 0 0 0
0 0 0 1 0 0 0 0 0 0 0
0 0 0 1 0 0 0 1 0 0 0
0 0 0 0 0 0 0 0 0 0 0
0 0 0 0 0 0 0 1 0 0 0
0 0 0 0 0 0 0 0 0 0 0
0 0 0 0 0 0 0 1 0 0 0
0 0 0 0 0 0 0 0 0 0 0
0 0 0 0 0 0 0 1 0 0 0
0 0 0 0 0 0 0 0 0 0 0
0 0 0 0 0 0 0 1 0 0 0
0 0 0 0 0 0 0 0 0 0 0
0 0 0 0 0 0 0 1 0 0 0
0 0 0 0 0 0 0 0 0 0 0
0 0 0 0 0 0 0 1 0 0 0
0 0 0 0 0 0 0 0 0 0 0
0 0 0 0 0 0 0 1 0 0 0
0 0 0 0 0 0 0 0 0 0 0
0 0 0 0 0 0 0 1 0 0 0
0 0 0 0 0 0 0 0 0 0 0
0 0 0 0 0 0 0 1 0 0 0
0 0 0 0 0 0 0 0 0 0 0
0 0 0 0 0 0 0 1 0 0 0
0 0 0 0 0 0 0 0 0 0 0
0 0 0 0 0 0 0 1 0 0 0
0 0 0 0 0 0 0 0 0 0 0
0 0 0 0 0 0 0 1 0 0 0
0 0 0 0 0 0 0 0 0 0 0
0 0 0 0 0 0 0 1 0 0 0
0 0 0 0 0 0 0 0 0 0 0
0 0 0 0 0 0 0 1 0 0 0
0 0 0 0 0 0 0 0 0 0 0
0 0 0 0 0 0 0 1 0 0 0
0 0 0 0 0 0 0 0 0 0 0
0 0 0 0 0 0 0 1 0 0 0
0 0 0 0 0 0 0 0 0 0 0
0 0 0 0 0 0 0 1 0 0 0
0 0 0 0 0 0 0 0 0 0 0
0 0 0 0 0 0 0 1 0 0 0
0 0 0 0 0 0 0 0 0 0 0
0 0 0 0 0 0 0 1 0 0 0
0 0 271 0 1 0 0 0 0 0 0
0 0 0 0 1 0 0 1 0 0 0
0 0 565 0 1 0 0 0 0 0 0
0 0 0 0 1 0 0 1 0 0 0
0 0 4352 0 1 0 0 0 0 0 0
0 0 0 0 1 0 0 1 0 0 0
0 0 2819 0 1 0 0 0 0 0 0
0 0 0 0 1 0 0 1 0 0 0
0 0 7936 0 1 0 0 0 0 0 0
0 0 0 0 1 0 0 1 0 0 0
0 0 0 1 0 0 0 0 0 0 0
0 0 0 1 0 0 0 1 0 0 0
0 0 0 0 0 0 0 0 0 0 0
0 0 0 0 0 0 0 1 0 0 0
0 0 0 0 0 0 0 0 0 0 0
0 0 0 0 0 0 0 1 0 0 0
0 0 0 0 0 0 0 0 0 0 0
0 0 0 0 0 0 0 1 0 0 0
0 0 0 0 0 0 0 0 0 0 0
0 0 0 0 0 0 0 1 0 0 0
0 0 0 0 0 0 0 0 0 0 0
0 0 0 0 0 0 0 1 0 0 0
0 0 0 0 0 0 0 0 0 0 0
0 0 0 0 0 0 0 1 0 0 0
0 0 0 0 0 0 0 0 0 0 0
0 0 0 0 0 0 0 1 0 0 0
0 0 0 0 0 0 0 0 0 0 0
0 0 0 0 0 0 0 1 0 0 0
0 0 0 0 0 0 0 0 0 0 0
0 0 0 0 0 0 0 1 0 0 0
0 0 0 0 0 0 0 0 0 0 0
0 0 0 0 0 0 0 1 0 0 0
0 0 271 0 1 0 0 0 0 0 0
0 0 0 0 1 0 0 1 0 0 0
0 0 565 0 1 0 0 0 0 0 0
0 0 0 0 1 0 0 1 0 0 0
0 0 4352 0 1 0 0 0 0 0 0
0 0 0 0 1 0 0 1 0 0 0
0 0 2819 0 1 0 0 0 0 0 0
0 0 0 0 1 0 0 1 0 0 0
0 0 7936 0 1 0 0 0 0 0 0
0 0 0 0 1 0 0 1 0 0 0
0 0 0 1 0 0 0 0 0 0 0
0 0 0 1 0 0 0 1 0 0 0
0 0 0 0 0 0 0 0 0 0 0
0 0 0 0 0 0 0 1 0 0 0
0 0 0 0 0 0 0 0 0 0 0
0 0 0 0 0 0 0 1 0 0 0
0 0 0 0 0 0 0 0 0 0 0
0 0 0 0 0 0 0 1 0 0 0
0 0 0 0 0 0 0 0 0 0 0
0 0 0 0 0 0 0 1 0 0 0
0 0 0 0 0 0 0 0 0 0 0
0 0 0 0 0 0 0 1 0 0 0
0 0 0 0 0 0 0 0 0 0 0
0 0 0 0 0 0 0 1 0 0 0
0 0 0 0 0 0 0 0 0 0 0
0 0 0 0 0 0 0 1 0 0 0
0 0 0 0 0 0 0 0 0 0 0
0 0 0 0 0 0 0 1 0 0 0
0 0 0 0 0 0 0 0 0 0 0
0 0 0 0 0 0 0 1 0 0 0
0 0 0 0 0 0 0 0 0 0 0
0 0 0 0 0 0 0 1 0 0 0
0 0 271 0 1 0 0 0 0 0 0
0 0 0 0 1 0 0 1 0 0 0
0 0 565 0 1 0 0 0 0 0 0
0 0 0 0 1 0 0 1 0 0 0
0 0 4352 0 1 0 0 0 0 0 0
0 0 0 0 1 0 0 1 0 0 0
0 0 2819 0 1 0 0 0 0 0 0
0 0 0 0 1 0 0 1 0 0 0
0 0 7936 0 1 0 0 0 0 0 0
0 0 0 0 1 0 0 1 0 0 0
0 0 0 1 0 0 0 0 0 0 0
0 0 0 1 0 0 0 1 0 0 0
0 0 0 0 0 0 0 0 0 0 0
0 0 0 0 0 0 0 1 0 0 0
0 0 0 0 0 0 0 0 0 0 0
0 0 0 0 0 0 0 1 0 0 0
0 0 0 0 0 0 0 0 0 0 0
0 0 0 0 0 0 0 1 0 0 0
0 0 0 0 0 0 0 0 0 0 0
0 0 0 0 0 0 0 1 0 0 0
0 0 0 0 0 0 0 0 0 0 0
0 0 0 0 0 0 0 1 0 0 0
0 0 0 0 0 0 0 0 0 0 0
0 0 0 0 0 0 0 1 0 0 0
0 0 0 0 0 0 0 0 0 0 0
0 0 0 0 0 0 0 1 0 0 0
0 0 0 0 0 0 0 0 0 0 0
0 0 0 0 0 0 0 1 0 0 0
0 0 0 0 0 0 0 0 0 0 0
0 0 0 0 0 0 0 1 0 0 0
0 0 0 0 0 0 0 0 0 0 0
0 0 0 0 0 0 0 1 0 0 0
*/
