// Digital circuit TEMPLATE ver.Multi-Cycle.dig as structural Verilog
module TEMPLATE_ver_Multi_Cycle (
  input  [7:0] M,
  input  [7:0] N,
  input  [12:0] progIN,
  input  reset,
  input  progLoad,
  input  start,
  input  result,
  input  clk,
  output valid,
  output done,
  output [7:0] \output ,
  output [7:0] out_12
);

  wire _00, _0000, _00000, _00001, _0001, _01, _00010, _0010, _10, _00011, _0011, _11, _00100, _0100, _00101,
       _0101, _00110, _0110, _00111, _0111, _01000, _1000, _01001, _1001, _01010, _1010, _01011, _1011,
       _01100, _1100, _01101, _1101, _01110, _1110, _01111, _1111, _10000, _10001, _10010, _10011, _10100,
       _10101, _10110, _10111, _11000, _11001, _11010, _11011, _11100, _11101, _11110, _11111, ALU,
       and_1_out, and_2_out, and_3_out, and_6_out, and_7_out, and_8_out, and_9_out, and_10_out, and_11_out,
       and_12_out, and_13_out, and_14_out, and_15_out, and_16_out, and_17_out, and_18_out, and_19_out,
       and_20_out, and_22_out, en_rRAM, enA, enB, enC, eq, eq_t, gr, gt, isPrime_d, jump, jumpOp, le, lt,
       move, multiplexer_8_out, multiplexer_9_out, multiplexer_10_out, multiplexer_11_out,
       multiplexer_12_out, multiplexer_13_out, multiplexer_14_out, multiplexer_15_out, multiplexer_16_out,
       not_2_out, not_3_out, not_4_out, or_1_out, or_2_out, or_3_out, or_4_out, or_5_out, or_6_out, or_7_out,
       or_8_out, or_9_out, or_13_out, or_15_out, or_16_out, or_17_out, or_18_out, or_19_out, or_20_out,
       or_21_out, or_22_out, or_23_out, or_24_out, or_25_out, or_26_out, or_27_out, or_28_out, P_a, P_b, Q_a,
       Q_b, Q_c, Q_d, r_cnt_eq_16, r_cnt_gt_16, r_cnt_lt_16, result_cnt_eq_16, result_cnt_gt_16,
       result_cnt_lt_16;
  wire [2:1] bitcount_4_out;
  wire [3:1] bitcount_2_out, bitcount_3_out;
  wire [4:0] bitcount_1_out, opcode;
  wire [7:0] A, A_B, A_lt__lt_B, accA, accB, AND, cnt, DIFF, DIV, MOD, MUL, multiplexer_1_out,
       multiplexer_2_out, multiplexer_3_out, multiplexer_5_out, multiplexer_6_out, multiplexer_7_out,
       operand, OR, pRAM_operand, r_cnt, regC, result_cnt, rRAM_operand, SUM, val, XOR;
  wire [12:8] pRAM_d1;

  or or_1 (or_1_out, reset, ~progLoad);  // Or
  CounterPreset #(.maxValue(256), .Bits(8)) u_cnt (
    .en(progLoad), .C(clk), .dir(1'b0), .in({8{1'b0}}), .ld(1'b0), .clr(or_1_out), .out(cnt));  // open: ovf
  or or_2 (or_2_out, _00, result);
  Multiplexer #(.Selector_Bits(2), .Bits(8)) multiplexer_1 (
    .sel({en_rRAM, _01010}), .in_0(r_cnt), .in_1(operand), .in_2(operand), .in_3({8{1'b0}}),
    .out(multiplexer_1_out));
  Multiplexer #(.Bits(8)) multiplexer_2 (.sel(_01001), .in_0(cnt), .in_1(operand), .out(multiplexer_2_out));
  or or_3 (or_3_out, en_rRAM, _0011);
  Multiplexer #(.Bits(8)) multiplexer_3 (.sel(en_rRAM), .in_0({8{1'b0}}), .in_1(val), .out(multiplexer_3_out));
  CounterPreset #(.maxValue(256), .Bits(8)) u_r_cnt (
    .en(_0011), .C(clk), .dir(1'b0), .in({8{1'b0}}), .ld(1'b0), .clr(r_cnt_eq_16), .out(r_cnt));  // open: ovf
  Comparator #(.Bits(8)) u_r_cnt_eq_16 (.a(r_cnt), .b(8'h10), .gt(r_cnt_gt_16), .eq(r_cnt_eq_16), .lt(r_cnt_lt_16));
  Counter #(.Bits(8)) u_result_cnt (.en(_01), .C(clk), .clr(or_2_out), .out(result_cnt));  // open: ovf
  RAMDualAccess #(.AddrBits(8), .Bits(13)) pRAM (
    .str(progLoad), .C(clk), .ld(_01001), .A1(multiplexer_2_out), .Din1(progIN), .A2(out_12),
    .D1({pRAM_d1, pRAM_operand}), .D2({opcode, operand}));
  RAMDualAccess #(.AddrBits(8), .Bits(8)) rRAM (
    .str(or_3_out), .C(clk), .ld(_01010), .A1(multiplexer_1_out), .Din1(multiplexer_3_out), .A2(result_cnt),
    .D1(rRAM_operand), .D2(\output ));
  or or_4 (or_4_out, reset, _11111);
  or or_5 (or_5_out, _0101, _0111, _1000, _0110);
  CounterPreset #(.maxValue(256), .Bits(8)) pc (
    .en(or_5_out), .C(clk), .dir(1'b0), .in(operand), .ld(jump), .clr(or_4_out), .out(out_12));  // open: ovf
  Comparator #(.Bits(8)) comparator_1 (
    .a(result_cnt), .b(8'h10), .gt(result_cnt_gt_16), .eq(result_cnt_eq_16), .lt(result_cnt_lt_16));
  Multiplexer #(.Selector_Bits(5), .Bits(8)) multiplexer_4 (
    .sel(opcode), .in_0({8{1'b0}}), .in_1(operand), .in_2(operand), .in_3(accB), .in_4(accA), .in_5(accA),
    .in_6(regC), .in_7(M), .in_8(N), .in_9(pRAM_operand), .in_10(rRAM_operand), .in_11(accA),
    .in_12({8{1'b0}}), .in_13({8{1'b0}}), .in_14({8{1'b0}}), .in_15({8{1'b0}}), .in_16({8{1'b0}}),
    .in_17(SUM), .in_18(DIFF), .in_19(MUL), .in_20(DIV), .in_21(MOD), .in_22(A_B), .in_23({8{1'b0}}),
    .in_24(A), .in_25(AND), .in_26(OR), .in_27(XOR), .in_28(A_lt__lt_B), .in_29({8{1'b0}}),
    .in_30({8{1'b0}}), .in_31({8{1'b0}}), .out(val));
  Multiplexer #(.Bits(8)) multiplexer_5 (.sel(reset), .in_0(val), .in_1({8{1'b0}}), .out(multiplexer_5_out));
  Register #(.Bits(8)) u_regC (.D(multiplexer_5_out), .C(clk), .en(enC), .Q(regC));
  BitCount #(.Bits(16)) bitcount_1 (
    .in({_11100, _11011, _11010, _11001, _11000, _10110, _10101, _10100, _10011, _10010, _10001, _01010, _01001, _00110, _00011, _00001}),
    .out(bitcount_1_out));
  or or_6 (or_6_out, reset, start, progLoad);
  or or_7 (or_7_out, _0101, _0111);
  or or_8 (or_8_out, _00010, _00100);
  or or_9 (or_9_out, _00101, _00111, _01000);
  Multiplexer #(.Bits(8)) multiplexer_6 (.sel(reset), .in_0(val), .in_1({8{1'b0}}), .out(multiplexer_6_out));
  Register #(.Bits(8)) u_accB (.D(multiplexer_6_out), .C(clk), .en(enB), .Q(accB));
  RS_FF_AS rs_ff_as_1 (.S(_11111), .R(or_6_out), .Q(valid));  // open: nQ
  and and_1 (and_1_out, bitcount_1_out[0], or_7_out);
  and and_2 (and_2_out, or_8_out, _0101);
  and and_3 (and_3_out, or_9_out, _0101);
  or or_10 (enA, and_1_out, reset);
  or or_11 (enB, reset, and_2_out);
  or or_12 (enC, reset, and_3_out);
  and and_4 (en_rRAM, _01011, _0101);
  Multiplexer #(.Bits(8)) multiplexer_7 (.sel(reset), .in_0(val), .in_1({8{1'b0}}), .out(multiplexer_7_out));
  Register #(.Bits(8)) u_accA (.D(multiplexer_7_out), .C(clk), .en(enA), .Q(accA));
  or or_13 (or_13_out, reset, start, progLoad, result);
  Seven_Seg_Hex seven_seg_hex_1 (.d(\output [7:4]), .dp(1'b0));
  RS_FF_AS rs_ff_as_2 (.S(result_cnt_eq_16), .R(or_13_out), .Q(done));  // open: nQ
  assign AND = accA & accB;  // And and_5, 8 bits wide
  assign OR = accA | accB;  // Or or_14, 8 bits wide
  assign XOR = accA ^ accB;  // XOr xor_1, 8 bits wide
  Add #(.Bits(8)) add_1 (.a(accA), .b(accB), .c_i(1'b0), .s(SUM));  // open: c_o
  Sub #(.Bits(8)) sub_1 (.a(accA), .b(accB), .c_i(1'b0), .s(DIFF));  // open: c_o
  Mul #(.Bits(4)) mul_1 (.a(accA[3:0]), .b(accB[3:0]), .mul(MUL));
  Div #(.Bits(8)) divide (.a(accA), .b(accB), .q(DIV), .r(MOD));
  assign A = ~accA;  // Not not_1, 8 bits wide
  BarrelShifter #(.Bits(8), .barrelShifterMode("arithmetic")) barrelshifter_1 (
    .in(accA), .shift({1'b0, accB[2:0]}), .out(A_lt__lt_B));
  LookUpTable #(.Bits(8)) exponent (
    .in0(accB[0]), .in1(accB[1]), .in2(accB[2]), .in3(accA[0]), .in4(accA[1]), .in5(accA[2]), .out(A_B));
  Seven_Seg_Hex seven_seg_hex_2 (.d(\output [3:0]), .dp(1'b0));
  or or_15 (or_15_out, _11110, _11111);
  and and_6 (and_6_out, ~start, ~reset);  // And
  and and_7 (and_7_out, lt, _10111);
  or or_16 (or_16_out, start, progLoad, reset);
  and and_8 (and_8_out, ~reset, ~result);  // And
  or or_17 (or_17_out, start, progLoad, reset);
  Multiplexer #(.Selector_Bits(4)) multiplexer_8 (
    .sel({Q_a, Q_b, Q_c, Q_d}), .in_0(1'b0), .in_1(1'b0), .in_2(1'b0), .in_3(1'b0), .in_4(or_15_out),
    .in_5(1'b0), .in_6(1'b0), .in_7(1'b0), .in_8(1'b0), .in_9(and_6_out), .in_10(1'b0), .in_11(1'b0),
    .in_12(1'b0), .in_13(1'b0), .in_14(1'b0), .in_15(1'b0), .out(multiplexer_8_out));
  not not_2 (not_2_out, result_cnt_eq_16);
  Multiplexer multiplexer_9 (.sel(_0111), .in_0(1'b0), .in_1(and_7_out), .out(multiplexer_9_out));
  or or_18 (or_18_out, start, and_11_out);
  D_FF d_ff_1 (.D(multiplexer_8_out), .C(clk), .Q(Q_a));  // open: nQ
  Multiplexer #(.Selector_Bits(2)) multiplexer_10 (
    .sel({P_a, P_b}), .in_0(1'b0), .in_1(result_cnt_eq_16), .in_2(and_8_out), .in_3(1'b0),
    .out(multiplexer_10_out));
  Multiplexer #(.Selector_Bits(2)) multiplexer_11 (
    .sel({P_a, P_b}), .in_0(result), .in_1(not_2_out), .in_2(result), .in_3(1'b0), .out(multiplexer_11_out));
  Register register_1 (.D(multiplexer_9_out), .C(clk), .en(or_18_out), .Q(le));
  Multiplexer multiplexer_12 (.sel(_0111), .in_0(1'b0), .in_1(or_20_out), .out(multiplexer_12_out));
  Register register_2 (.D(multiplexer_12_out), .C(clk), .en(or_19_out), .Q(eq_t));
  or or_19 (or_19_out, start, and_12_out);
  and and_9 (and_9_out, ~or_16_out, multiplexer_10_out);  // And
  and and_10 (and_10_out, ~or_17_out, multiplexer_11_out);  // And
  and and_11 (and_11_out, _0111, _10111);
  and and_12 (and_12_out, _0111, or_21_out);
  or or_20 (or_20_out, and_15_out, and_14_out);
  D_FF d_ff_2 (.D(and_9_out), .C(clk), .Q(P_a));  // open: nQ
  D_FF d_ff_3 (.D(and_10_out), .C(clk), .Q(P_b));  // open: nQ
  and and_13 (and_13_out, gt, _10111);
  and and_14 (and_14_out, _11101, isPrime_d);
  and and_15 (and_15_out, eq, _10111);
  or or_21 (or_21_out, _11101, _10111);
  or or_22 (or_22_out, ALU, jumpOp, move);
  Multiplexer multiplexer_13 (.sel(_0111), .in_0(1'b0), .in_1(and_13_out), .out(multiplexer_13_out));
  or or_23 (or_23_out, start, and_16_out);
  ROM #(.AddrBits(8)) isPrime (.A(accA), .sel(1'b1), .D(isPrime_d));
  Multiplexer #(.Selector_Bits(4)) multiplexer_14 (
    .sel({Q_a, Q_b, Q_c, Q_d}), .in_0(start), .in_1(start), .in_2(1'b0), .in_3(1'b0), .in_4(or_22_out),
    .in_5(1'b1), .in_6(1'b1), .in_7(1'b1), .in_8(1'b1), .in_9(start), .in_10(1'b0), .in_11(1'b0),
    .in_12(1'b0), .in_13(1'b0), .in_14(1'b0), .in_15(1'b0), .out(multiplexer_14_out));
  Decoder #(.Selector_Bits(2)) decoder_1 (.sel({P_a, P_b}), .out_0(_00), .out_1(_01), .out_2(_10), .out_3(_11));
  Register register_3 (.D(multiplexer_13_out), .C(clk), .en(or_23_out), .Q(gr));
  or or_24 (or_24_out, eq_t, gr);
  and and_16 (and_16_out, _0111, _10111);
  D_FF d_ff_4 (.D(multiplexer_14_out), .C(clk), .Q(Q_b));  // open: nQ
  and and_17 (and_17_out, _01101, eq_t);
  and and_18 (and_18_out, _01110, gr);
  and and_19 (and_19_out, _01111, le);
  and and_20 (and_20_out, _10000, or_24_out);
  or or_25 (or_25_out, ALU, jumpOp);
  Comparator #(.Signed("true"), .Bits(8)) comparator_2 (.a(accA), .b(accB), .gt(gt), .eq(eq), .lt(lt));
  or or_26 (or_26_out, _01100, and_17_out, and_18_out, and_19_out, and_20_out);
  Multiplexer #(.Selector_Bits(4)) multiplexer_15 (
    .sel({Q_a, Q_b, Q_c, Q_d}), .in_0(reset), .in_1(reset), .in_2(1'b1), .in_3(not_3_out), .in_4(or_25_out),
    .in_5(1'b0), .in_6(1'b0), .in_7(1'b0), .in_8(1'b0), .in_9(reset), .in_10(1'b0), .in_11(1'b0),
    .in_12(1'b0), .in_13(1'b0), .in_14(1'b0), .in_15(1'b0), .out(multiplexer_15_out));
  not not_3 (not_3_out, r_cnt_eq_16);
  and and_21 (jump, or_26_out, _0110);
  D_FF d_ff_5 (.D(multiplexer_15_out), .C(clk), .Q(Q_c));  // open: nQ
  Comparator #(.Signed("true"), .Bits(8)) comparator_3 (.a(accA), .b(accB), .gt(gt), .eq(eq), .lt(lt));
  or or_27 (or_27_out, ALU, _11111, move);
  and and_22 (and_22_out, ~start, ~reset);  // And
  not not_4 (not_4_out, r_cnt_eq_16);
  Multiplexer #(.Selector_Bits(4)) multiplexer_16 (
    .sel({Q_a, Q_b, Q_c, Q_d}), .in_0(progLoad), .in_1(progLoad), .in_2(1'b1), .in_3(not_4_out),
    .in_4(or_27_out), .in_5(1'b0), .in_6(1'b0), .in_7(1'b0), .in_8(1'b0), .in_9(and_22_out), .in_10(1'b0),
    .in_11(1'b0), .in_12(1'b0), .in_13(1'b0), .in_14(1'b0), .in_15(1'b0), .out(multiplexer_16_out));
  D_FF d_ff_6 (.D(multiplexer_16_out), .C(clk), .Q(Q_d));  // open: nQ
  Decoder #(.Selector_Bits(4)) decoder_2 (
    .sel({Q_a, Q_b, Q_c, Q_d}), .out_0(_0000), .out_1(_0001), .out_2(_0010), .out_3(_0011), .out_4(_0100),
    .out_5(_0101), .out_6(_0110), .out_7(_0111), .out_8(_1000), .out_9(_1001), .out_10(_1010),
    .out_11(_1011), .out_12(_1100), .out_13(_1101), .out_14(_1110), .out_15(_1111));
  or or_28 (or_28_out, _1000, _0111, _0110, _0101, _0100);
  BitCount #(.Bits(13)) bitcount_2 (
    .in({_10001, _10010, _10011, _10100, _10101, _10110, _10111, _11000, _11001, _11010, _11011, _11100, _11101}),
    .out({bitcount_2_out, ALU}));
  BitCount #(.Bits(12)) bitcount_3 (
    .in({_00000, _00001, _00010, _00011, _00100, _00101, _00110, _00111, _01000, _01001, _01010, _01011}),
    .out({bitcount_3_out, move}));
  Demultiplexer #(.Selector_Bits(5)) demultiplexer_1 (
    .sel(opcode), .in(or_28_out), .out_0(_00000), .out_1(_00001), .out_2(_00010), .out_3(_00011),
    .out_4(_00100), .out_5(_00101), .out_6(_00110), .out_7(_00111), .out_8(_01000), .out_9(_01001),
    .out_10(_01010), .out_11(_01011), .out_12(_01100), .out_13(_01101), .out_14(_01110), .out_15(_01111),
    .out_16(_10000), .out_17(_10001), .out_18(_10010), .out_19(_10011), .out_20(_10100), .out_21(_10101),
    .out_22(_10110), .out_23(_10111), .out_24(_11000), .out_25(_11001), .out_26(_11010), .out_27(_11011),
    .out_28(_11100), .out_29(_11101), .out_30(_11110), .out_31(_11111));
  BitCount #(.Bits(5)) bitcount_4 (.in({_01100, _01101, _01110, _01111, _10000}), .out({bitcount_4_out, jumpOp}));

  // Other names for the same wires on the sheet: future = _11110; pc[7:0] = out_12; stop = _11111

  // Notes on the sheet:
  //   Testcases
  //   Counters
  //   I/O
  //   LoadValue
  //   Registers
  //   ALU
  //   contents of exponent (hex, n*v repeats v):
  //   1,0,a0000,a00000,0,40000,0,0,9*1,2,4,8,10,20,40,80,1,3,9,1b,51
  //   ,f3,d9,8b,1,4,10,40,4*0,1,5,19,7d,71,35,9,2d,1,6,24,d8,10,60,40
  //   ,80,1,7,31,57,61,a7,91,f7,0,0,0,1,0,0,0,1,0,1,5*0,1,0,0,0,1,5*0
  //   ,1,7*0,1,0,0,0,1,0,1,0,0,0,1,0,1,0,0,0,1,13*0,1,0,0,0,1,5*0,1
  //   ,0,1,9*0,1,0,1,5*0,1,5*0,1,0,0,0,1,5*0,1,5*0,1,0,1,9*0,1,0,1,0,0,0
  //   ,1,0,1,11*0,1,11*0,1,0,0,0,1,0,1,0,0,0,1,5*0,1,0,1,9*0,1
  //   Processing States
  //   Result Showing States
  //   Flags
  //   contents of isPrime (hex, n*v repeats v):
  //   0,0,1,1,0,1,0,1,0,0,0,1,0,1,0,0,0,1,0,1,0,0,0,1,5*0,1,0,1,5*0
  //   ,1,0,0,0,1,0,1,0,0,0,1,5*0,1,5*0,1,0,1,5*0,1,0,0,0,1,0,1,5*0,1
  //   ,0,0,0,1,5*0,1,7*0,1,0,0,0,1,0,1,0,0,0,1,0,1,0,0,0,1,13*0,1,0,0,0
  //   ,1,5*0,1,0,1,9*0,1,0,1,5*0,1,5*0,1,0,0,0,1,5*0,1,5*0,1,0,1,9*0
  //   ,1,0,1,0,0,0,1,0,1,11*0,1,11*0,1,0,0,0,1,0,1,0,0,0,1,5*0,1,0,1
  //   ,9*0,1
  //   Members
  //   6733285921	อนรรฆวี ชูจินดา (ผู้พัฒนาวงจรหลัก)	
  //   6733285921	ป้อมบุญ ป้อมบุญมี (ผู้พัฒนาวงจรหลัก)
  //   6733285921	ชิติพัฒน์ ภู่ทอง
  //   6733013521 กฤษฎา ลิ้มศรีประพันธ์
endmodule

/* Test case 01_P01T01:
M N progIN reset progLoad start result clk valid done output
0 0 0 0 0 0 0 0 x x x
0 0 0 0 0 0 0 1 x x x
0 0 0 1 0 0 0 0 x x x
0 0 0 1 0 0 0 1 0 0 x
0 0 0 0 0 0 0 0 0 0 x
0 0 0 0 0 0 0 1 0 0 x
0 0 0 0 0 0 0 0 0 0 x
0 0 0 0 0 0 0 1 0 0 x
0 0 0 0 0 0 0 0 0 0 x
0 0 0 0 0 0 0 1 0 0 x
0 0 0 0 0 0 0 0 0 0 x
0 0 0 0 0 0 0 1 0 0 x
0 0 0 0 0 0 0 0 0 0 x
0 0 0 0 0 0 0 1 0 0 x
0 0 0 0 0 0 0 0 0 0 x
0 0 0 0 0 0 0 1 0 0 x
0 0 0 0 0 0 0 0 0 0 x
0 0 0 0 0 0 0 1 0 0 x
0 0 0 0 0 0 0 0 0 0 x
0 0 0 0 0 0 0 1 0 0 x
0 0 0 0 0 0 0 0 0 0 x
0 0 0 0 0 0 0 1 0 0 x
0 0 0 0 0 0 0 0 0 0 x
0 0 0 0 0 0 0 1 0 0 x
0 0 0 0 0 0 0 0 0 0 x
0 0 0 0 0 0 0 1 0 0 x
0 0 0 0 0 0 0 0 0 0 x
0 0 0 0 0 0 0 1 0 0 x
0 0 0 0 0 0 0 0 0 0 x
0 0 0 0 0 0 0 1 0 0 x
0 0 0 0 0 0 0 0 0 0 x
0 0 0 0 0 0 0 1 0 0 x
0 0 0 0 0 0 0 0 0 0 x
0 0 0 0 0 0 0 1 0 0 x
0 0 0 0 0 0 0 0 0 0 x
0 0 0 0 0 0 0 1 0 0 x
0 0 0 0 0 0 0 0 0 0 x
0 0 0 0 0 0 0 1 0 0 x
0 0 0 0 0 0 0 0 0 0 x
0 0 0 0 0 0 0 1 0 0 x
0 0 0 0 0 0 0 0 0 0 x
0 0 0 0 0 0 0 1 0 0 x
0 0 271 0 1 0 0 0 0 0 x
0 0 271 0 1 0 0 1 0 0 x
0 0 565 0 1 0 0 0 0 0 x
0 0 565 0 1 0 0 1 0 0 x
0 0 4352 0 1 0 0 0 0 0 x
0 0 4352 0 1 0 0 1 0 0 x
0 0 2819 0 1 0 0 0 0 0 x
0 0 2819 0 1 0 0 1 0 0 x
0 0 7936 0 1 0 0 0 0 0 x
0 0 7936 0 1 0 0 1 0 0 x
0 0 0 0 0 1 0 0 0 0 x
0 0 0 0 0 1 0 1 0 0 x
0 0 0 0 0 0 0 0 x 0 x
0 0 0 0 0 0 0 1 x 0 x
0 0 0 0 0 0 0 0 x 0 x
0 0 0 0 0 0 0 1 x 0 x
0 0 0 0 0 0 0 0 x 0 x
0 0 0 0 0 0 0 1 x 0 x
0 0 0 0 0 0 0 0 x 0 x
0 0 0 0 0 0 0 1 x 0 x
0 0 0 0 0 0 0 0 x 0 x
0 0 0 0 0 0 0 1 x 0 x
0 0 0 0 0 0 0 0 x 0 x
0 0 0 0 0 0 0 1 x 0 x
0 0 0 0 0 0 0 0 x 0 x
0 0 0 0 0 0 0 1 x 0 x
0 0 0 0 0 0 0 0 x 0 x
0 0 0 0 0 0 0 1 x 0 x
0 0 0 0 0 0 0 0 x 0 x
0 0 0 0 0 0 0 1 x 0 x
0 0 0 0 0 0 0 0 x 0 x
0 0 0 0 0 0 0 1 x 0 x
0 0 0 0 0 0 0 0 x 0 x
0 0 0 0 0 0 0 1 x 0 x
0 0 0 0 0 0 0 0 x 0 x
0 0 0 0 0 0 0 1 x 0 x
0 0 0 0 0 0 0 0 x 0 x
0 0 0 0 0 0 0 1 x 0 x
0 0 0 0 0 0 0 0 x 0 x
0 0 0 0 0 0 0 1 x 0 x
0 0 0 0 0 0 0 0 x 0 x
0 0 0 0 0 0 0 1 x 0 x
0 0 0 0 0 0 0 0 x 0 x
0 0 0 0 0 0 0 1 x 0 x
0 0 0 0 0 0 0 0 x 0 x
0 0 0 0 0 0 0 1 x 0 x
0 0 0 0 0 0 0 0 x 0 x
0 0 0 0 0 0 0 1 x 0 x
0 0 0 0 0 0 0 0 x 0 x
0 0 0 0 0 0 0 1 x 0 x
0 0 0 0 0 0 0 0 x 0 x
0 0 0 0 0 0 0 1 x 0 x
0 0 0 0 0 0 0 0 x 0 x
0 0 0 0 0 0 0 1 x 0 x
0 0 0 0 0 0 0 0 x 0 x
0 0 0 0 0 0 0 1 x 0 x
0 0 0 0 0 0 0 0 x 0 x
0 0 0 0 0 0 0 1 x 0 x
0 0 0 0 0 0 0 0 x 0 x
0 0 0 0 0 0 0 1 x 0 x
0 0 0 0 0 0 0 0 x 0 x
0 0 0 0 0 0 0 1 x 0 x
0 0 0 0 0 0 0 0 x 0 x
0 0 0 0 0 0 0 1 1 0 x
0 0 0 0 0 0 1 0 1 0 x
0 0 0 0 0 0 1 1 1 0 0
0 0 0 0 0 0 0 0 1 0 0
0 0 0 0 0 0 0 1 1 0 0
0 0 0 0 0 0 0 0 1 0 0
0 0 0 0 0 0 0 1 1 0 0
0 0 0 0 0 0 0 0 1 0 0
0 0 0 0 0 0 0 1 1 0 68
0 0 0 0 0 0 0 0 1 0 68
0 0 0 0 0 0 0 1 1 0 0
0 0 0 0 0 0 0 0 1 0 0
0 0 0 0 0 0 0 1 1 0 0
0 0 0 0 0 0 0 0 1 0 0
0 0 0 0 0 0 0 1 1 0 0
0 0 0 0 0 0 0 0 1 0 0
0 0 0 0 0 0 0 1 1 0 0
0 0 0 0 0 0 0 0 1 0 0
0 0 0 0 0 0 0 1 1 0 0
0 0 0 0 0 0 0 0 1 0 0
0 0 0 0 0 0 0 1 1 0 0
0 0 0 0 0 0 0 0 1 0 0
0 0 0 0 0 0 0 1 1 0 0
0 0 0 0 0 0 0 0 1 0 0
0 0 0 0 0 0 0 1 1 0 0
0 0 0 0 0 0 0 0 1 0 0
0 0 0 0 0 0 0 1 1 0 0
0 0 0 0 0 0 0 0 1 0 0
0 0 0 0 0 0 0 1 1 0 0
0 0 0 0 0 0 0 0 1 0 0
0 0 0 0 0 0 0 1 1 0 0
0 0 0 0 0 0 0 0 1 0 0
0 0 0 0 0 0 0 1 1 0 0
0 0 0 0 0 0 0 0 1 0 0
0 0 0 0 0 0 0 1 1 1 x
0 0 0 0 0 0 0 0 1 1 x
0 0 0 0 0 0 0 1 1 1 x
0 0 0 0 0 0 0 0 1 1 x
*/

/* Test case 07_P06T02:
M N progIN reset progLoad start result clk valid done output
0 0 0 0 0 0 0 0 x x x
0 0 0 0 0 0 0 1 x x x
0 0 0 1 0 0 0 0 x x x
0 0 0 1 0 0 0 1 0 0 x
0 0 0 0 0 0 0 0 0 0 x
0 0 0 0 0 0 0 1 0 0 x
0 0 0 0 0 0 0 0 0 0 x
0 0 0 0 0 0 0 1 0 0 x
0 0 0 0 0 0 0 0 0 0 x
0 0 0 0 0 0 0 1 0 0 x
0 0 0 0 0 0 0 0 0 0 x
0 0 0 0 0 0 0 1 0 0 x
0 0 0 0 0 0 0 0 0 0 x
0 0 0 0 0 0 0 1 0 0 x
0 0 0 0 0 0 0 0 0 0 x
0 0 0 0 0 0 0 1 0 0 x
0 0 0 0 0 0 0 0 0 0 x
0 0 0 0 0 0 0 1 0 0 x
0 0 0 0 0 0 0 0 0 0 x
0 0 0 0 0 0 0 1 0 0 x
0 0 0 0 0 0 0 0 0 0 x
0 0 0 0 0 0 0 1 0 0 x
0 0 0 0 0 0 0 0 0 0 x
0 0 0 0 0 0 0 1 0 0 x
0 0 0 0 0 0 0 0 0 0 x
0 0 0 0 0 0 0 1 0 0 x
0 0 0 0 0 0 0 0 0 0 x
0 0 0 0 0 0 0 1 0 0 x
0 0 0 0 0 0 0 0 0 0 x
0 0 0 0 0 0 0 1 0 0 x
0 0 0 0 0 0 0 0 0 0 x
0 0 0 0 0 0 0 1 0 0 x
0 0 0 0 0 0 0 0 0 0 x
0 0 0 0 0 0 0 1 0 0 x
0 0 0 0 0 0 0 0 0 0 x
0 0 0 0 0 0 0 1 0 0 x
0 0 0 0 0 0 0 0 0 0 x
0 0 0 0 0 0 0 1 0 0 x
0 0 0 0 0 0 0 0 0 0 x
0 0 0 0 0 0 0 1 0 0 x
0 0 0 0 0 0 0 0 0 0 x
0 0 0 0 0 0 0 1 0 0 x
0 0 1792 0 1 0 0 0 0 0 x
0 0 1792 0 1 0 0 1 0 0 x
0 0 1536 0 1 0 0 0 0 0 x
0 0 1536 0 1 0 0 1 0 0 x
0 0 2817 0 1 0 0 0 0 0 x
0 0 2817 0 1 0 0 1 0 0 x
0 0 2048 0 1 0 0 0 0 0 x
0 0 2048 0 1 0 0 1 0 0 x
0 0 1536 0 1 0 0 0 0 0 x
0 0 1536 0 1 0 0 1 0 0 x
0 0 2818 0 1 0 0 0 0 0 x
0 0 2818 0 1 0 0 1 0 0 x
0 0 1024 0 1 0 0 0 0 0 x
0 0 1024 0 1 0 0 1 0 0 x
0 0 2561 0 1 0 0 0 0 0 x
0 0 2561 0 1 0 0 1 0 0 x
0 0 4864 0 1 0 0 0 0 0 x
0 0 4864 0 1 0 0 1 0 0 x
0 0 2819 0 1 0 0 0 0 0 x
0 0 2819 0 1 0 0 1 0 0 x
0 0 2561 0 1 0 0 0 0 0 x
0 0 2561 0 1 0 0 1 0 0 x
0 0 5120 0 1 0 0 0 0 0 x
0 0 5120 0 1 0 0 1 0 0 x
0 0 2820 0 1 0 0 0 0 0 x
0 0 2820 0 1 0 0 1 0 0 x
0 0 7936 0 1 0 0 0 0 0 x
0 0 7936 0 1 0 0 1 0 0 x
15 7 0 0 0 1 0 0 0 0 x
15 7 0 0 0 1 0 1 0 0 x
15 7 0 0 0 0 0 0 x 0 x
15 7 0 0 0 0 0 1 x 0 x
15 7 0 0 0 0 0 0 x 0 x
15 7 0 0 0 0 0 1 x 0 x
15 7 0 0 0 0 0 0 x 0 x
15 7 0 0 0 0 0 1 x 0 x
15 7 0 0 0 0 0 0 x 0 x
15 7 0 0 0 0 0 1 x 0 x
15 7 0 0 0 0 0 0 x 0 x
15 7 0 0 0 0 0 1 x 0 x
15 7 0 0 0 0 0 0 x 0 x
15 7 0 0 0 0 0 1 x 0 x
15 7 0 0 0 0 0 0 x 0 x
15 7 0 0 0 0 0 1 x 0 x
15 7 0 0 0 0 0 0 x 0 x
15 7 0 0 0 0 0 1 x 0 x
15 7 0 0 0 0 0 0 x 0 x
15 7 0 0 0 0 0 1 x 0 x
15 7 0 0 0 0 0 0 x 0 x
15 7 0 0 0 0 0 1 x 0 x
15 7 0 0 0 0 0 0 x 0 x
15 7 0 0 0 0 0 1 x 0 x
15 7 0 0 0 0 0 0 x 0 x
15 7 0 0 0 0 0 1 x 0 x
15 7 0 0 0 0 0 0 x 0 x
15 7 0 0 0 0 0 1 x 0 x
15 7 0 0 0 0 0 0 x 0 x
15 7 0 0 0 0 0 1 x 0 x
15 7 0 0 0 0 0 0 x 0 x
15 7 0 0 0 0 0 1 x 0 x
15 7 0 0 0 0 0 0 x 0 x
15 7 0 0 0 0 0 1 x 0 x
15 7 0 0 0 0 0 0 x 0 x
15 7 0 0 0 0 0 1 x 0 x
15 7 0 0 0 0 0 0 x 0 x
15 7 0 0 0 0 0 1 x 0 x
15 7 0 0 0 0 0 0 x 0 x
15 7 0 0 0 0 0 1 x 0 x
15 7 0 0 0 0 0 0 x 0 x
0 0 0 0 0 0 0 1 x 0 x
0 0 0 0 0 0 0 0 x 0 x
0 0 0 0 0 0 0 1 x 0 x
0 0 0 0 0 0 0 0 x 0 x
0 0 0 0 0 0 0 1 x 0 x
0 0 0 0 0 0 0 0 x 0 x
0 0 0 0 0 0 0 1 x 0 x
0 0 0 0 0 0 0 0 x 0 x
0 0 0 0 0 0 0 1 x 0 x
0 0 0 0 0 0 0 0 x 0 x
0 0 0 0 0 0 0 1 x 0 x
0 0 0 0 0 0 0 0 x 0 x
0 0 0 0 0 0 0 1 1 0 x
0 0 0 0 0 0 1 0 1 0 0
0 0 0 0 0 0 1 1 1 0 0
0 0 0 0 0 0 0 0 1 0 0
0 0 0 0 0 0 0 1 1 0 15
0 0 0 0 0 0 0 0 1 0 15
0 0 0 0 0 0 0 1 1 0 7
0 0 0 0 0 0 0 0 1 0 7
0 0 0 0 0 0 0 1 1 0 105
0 0 0 0 0 0 0 0 1 0 105
0 0 0 0 0 0 0 1 1 0 2
0 0 0 0 0 0 0 0 1 0 2
0 0 0 0 0 0 0 1 1 0 0
0 0 0 0 0 0 0 0 1 0 0
0 0 0 0 0 0 0 1 1 0 0
0 0 0 0 0 0 0 0 1 0 0
0 0 0 0 0 0 0 1 1 0 0
0 0 0 0 0 0 0 0 1 0 0
0 0 0 0 0 0 0 1 1 0 0
0 0 0 0 0 0 0 0 1 0 0
0 0 0 0 0 0 0 1 1 0 0
0 0 0 0 0 0 0 0 1 0 0
0 0 0 0 0 0 0 1 1 0 0
0 0 0 0 0 0 0 0 1 0 0
0 0 0 0 0 0 0 1 1 0 0
0 0 0 0 0 0 0 0 1 0 0
0 0 0 0 0 0 0 1 1 0 0
0 0 0 0 0 0 0 0 1 0 0
0 0 0 0 0 0 0 1 1 0 0
0 0 0 0 0 0 0 0 1 0 0
0 0 0 0 0 0 0 1 1 0 0
0 0 0 0 0 0 0 0 1 0 0
0 0 0 0 0 0 0 1 1 0 0
0 0 0 0 0 0 0 0 1 0 0
0 0 0 0 0 0 0 1 1 1 x
0 0 0 0 0 0 0 0 1 1 x
0 0 0 0 0 0 0 1 1 1 x
0 0 0 0 0 0 0 0 1 1 x
*/

/* Test case 02_P01T2:
M N progIN reset progLoad start result clk valid done output
0 0 0 0 0 0 0 0 x x x
0 0 0 0 0 0 0 1 x x x
0 0 0 1 0 0 0 0 x x x
0 0 0 1 0 0 0 1 0 0 x
0 0 0 0 0 0 0 0 0 0 x
0 0 0 0 0 0 0 1 0 0 x
0 0 0 0 0 0 0 0 0 0 x
0 0 0 0 0 0 0 1 0 0 x
0 0 0 0 0 0 0 0 0 0 x
0 0 0 0 0 0 0 1 0 0 x
0 0 0 0 0 0 0 0 0 0 x
0 0 0 0 0 0 0 1 0 0 x
0 0 0 0 0 0 0 0 0 0 x
0 0 0 0 0 0 0 1 0 0 x
0 0 0 0 0 0 0 0 0 0 x
0 0 0 0 0 0 0 1 0 0 x
0 0 0 0 0 0 0 0 0 0 x
0 0 0 0 0 0 0 1 0 0 x
0 0 0 0 0 0 0 0 0 0 x
0 0 0 0 0 0 0 1 0 0 x
0 0 0 0 0 0 0 0 0 0 x
0 0 0 0 0 0 0 1 0 0 x
0 0 0 0 0 0 0 0 0 0 x
0 0 0 0 0 0 0 1 0 0 x
0 0 0 0 0 0 0 0 0 0 x
0 0 0 0 0 0 0 1 0 0 x
0 0 0 0 0 0 0 0 0 0 x
0 0 0 0 0 0 0 1 0 0 x
0 0 0 0 0 0 0 0 0 0 x
0 0 0 0 0 0 0 1 0 0 x
0 0 0 0 0 0 0 0 0 0 x
0 0 0 0 0 0 0 1 0 0 x
0 0 0 0 0 0 0 0 0 0 x
0 0 0 0 0 0 0 1 0 0 x
0 0 0 0 0 0 0 0 0 0 x
0 0 0 0 0 0 0 1 0 0 x
0 0 0 0 0 0 0 0 0 0 x
0 0 0 0 0 0 0 1 0 0 x
0 0 0 0 0 0 0 0 0 0 x
0 0 0 0 0 0 0 1 0 0 x
0 0 0 0 0 0 0 0 0 0 x
0 0 0 0 0 0 0 1 0 0 x
0 0 271 0 1 0 0 0 0 0 x
0 0 271 0 1 0 0 1 0 0 x
0 0 565 0 1 0 0 0 0 0 x
0 0 565 0 1 0 0 1 0 0 x
0 0 4352 0 1 0 0 0 0 0 x
0 0 4352 0 1 0 0 1 0 0 x
0 0 2819 0 1 0 0 0 0 0 x
0 0 2819 0 1 0 0 1 0 0 x
0 0 7936 0 1 0 0 0 0 0 x
0 0 7936 0 1 0 0 1 0 0 x
0 0 0 0 0 1 0 0 0 0 x
0 0 0 0 0 1 0 1 0 0 x
0 0 0 0 0 0 0 0 x 0 x
0 0 0 0 0 0 0 1 x 0 x
0 0 0 0 0 0 0 0 x 0 x
0 0 0 0 0 0 0 1 x 0 x
0 0 0 0 0 0 0 0 x 0 x
0 0 0 0 0 0 0 1 x 0 x
0 0 0 0 0 0 0 0 x 0 x
0 0 0 0 0 0 0 1 x 0 x
0 0 0 0 0 0 0 0 x 0 x
0 0 0 0 0 0 0 1 x 0 x
0 0 0 0 0 0 0 0 x 0 x
0 0 0 0 0 0 0 1 x 0 x
0 0 0 0 0 0 0 0 x 0 x
0 0 0 0 0 0 0 1 x 0 x
0 0 0 0 0 0 0 0 x 0 x
0 0 0 0 0 0 0 1 x 0 x
0 0 0 0 0 0 0 0 x 0 x
0 0 0 0 0 0 0 1 x 0 x
0 0 0 0 0 0 0 0 x 0 x
0 0 0 0 0 0 0 1 x 0 x
0 0 0 0 0 0 0 0 x 0 x
0 0 0 0 0 0 0 1 x 0 x
0 0 0 0 0 0 0 0 x 0 x
0 0 0 0 0 0 0 1 x 0 x
0 0 0 0 0 0 0 0 x 0 x
0 0 0 0 0 0 0 1 x 0 x
0 0 0 0 0 0 0 0 x 0 x
0 0 0 0 0 0 0 1 x 0 x
0 0 0 0 0 0 0 0 x 0 x
0 0 0 0 0 0 0 1 x 0 x
0 0 0 0 0 0 0 0 x 0 x
0 0 0 0 0 0 0 1 x 0 x
0 0 0 0 0 0 0 0 x 0 x
0 0 0 0 0 0 0 1 x 0 x
0 0 0 0 0 0 0 0 x 0 x
0 0 0 0 0 0 0 1 x 0 x
0 0 0 0 0 0 0 0 x 0 x
0 0 0 0 0 0 0 1 x 0 x
0 0 0 0 0 0 0 0 x 0 x
0 0 0 0 0 0 0 1 x 0 x
0 0 0 0 0 0 0 0 x 0 x
0 0 0 0 0 0 0 1 x 0 x
0 0 0 0 0 0 0 0 x 0 x
0 0 0 0 0 0 0 1 x 0 x
0 0 0 0 0 0 0 0 x 0 x
0 0 0 0 0 0 0 1 x 0 x
0 0 0 0 0 0 0 0 x 0 x
0 0 0 0 0 0 0 1 x 0 x
0 0 0 0 0 0 0 0 x 0 x
0 0 0 0 0 0 0 1 x 0 x
0 0 0 0 0 0 0 0 x 0 x
0 0 0 0 0 0 0 1 1 0 x
0 0 0 0 0 0 1 0 1 0 x
0 0 0 0 0 0 1 1 1 0 0
0 0 0 0 0 0 0 0 1 0 0
0 0 0 0 0 0 0 1 1 0 0
0 0 0 0 0 0 0 0 1 0 0
0 0 0 0 0 0 0 1 1 0 0
0 0 0 0 0 0 0 0 1 0 0
0 0 0 0 0 0 0 1 1 0 68
0 0 0 0 0 0 0 0 1 0 68
0 0 0 0 0 0 0 1 1 0 0
0 0 0 0 0 0 0 0 1 0 0
0 0 0 0 0 0 0 1 1 0 0
0 0 0 0 0 0 0 0 1 0 0
0 0 0 0 0 0 0 1 1 0 0
0 0 0 0 0 0 0 0 1 0 0
0 0 0 0 0 0 0 1 1 0 0
0 0 0 0 0 0 0 0 1 0 0
0 0 0 0 0 0 0 1 1 0 0
0 0 0 0 0 0 0 0 1 0 0
0 0 0 0 0 0 0 1 1 0 0
0 0 0 0 0 0 0 0 1 0 0
0 0 0 0 0 0 0 1 1 0 0
0 0 0 0 0 0 0 0 1 0 0
0 0 0 0 0 0 0 1 1 0 0
0 0 0 0 0 0 0 0 1 0 0
0 0 0 0 0 0 0 1 1 0 0
0 0 0 0 0 0 0 0 1 0 0
0 0 0 0 0 0 0 1 1 0 0
0 0 0 0 0 0 0 0 1 0 0
0 0 0 0 0 0 0 1 1 0 0
0 0 0 0 0 0 0 0 1 0 0
0 0 0 0 0 0 0 1 1 0 0
0 0 0 0 0 0 0 0 1 0 0
0 0 0 0 0 0 0 1 1 1 x
0 0 0 0 0 0 0 0 1 1 x
0 0 0 0 0 0 0 1 1 1 x
0 0 0 0 0 0 0 0 1 1 x
0 0 0 0 0 0 0 1 1 1 x
0 0 0 0 0 0 1 0 1 X x
0 0 0 0 0 0 1 1 1 X 0
0 0 0 0 0 0 0 0 1 0 0
0 0 0 0 0 0 0 1 1 0 0
0 0 0 0 0 0 0 0 1 0 0
0 0 0 0 0 0 0 1 1 0 0
0 0 0 0 0 0 0 0 1 0 0
0 0 0 0 0 0 0 1 1 0 68
0 0 0 0 0 0 0 0 1 0 68
0 0 0 0 0 0 0 1 1 0 0
0 0 0 0 0 0 0 0 1 0 0
0 0 0 0 0 0 0 1 1 0 0
0 0 0 0 0 0 0 0 1 0 0
0 0 0 0 0 0 0 1 1 0 0
0 0 0 0 0 0 0 0 1 0 0
0 0 0 0 0 0 0 1 1 0 0
0 0 0 0 0 0 0 0 1 0 0
0 0 0 0 0 0 0 1 1 0 0
0 0 0 0 0 0 0 0 1 0 0
0 0 0 0 0 0 0 1 1 0 0
0 0 0 0 0 0 0 0 1 0 0
0 0 0 0 0 0 0 1 1 0 0
0 0 0 0 0 0 0 0 1 0 0
0 0 0 0 0 0 0 1 1 0 0
0 0 0 0 0 0 0 0 1 0 0
0 0 0 0 0 0 0 1 1 0 0
0 0 0 0 0 0 0 0 1 0 0
0 0 0 0 0 0 0 1 1 0 0
0 0 0 0 0 0 0 0 1 0 0
0 0 0 0 0 0 0 1 1 0 0
0 0 0 0 0 0 0 0 1 0 0
0 0 0 0 0 0 0 1 1 0 0
0 0 0 0 0 0 0 0 1 0 0
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*/

/* Test case 08_P06T2:
M N progIN reset progLoad start result clk valid done output
0 0 0 0 0 0 0 0 x x x
0 0 0 0 0 0 0 1 x x x
0 0 0 1 0 0 0 0 x x x
0 0 0 1 0 0 0 1 0 0 x
0 0 0 0 0 0 0 0 0 0 x
0 0 0 0 0 0 0 1 0 0 x
0 0 0 0 0 0 0 0 0 0 x
0 0 0 0 0 0 0 1 0 0 x
0 0 0 0 0 0 0 0 0 0 x
0 0 0 0 0 0 0 1 0 0 x
0 0 0 0 0 0 0 0 0 0 x
0 0 0 0 0 0 0 1 0 0 x
0 0 0 0 0 0 0 0 0 0 x
0 0 0 0 0 0 0 1 0 0 x
0 0 0 0 0 0 0 0 0 0 x
0 0 0 0 0 0 0 1 0 0 x
0 0 0 0 0 0 0 0 0 0 x
0 0 0 0 0 0 0 1 0 0 x
0 0 0 0 0 0 0 0 0 0 x
0 0 0 0 0 0 0 1 0 0 x
0 0 0 0 0 0 0 0 0 0 x
0 0 0 0 0 0 0 1 0 0 x
0 0 0 0 0 0 0 0 0 0 x
0 0 0 0 0 0 0 1 0 0 x
0 0 0 0 0 0 0 0 0 0 x
0 0 0 0 0 0 0 1 0 0 x
0 0 0 0 0 0 0 0 0 0 x
0 0 0 0 0 0 0 1 0 0 x
0 0 0 0 0 0 0 0 0 0 x
0 0 0 0 0 0 0 1 0 0 x
0 0 0 0 0 0 0 0 0 0 x
0 0 0 0 0 0 0 1 0 0 x
0 0 0 0 0 0 0 0 0 0 x
0 0 0 0 0 0 0 1 0 0 x
0 0 0 0 0 0 0 0 0 0 x
0 0 0 0 0 0 0 1 0 0 x
0 0 0 0 0 0 0 0 0 0 x
0 0 0 0 0 0 0 1 0 0 x
0 0 0 0 0 0 0 0 0 0 x
0 0 0 0 0 0 0 1 0 0 x
0 0 0 0 0 0 0 0 0 0 x
0 0 0 0 0 0 0 1 0 0 x
0 0 1792 0 1 0 0 0 0 0 x
0 0 1792 0 1 0 0 1 0 0 x
0 0 1536 0 1 0 0 0 0 0 x
0 0 1536 0 1 0 0 1 0 0 x
0 0 2817 0 1 0 0 0 0 0 x
0 0 2817 0 1 0 0 1 0 0 x
0 0 2048 0 1 0 0 0 0 0 x
0 0 2048 0 1 0 0 1 0 0 x
0 0 1536 0 1 0 0 0 0 0 x
0 0 1536 0 1 0 0 1 0 0 x
0 0 2818 0 1 0 0 0 0 0 x
0 0 2818 0 1 0 0 1 0 0 x
0 0 1024 0 1 0 0 0 0 0 x
0 0 1024 0 1 0 0 1 0 0 x
0 0 2561 0 1 0 0 0 0 0 x
0 0 2561 0 1 0 0 1 0 0 x
0 0 4864 0 1 0 0 0 0 0 x
0 0 4864 0 1 0 0 1 0 0 x
0 0 2819 0 1 0 0 0 0 0 x
0 0 2819 0 1 0 0 1 0 0 x
0 0 2561 0 1 0 0 0 0 0 x
0 0 2561 0 1 0 0 1 0 0 x
0 0 5120 0 1 0 0 0 0 0 x
0 0 5120 0 1 0 0 1 0 0 x
0 0 2820 0 1 0 0 0 0 0 x
0 0 2820 0 1 0 0 1 0 0 x
0 0 7936 0 1 0 0 0 0 0 x
0 0 7936 0 1 0 0 1 0 0 x
15 7 0 0 0 1 0 0 0 0 x
15 7 0 0 0 1 0 1 0 0 x
15 7 0 0 0 0 0 0 x 0 x
15 7 0 0 0 0 0 1 x 0 x
15 7 0 0 0 0 0 0 x 0 x
15 7 0 0 0 0 0 1 x 0 x
15 7 0 0 0 0 0 0 x 0 x
15 7 0 0 0 0 0 1 x 0 x
15 7 0 0 0 0 0 0 x 0 x
15 7 0 0 0 0 0 1 x 0 x
15 7 0 0 0 0 0 0 x 0 x
15 7 0 0 0 0 0 1 x 0 x
15 7 0 0 0 0 0 0 x 0 x
15 7 0 0 0 0 0 1 x 0 x
15 7 0 0 0 0 0 0 x 0 x
15 7 0 0 0 0 0 1 x 0 x
15 7 0 0 0 0 0 0 x 0 x
15 7 0 0 0 0 0 1 x 0 x
15 7 0 0 0 0 0 0 x 0 x
15 7 0 0 0 0 0 1 x 0 x
15 7 0 0 0 0 0 0 x 0 x
15 7 0 0 0 0 0 1 x 0 x
15 7 0 0 0 0 0 0 x 0 x
15 7 0 0 0 0 0 1 x 0 x
15 7 0 0 0 0 0 0 x 0 x
15 7 0 0 0 0 0 1 x 0 x
15 7 0 0 0 0 0 0 x 0 x
15 7 0 0 0 0 0 1 x 0 x
15 7 0 0 0 0 0 0 x 0 x
15 7 0 0 0 0 0 1 x 0 x
15 7 0 0 0 0 0 0 x 0 x
15 7 0 0 0 0 0 1 x 0 x
15 7 0 0 0 0 0 0 x 0 x
15 7 0 0 0 0 0 1 x 0 x
15 7 0 0 0 0 0 0 x 0 x
15 7 0 0 0 0 0 1 x 0 x
15 7 0 0 0 0 0 0 x 0 x
15 7 0 0 0 0 0 1 x 0 x
15 7 0 0 0 0 0 0 x 0 x
15 7 0 0 0 0 0 1 x 0 x
15 7 0 0 0 0 0 0 x 0 x
0 0 0 0 0 0 0 1 x 0 x
0 0 0 0 0 0 0 0 x 0 x
0 0 0 0 0 0 0 1 x 0 x
0 0 0 0 0 0 0 0 x 0 x
0 0 0 0 0 0 0 1 x 0 x
0 0 0 0 0 0 0 0 x 0 x
0 0 0 0 0 0 0 1 x 0 x
0 0 0 0 0 0 0 0 x 0 x
0 0 0 0 0 0 0 1 x 0 x
0 0 0 0 0 0 0 0 x 0 x
0 0 0 0 0 0 0 1 x 0 x
0 0 0 0 0 0 0 0 x 0 x
0 0 0 0 0 0 0 1 1 0 x
0 0 0 0 0 0 1 0 1 0 0
0 0 0 0 0 0 1 1 1 0 0
0 0 0 0 0 0 0 0 1 0 0
0 0 0 0 0 0 0 1 1 0 15
0 0 0 0 0 0 0 0 1 0 15
0 0 0 0 0 0 0 1 1 0 7
0 0 0 0 0 0 0 0 1 0 7
0 0 0 0 0 0 0 1 1 0 105
0 0 0 0 0 0 0 0 1 0 105
0 0 0 0 0 0 0 1 1 0 2
0 0 0 0 0 0 0 0 1 0 2
0 0 0 0 0 0 0 1 1 0 0
0 0 0 0 0 0 0 0 1 0 0
0 0 0 0 0 0 0 1 1 0 0
0 0 0 0 0 0 0 0 1 0 0
0 0 0 0 0 0 0 1 1 0 0
0 0 0 0 0 0 0 0 1 0 0
0 0 0 0 0 0 0 1 1 0 0
0 0 0 0 0 0 0 0 1 0 0
0 0 0 0 0 0 0 1 1 0 0
0 0 0 0 0 0 0 0 1 0 0
0 0 0 0 0 0 0 1 1 0 0
0 0 0 0 0 0 0 0 1 0 0
0 0 0 0 0 0 0 1 1 0 0
0 0 0 0 0 0 0 0 1 0 0
0 0 0 0 0 0 0 1 1 0 0
0 0 0 0 0 0 0 0 1 0 0
0 0 0 0 0 0 0 1 1 0 0
0 0 0 0 0 0 0 0 1 0 0
0 0 0 0 0 0 0 1 1 0 0
0 0 0 0 0 0 0 0 1 0 0
0 0 0 0 0 0 0 1 1 0 0
0 0 0 0 0 0 0 0 1 0 0
0 0 0 0 0 0 0 1 1 1 x
0 0 0 0 0 0 0 0 1 1 x
0 0 0 0 0 0 0 1 1 1 x
0 0 0 0 0 0 0 0 1 1 x
0 0 0 0 0 0 0 1 1 1 x
0 0 0 1 0 0 0 0 x x x
0 0 0 1 0 0 0 1 0 0 x
0 0 0 0 0 0 0 0 0 0 x
0 0 0 0 0 0 0 1 0 0 x
0 0 0 0 0 0 0 0 0 0 x
0 0 0 0 0 0 0 1 0 0 x
0 0 0 0 0 0 0 0 0 0 x
0 0 0 0 0 0 0 1 0 0 x
0 0 0 0 0 0 0 0 0 0 x
0 0 0 0 0 0 0 1 0 0 x
0 0 0 0 0 0 0 0 0 0 x
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*/

/* Test case 03_P02T01:
M N progIN reset progLoad start result clk valid done output
0 0 0 0 0 0 0 0 x x x
0 0 0 0 0 0 0 1 x x x
0 0 0 1 0 0 0 0 x x x
0 0 0 1 0 0 0 1 0 0 x
0 0 0 0 0 0 0 0 0 0 x
0 0 0 0 0 0 0 1 0 0 x
0 0 0 0 0 0 0 0 0 0 x
0 0 0 0 0 0 0 1 0 0 x
0 0 0 0 0 0 0 0 0 0 x
0 0 0 0 0 0 0 1 0 0 x
0 0 0 0 0 0 0 0 0 0 x
0 0 0 0 0 0 0 1 0 0 x
0 0 0 0 0 0 0 0 0 0 x
0 0 0 0 0 0 0 1 0 0 x
0 0 0 0 0 0 0 0 0 0 x
0 0 0 0 0 0 0 1 0 0 x
0 0 0 0 0 0 0 0 0 0 x
0 0 0 0 0 0 0 1 0 0 x
0 0 0 0 0 0 0 0 0 0 x
0 0 0 0 0 0 0 1 0 0 x
0 0 0 0 0 0 0 0 0 0 x
0 0 0 0 0 0 0 1 0 0 x
0 0 0 0 0 0 0 0 0 0 x
0 0 0 0 0 0 0 1 0 0 x
0 0 0 0 0 0 0 0 0 0 x
0 0 0 0 0 0 0 1 0 0 x
0 0 0 0 0 0 0 0 0 0 x
0 0 0 0 0 0 0 1 0 0 x
0 0 0 0 0 0 0 0 0 0 x
0 0 0 0 0 0 0 1 0 0 x
0 0 0 0 0 0 0 0 0 0 x
0 0 0 0 0 0 0 1 0 0 x
0 0 0 0 0 0 0 0 0 0 x
0 0 0 0 0 0 0 1 0 0 x
0 0 0 0 0 0 0 0 0 0 x
0 0 0 0 0 0 0 1 0 0 x
0 0 0 0 0 0 0 0 0 0 x
0 0 0 0 0 0 0 1 0 0 x
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*/

/* Test case 04_P03T01:
M N progIN reset progLoad start result clk valid done output
0 0 0 0 0 0 0 0 x x x
0 0 0 0 0 0 0 1 x x x
0 0 0 1 0 0 0 0 x x x
0 0 0 1 0 0 0 1 0 0 x
0 0 0 0 0 0 0 0 0 0 x
0 0 0 0 0 0 0 1 0 0 x
0 0 0 0 0 0 0 0 0 0 x
0 0 0 0 0 0 0 1 0 0 x
0 0 0 0 0 0 0 0 0 0 x
0 0 0 0 0 0 0 1 0 0 x
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*/

/* Test case 05_P04T01:
M N progIN reset progLoad start result clk valid done output
0 0 0 0 0 0 0 0 x x x
0 0 0 0 0 0 0 1 x x x
0 0 0 1 0 0 0 0 x x x
0 0 0 1 0 0 0 1 0 0 x
0 0 0 0 0 0 0 0 0 0 x
0 0 0 0 0 0 0 1 0 0 x
0 0 0 0 0 0 0 0 0 0 x
0 0 0 0 0 0 0 1 0 0 x
0 0 0 0 0 0 0 0 0 0 x
0 0 0 0 0 0 0 1 0 0 x
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*/

/* Test case 06_P05T01:
M N progIN reset progLoad start result clk valid done output
0 0 0 0 0 0 0 0 x x x
0 0 0 0 0 0 0 1 x x x
0 0 0 1 0 0 0 0 x x x
0 0 0 1 0 0 0 1 0 0 x
0 0 0 0 0 0 0 0 0 0 x
0 0 0 0 0 0 0 1 0 0 x
0 0 0 0 0 0 0 0 0 0 x
0 0 0 0 0 0 0 1 0 0 x
0 0 0 0 0 0 0 0 0 0 x
0 0 0 0 0 0 0 1 0 0 x
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*/
