// Digital circuit TEMPLETE Main.dig as structural Verilog
module TEMPLETE_Main (
  input  [7:0] M,
  input  [7:0] N,
  input  [12:0] progIN,
  input  reset,
  input  progLoad,
  input  start,
  input  result,
  input  clk,
  output valid,
  output done,
  output [7:0] \output ,
  output [12:0] out_12
);

  wire _00, _000, _00000, _00001, _001, _01, _00010, _010, _10, _00011, _011, _11, _00100, _100, _00101,
       _101, _00110, _110, _00111, _111, _01000, _01001, _01010, _01011, _01100, _01101, _01110, _01111,
       _10000, _10001, _10010, _10011, _10100, _10101, _10110, _10111, _11000, _11001, _11010, _11011,
       _11100, _11101, _11110, _11111, and_2_out, and_3_out, and_4_out, and_5_out, and_6_out, and_7_out,
       and_9_out, and_10_out, and_11_out, and_12_out, d_ff_1_nq, d_ff_2_q, d_ff_3_q, enA, enB, enC, eq, eq_t,
       gr, gt, jump, le, lt, multiplexer_6_out, multiplexer_10_out, multiplexer_11_out, multiplexer_12_out,
       multiplexer_13_out, multiplexer_14_out, multiplexer_15_out, multiplexer_16_out, not_2_out, not_3_out,
       not_4_out, not_5_out, or_1_out, or_2_out, or_4_out, or_5_out, or_6_out, or_11_out, or_12_out,
       or_13_out, or_15_out, or_16_out, P_a, P_b, Q_a, Q_b, Q_c, r_cnt_eq_16, r_cnt_gt_16, r_cnt_lt_16,
       result_cnt_eq_16, result_cnt_gt_16, result_cnt_lt_16, rom_1_d, start_t;
  wire [4:0] bitcount_1_out;
  wire [7:0] A, A_B, A_lt__lt_B, accA, accB, AND, cnt, DIFF, DIV, MOD, MUL, multiplexer_1_out,
       multiplexer_2_out, multiplexer_3_out, multiplexer_5_out, multiplexer_7_out, multiplexer_8_out,
       multiplexer_9_out, OR, pc, pRAM_operand, r_cnt, regC, result_cnt, rRAM_operand, SUM, val, XOR;
  wire [12:8] pRAM_d1;

  Multiplexer #(.Bits(8)) multiplexer_1 (.sel(jump), .in_0({8{1'b0}}), .in_1(out_12[7:0]), .out(multiplexer_1_out));
  or or_1 (or_1_out, _00, result);
  CounterPreset #(.maxValue(256), .Bits(8)) u_cnt (
    .en(progLoad), .C(clk), .dir(1'b0), .in({8{1'b0}}), .ld(1'b0), .clr(_010), .out(cnt));  // open: ovf
  CounterPreset #(.maxValue(256), .Bits(8)) u_r_cnt (
    .en(_011), .C(clk), .dir(1'b0), .in({8{1'b0}}), .ld(1'b0), .clr(r_cnt_eq_16), .out(r_cnt));  // open: ovf
  Comparator #(.Bits(8)) u_r_cnt_eq_16 (.a(r_cnt), .b(8'h10), .gt(r_cnt_gt_16), .eq(r_cnt_eq_16), .lt(r_cnt_lt_16));
  CounterPreset #(.maxValue(256), .Bits(8)) u_pc (
    .en(_100), .C(clk), .dir(1'b0), .in(multiplexer_1_out), .ld(jump), .clr(or_2_out), .out(pc));  // open: ovf
  or or_2 (or_2_out, start, reset, _11111);
  Counter #(.Bits(8)) u_result_cnt (.en(_01), .C(clk), .clr(or_1_out), .out(result_cnt));  // open: ovf
  Comparator #(.Bits(8)) comparator_1 (
    .a(result_cnt), .b(8'h10), .gt(result_cnt_gt_16), .eq(result_cnt_eq_16), .lt(result_cnt_lt_16));
  D_FF d_ff_1 (.D(start), .C(clk), .nQ(d_ff_1_nq));  // open: Q
  Multiplexer #(.Bits(8)) multiplexer_2 (.sel(_01001), .in_0(cnt), .in_1(out_12[7:0]), .out(multiplexer_2_out));
  Multiplexer #(.Selector_Bits(2), .Bits(8)) multiplexer_3 (
    .sel({_01011, _01010}), .in_0(r_cnt), .in_1(out_12[7:0]), .in_2(out_12[7:0]), .in_3({8{1'b0}}),
    .out(multiplexer_3_out));
  Multiplexer #(.Selector_Bits(5), .Bits(8)) multiplexer_4 (
    .sel(out_12[12:8]), .in_0({8{1'b0}}), .in_1(out_12[7:0]), .in_2(out_12[7:0]), .in_3(accB), .in_4(accA),
    .in_5(accA), .in_6(regC), .in_7(M), .in_8(N), .in_9(pRAM_operand), .in_10(rRAM_operand), .in_11(accA),
    .in_12({8{1'b0}}), .in_13({8{1'b0}}), .in_14({8{1'b0}}), .in_15({8{1'b0}}), .in_16({8{1'b0}}),
    .in_17(SUM), .in_18(DIFF), .in_19(MUL), .in_20(DIV), .in_21(MOD), .in_22(A_B), .in_23({8{1'b0}}),
    .in_24(A), .in_25(AND), .in_26(OR), .in_27(XOR), .in_28(A_lt__lt_B), .in_29({8{1'b0}}),
    .in_30({8{1'b0}}), .in_31({8{1'b0}}), .out(val));
  D_FF d_ff_2 (.D(start), .C(clk), .Q(d_ff_2_q));  // open: nQ
  D_FF d_ff_3 (.D(d_ff_1_nq), .C(clk), .Q(d_ff_3_q));  // open: nQ
  or or_3 (done, result_cnt_eq_16, _10);
  RAMDualAccess #(.AddrBits(8), .Bits(13)) pRAM (
    .str(progLoad), .C(clk), .ld(_01001), .A1(multiplexer_2_out), .Din1(progIN), .A2(pc),
    .D1({pRAM_d1, pRAM_operand}), .D2(out_12));
  or or_4 (or_4_out, _01011, _011);
  and and_1 (start_t, d_ff_2_q, d_ff_3_q);
  JK_FF jk_ff_1 (.J(_11111), .C(clk), .K(reset), .Q(valid));  // open: nQ
  Multiplexer #(.Bits(8)) multiplexer_5 (.sel(_01011), .in_0({8{1'b0}}), .in_1(val), .out(multiplexer_5_out));
  RAMDualAccess #(.AddrBits(8), .Bits(8)) rRAM (
    .str(or_4_out), .C(clk), .ld(_01010), .A1(multiplexer_3_out), .Din1(multiplexer_5_out), .A2(result_cnt),
    .D1(rRAM_operand), .D2(\output ));
  or or_5 (or_5_out, eq_t, gr);
  BitCount #(.Bits(16)) bitcount_1 (
    .in({_11100, _11011, _11010, _11001, _11000, _10110, _10101, _10100, _10011, _10010, _10001, _01010, _01001, _00110, _00011, _00001}),
    .out(bitcount_1_out));
  and and_2 (and_2_out, _01101, eq_t);
  and and_3 (and_3_out, _01110, gr);
  and and_4 (and_4_out, _01111, le);
  and and_5 (and_5_out, _10000, or_5_out);
  Multiplexer multiplexer_6 (.sel(_10111), .in_0(1'b0), .in_1(lt), .out(multiplexer_6_out));
  or or_6 (or_6_out, start, _10111);
  Comparator #(.Signed("true"), .Bits(8)) comparator_2 (.a(accA), .b(accB), .gt(gt), .eq(eq), .lt(lt));
  Register register_1 (.D(multiplexer_6_out), .C(clk), .en(or_6_out), .Q(le));
  or or_7 (enA, bitcount_1_out[0], reset);
  or or_8 (enB, reset, _00010, _00100);
  or or_9 (enC, reset, _00101, _00111, _01000);
  or or_10 (jump, _01100, and_2_out, and_3_out, and_4_out, and_5_out);
  Seven_Seg_Hex seven_seg_hex_1 (.d(\output [7:4]), .dp(1'b0));
  or or_11 (or_11_out, start, _10111, _11101);
  Seven_Seg_Hex seven_seg_hex_2 (.d(\output [3:0]), .dp(1'b0));
  Multiplexer #(.Bits(8)) multiplexer_7 (.sel(reset), .in_0(val), .in_1({8{1'b0}}), .out(multiplexer_7_out));
  Multiplexer #(.Bits(8)) multiplexer_8 (.sel(reset), .in_0(val), .in_1({8{1'b0}}), .out(multiplexer_8_out));
  Multiplexer #(.Bits(8)) multiplexer_9 (.sel(reset), .in_0(val), .in_1({8{1'b0}}), .out(multiplexer_9_out));
  Multiplexer multiplexer_10 (.sel(start), .in_0(or_12_out), .in_1(1'b0), .out(multiplexer_10_out));
  Register register_2 (.D(multiplexer_10_out), .C(clk), .en(or_11_out), .Q(eq_t));
  Register #(.Bits(8)) u_accA (.D(multiplexer_7_out), .C(clk), .en(enA), .Q(accA));
  Register #(.Bits(8)) u_accB (.D(multiplexer_8_out), .C(clk), .en(enB), .Q(accB));
  Register #(.Bits(8)) u_regC (.D(multiplexer_9_out), .C(clk), .en(enC), .Q(regC));
  or or_12 (or_12_out, and_7_out, and_6_out);
  and and_6 (and_6_out, _11101, rom_1_d);
  and and_7 (and_7_out, eq, _10111);
  ROM #(.AddrBits(8)) rom_1 (.A(accA), .sel(1'b1), .D(rom_1_d));
  Multiplexer multiplexer_11 (.sel(_10111), .in_0(1'b0), .in_1(gt), .out(multiplexer_11_out));
  or or_13 (or_13_out, start, _10111);
  Register register_3 (.D(multiplexer_11_out), .C(clk), .en(or_13_out), .Q(gr));
  assign AND = accA & accB;  // And and_8, 8 bits wide
  assign OR = accA | accB;  // Or or_14, 8 bits wide
  assign XOR = accA ^ accB;  // XOr xor_1, 8 bits wide
  Add #(.Bits(8)) add_1 (.a(accA), .b(accB), .c_i(1'b0), .s(SUM));  // open: c_o
  Sub #(.Bits(8)) sub_1 (.a(accA), .b(accB), .c_i(1'b0), .s(DIFF));  // open: c_o
  Mul #(.Bits(4)) mul_1 (.a(accA[3:0]), .b(accB[3:0]), .mul(MUL));
  Div #(.Bits(8)) divide (.a(accA), .b(accB), .q(DIV), .r(MOD));
  assign A = ~accA;  // Not not_1, 8 bits wide
  BarrelShifter #(.Bits(8), .barrelShifterMode("arithmetic")) barrelshifter_1 (
    .in(accA), .shift({1'b0, accB[2:0]}), .out(A_lt__lt_B));
  LookUpTable #(.Bits(8)) exponent (
    .in0(accB[0]), .in1(accB[1]), .in2(accB[2]), .in3(accA[0]), .in4(accA[1]), .in5(accA[2]), .out(A_B));
  Multiplexer #(.Selector_Bits(3)) multiplexer_12 (
    .sel({Q_a, Q_b, Q_c}), .in_0(start_t), .in_1(1'b0), .in_2(1'b0), .in_3(1'b0), .in_4(1'b1),
    .in_5(not_2_out), .in_6(1'b0), .in_7(1'b0), .out(multiplexer_12_out));
  not not_2 (not_2_out, reset);
  or or_15 (or_15_out, start, progLoad, reset);
  and and_9 (and_9_out, ~reset, ~result);  // And
  or or_16 (or_16_out, start, progLoad, reset);
  not not_3 (not_3_out, result_cnt_eq_16);
  D_FF d_ff_4 (.D(multiplexer_12_out), .C(clk), .Q(Q_a));  // open: nQ
  Multiplexer #(.Selector_Bits(2)) multiplexer_13 (
    .sel({P_a, P_b}), .in_0(1'b0), .in_1(result_cnt_eq_16), .in_2(and_9_out), .in_3(1'b0),
    .out(multiplexer_13_out));
  Multiplexer #(.Selector_Bits(2)) multiplexer_14 (
    .sel({P_a, P_b}), .in_0(result), .in_1(not_3_out), .in_2(result), .in_3(1'b0), .out(multiplexer_14_out));
  and and_10 (and_10_out, ~or_15_out, multiplexer_13_out);  // And
  and and_11 (and_11_out, ~or_16_out, multiplexer_14_out);  // And
  not not_4 (not_4_out, r_cnt_eq_16);
  D_FF d_ff_5 (.D(and_10_out), .C(clk), .Q(P_a));  // open: nQ
  D_FF d_ff_6 (.D(and_11_out), .C(clk), .Q(P_b));  // open: nQ
  Multiplexer #(.Selector_Bits(3)) multiplexer_15 (
    .sel({Q_a, Q_b, Q_c}), .in_0(reset), .in_1(1'b0), .in_2(1'b1), .in_3(not_4_out), .in_4(1'b0),
    .in_5(reset), .in_6(1'b0), .in_7(1'b0), .out(multiplexer_15_out));
  D_FF d_ff_7 (.D(multiplexer_15_out), .C(clk), .Q(Q_b));  // open: nQ
  Decoder #(.Selector_Bits(2)) decoder_1 (.sel({P_a, P_b}), .out_0(_00), .out_1(_01), .out_2(_10), .out_3(_11));
  and and_12 (and_12_out, ~start_t, ~reset);  // And
  not not_5 (not_5_out, r_cnt_eq_16);
  Multiplexer #(.Selector_Bits(3)) multiplexer_16 (
    .sel({Q_a, Q_b, Q_c}), .in_0(progLoad), .in_1(progLoad), .in_2(1'b1), .in_3(not_5_out), .in_4(_11111),
    .in_5(and_12_out), .in_6(1'b0), .in_7(1'b0), .out(multiplexer_16_out));
  D_FF d_ff_8 (.D(multiplexer_16_out), .C(clk), .Q(Q_c));  // open: nQ
  Decoder #(.Selector_Bits(3)) decoder_2 (
    .sel({Q_a, Q_b, Q_c}), .out_0(_000), .out_1(_001), .out_2(_010), .out_3(_011), .out_4(_100),
    .out_5(_101), .out_6(_110), .out_7(_111));
  Demultiplexer #(.Selector_Bits(5)) demultiplexer_1 (
    .sel(out_12[12:8]), .in(_100), .out_0(_00000), .out_1(_00001), .out_2(_00010), .out_3(_00011),
    .out_4(_00100), .out_5(_00101), .out_6(_00110), .out_7(_00111), .out_8(_01000), .out_9(_01001),
    .out_10(_01010), .out_11(_01011), .out_12(_01100), .out_13(_01101), .out_14(_01110), .out_15(_01111),
    .out_16(_10000), .out_17(_10001), .out_18(_10010), .out_19(_10011), .out_20(_10100), .out_21(_10101),
    .out_22(_10110), .out_23(_10111), .out_24(_11000), .out_25(_11001), .out_26(_11010), .out_27(_11011),
    .out_28(_11100), .out_29(_11101), .out_30(_11110), .out_31(_11111));

  // Other names for the same wires on the sheet: en_rRAM = _01011; operand[7:0] = out_12[7:0];
  //   opcode[4:0] = out_12[12:8]

  // Notes on the sheet:
  //   contents of rom_1 (hex, n*v repeats v):
  //   0,0,1,1,0,1,0,1,0,0,0,1,0,1,0,0,0,1,0,1,0,0,0,1,5*0,1,0,1,5*0
  //   ,1,0,0,0,1,0,1,0,0,0,1,5*0,1,5*0,1,0,1,5*0,1,0,0,0,1,0,1,5*0,1
  //   ,0,0,0,1,5*0,1,7*0,1,0,0,0,1,0,1,0,0,0,1,0,1,0,0,0,1,13*0,1,0,0,0
  //   ,1,5*0,1,0,1,9*0,1,0,1,5*0,1,5*0,1,0,0,0,1,5*0,1,5*0,1,0,1,9*0
  //   ,1,0,1,0,0,0,1,0,1,11*0,1,11*0,1,0,0,0,1,0,1,0,0,0,1,5*0,1,0,1
  //   ,9*0,1
  //   contents of exponent (hex, n*v repeats v):
  //   1,0,a0000,a00000,0,40000,0,0,9*1,2,4,8,10,20,40,80,1,3,9,1b,51
  //   ,f3,d9,8b,1,4,10,40,4*0,1,5,19,7d,71,35,9,2d,1,6,24,d8,10,60,40
  //   ,80,1,7,31,57,61,a7,91,f7,0,0,0,1,0,0,0,1,0,1,5*0,1,0,0,0,1,5*0
  //   ,1,7*0,1,0,0,0,1,0,1,0,0,0,1,0,1,0,0,0,1,13*0,1,0,0,0,1,5*0,1
  //   ,0,1,9*0,1,0,1,5*0,1,5*0,1,0,0,0,1,5*0,1,5*0,1,0,1,9*0,1,0,1,0,0,0
  //   ,1,0,1,11*0,1,11*0,1,0,0,0,1,0,1,0,0,0,1,5*0,1,0,1,9*0,1
endmodule

/* Test case Almostin1:
M N progIN reset progLoad start result clk valid done output
0 0 0 0 0 0 0 0 x x x
0 0 0 0 0 0 0 1 x x x
0 0 0b0000100000111 0 1 0 0 0 0 0 x
0 0 0b0000100000111 0 1 0 0 1 0 0 x
0 0 0b0001000000100 0 1 0 0 0 0 0 x
0 0 0b0001000000100 0 1 0 0 1 0 0 x
0 0 0b0000000000100 0 1 0 0 0 0 0 x
0 0 0b0000000000100 0 1 0 0 1 0 0 x
0 0 0b0010000000000 0 1 0 0 0 0 0 x
0 0 0b0010000000000 0 1 0 0 1 0 0 x
0 0 0b0100100000010 0 1 0 0 0 0 0 x
0 0 0b0100100000010 0 1 0 0 1 0 0 x
0 0 0b0010100000000 0 1 0 0 0 0 0 x
0 0 0b0010100000000 0 1 0 0 1 0 0 x
0 0 0b1000100000000 0 1 0 0 0 0 0 x
0 0 0b1000100000000 0 1 0 0 1 0 0 x
0 0 0b0101100000000 0 1 0 0 0 0 0 x
0 0 0b0101100000000 0 1 0 0 1 0 0 x
0 0 0b0011000000111 0 1 0 0 0 0 0 x
0 0 0b0011000000111 0 1 0 0 1 0 0 x
0 0 0b1001000000000 0 1 0 0 0 0 0 x
0 0 0b1001000000000 0 1 0 0 1 0 0 x
0 0 0b0101100000001 0 1 0 0 0 0 0 x
0 0 0b0101100000001 0 1 0 0 1 0 0 x
0 0 0b0011000000111 0 1 0 0 0 0 0 x
0 0 0b0011000000111 0 1 0 0 1 0 0 x
0 0 0b1001100000000 0 1 0 0 0 0 0 x
0 0 0b1001100000000 0 1 0 0 1 0 0 x
0 0 0b0101100000010 0 1 0 0 0 0 0 x
0 0 0b0101100000010 0 1 0 0 1 0 0 x
0 0 0b0011000000111 0 1 0 0 0 0 0 x
0 0 0b0011000000111 0 1 0 0 1 0 0 x
0 0 0b1010000000000 0 1 0 0 0 0 0 x
0 0 0b1010000000000 0 1 0 0 1 0 0 x
0 0 0b0101100000011 0 1 0 0 0 0 0 x
0 0 0b0101100000011 0 1 0 0 1 0 0 x
0 0 0b0011000000111 0 1 0 0 0 0 0 x
0 0 0b0011000000111 0 1 0 0 1 0 0 x
0 0 0b1010100000000 0 1 0 0 0 0 0 x
0 0 0b1010100000000 0 1 0 0 1 0 0 x
0 0 0b0101100000100 0 1 0 0 0 0 0 x
0 0 0b0101100000100 0 1 0 0 1 0 0 x
0 0 0b0011000000111 0 1 0 0 0 0 0 x
0 0 0b0011000000111 0 1 0 0 1 0 0 x
0 0 0b1011000000000 0 1 0 0 0 0 0 x
0 0 0b1011000000000 0 1 0 0 1 0 0 x
0 0 0b0101100000101 0 1 0 0 0 0 0 x
0 0 0b0101100000101 0 1 0 0 1 0 0 x
0 0 0b0011000000111 0 1 0 0 0 0 0 x
0 0 0b0011000000111 0 1 0 0 1 0 0 x
0 0 0b1100000000000 0 1 0 0 0 0 0 x
0 0 0b1100000000000 0 1 0 0 1 0 0 x
0 0 0b0101100000110 0 1 0 0 0 0 0 x
0 0 0b0101100000110 0 1 0 0 1 0 0 x
0 0 0b0011000000111 0 1 0 0 0 0 0 x
0 0 0b0011000000111 0 1 0 0 1 0 0 x
0 0 0b1100100000000 0 1 0 0 0 0 0 x
0 0 0b1100100000000 0 1 0 0 1 0 0 x
0 0 0b0101100000111 0 1 0 0 0 0 0 x
0 0 0b0101100000111 0 1 0 0 1 0 0 x
0 0 0b0011000000111 0 1 0 0 0 0 0 x
0 0 0b0011000000111 0 1 0 0 1 0 0 x
0 0 0b1101000000000 0 1 0 0 0 0 0 x
0 0 0b1101000000000 0 1 0 0 1 0 0 x
0 0 0b0101100001000 0 1 0 0 0 0 0 x
0 0 0b0101100001000 0 1 0 0 1 0 0 x
0 0 0b0011000000111 0 1 0 0 0 0 0 x
0 0 0b0011000000111 0 1 0 0 1 0 0 x
0 0 0b1101100000000 0 1 0 0 0 0 0 x
0 0 0b1101100000000 0 1 0 0 1 0 0 x
0 0 0b0101100001001 0 1 0 0 0 0 0 x
0 0 0b0101100001001 0 1 0 0 1 0 0 x
0 0 0b0011000000111 0 1 0 0 0 0 0 x
0 0 0b0011000000111 0 1 0 0 1 0 0 x
0 0 0b1110000000000 0 1 0 0 0 0 0 x
0 0 0b1110000000000 0 1 0 0 1 0 0 x
0 0 0b0101100001010 0 1 0 0 0 0 0 x
0 0 0b0101100001010 0 1 0 0 1 0 0 x
0 0 0b0011000000111 0 1 0 0 0 0 0 x
0 0 0b0011000000111 0 1 0 0 1 0 0 x
0 0 0b1111100000000 0 1 0 0 0 0 0 x
0 0 0b1111100000000 0 1 0 0 1 0 0 x
0 0 0 0 0 1 0 0 0 0 x
0 0 0 0 0 1 0 1 0 0 x
1 1 0 0 0 0 0 0 x x x
1 1 0 0 0 0 0 1 x x x
1 1 0 0 0 0 0 0 x x x
1 1 0 0 0 0 0 1 x x x
1 1 0 0 0 0 0 0 x x x
1 1 0 0 0 0 0 1 x x x
1 1 0 0 0 0 0 0 x x x
1 1 0 0 0 0 0 1 x x x
1 1 0 0 0 0 0 0 x x x
1 1 0 0 0 0 0 1 x x x
1 1 0 0 0 0 0 0 x x x
1 1 0 0 0 0 0 1 x x x
1 1 0 0 0 0 0 0 x x x
1 1 0 0 0 0 0 1 x x x
1 1 0 0 0 0 0 0 x x x
1 1 0 0 0 0 0 1 x x x
1 1 0 0 0 0 0 0 x x x
1 1 0 0 0 0 0 1 x x x
1 1 0 0 0 0 0 0 x x x
1 1 0 0 0 0 0 1 x x x
1 1 0 0 0 0 0 0 x x x
1 1 0 0 0 0 0 1 x x x
1 1 0 0 0 0 0 0 x x x
1 1 0 0 0 0 0 1 x x x
1 1 0 0 0 0 0 0 x x x
1 1 0 0 0 0 0 1 x x x
1 1 0 0 0 0 0 0 x x x
1 1 0 0 0 0 0 1 x x x
1 1 0 0 0 0 0 0 x x x
1 1 0 0 0 0 0 1 x x x
1 1 0 0 0 0 0 0 x x x
1 1 0 0 0 0 0 1 x x x
1 1 0 0 0 0 0 0 x x x
1 1 0 0 0 0 0 1 x x x
1 1 0 0 0 0 0 0 x x x
1 1 0 0 0 0 0 1 x x x
1 1 0 0 0 0 0 0 x x x
1 1 0 0 0 0 0 1 x x x
1 1 0 0 0 0 0 0 x x x
1 1 0 0 0 0 0 1 x x x
1 1 0 0 0 0 0 0 x x x
1 1 0 0 0 0 0 1 x x x
1 1 0 0 0 0 0 0 x x x
1 1 0 0 0 0 0 1 x x x
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*/

/* Test case 01_P01T01:
M N progIN reset progLoad start result clk valid done output
0 0 0 0 0 0 0 0 x x x
0 0 0 0 0 0 0 1 x x x
0 0 0 1 0 0 0 0 x x x
0 0 0 1 0 0 0 1 0 0 x
0 0 0 0 0 0 0 0 0 0 x
0 0 0 0 0 0 0 1 0 0 x
0 0 0 0 0 0 0 0 0 0 x
0 0 0 0 0 0 0 1 0 0 x
0 0 0 0 0 0 0 0 0 0 x
0 0 0 0 0 0 0 1 0 0 x
0 0 0 0 0 0 0 0 0 0 x
0 0 0 0 0 0 0 1 0 0 x
0 0 0 0 0 0 0 0 0 0 x
0 0 0 0 0 0 0 1 0 0 x
0 0 0 0 0 0 0 0 0 0 x
0 0 0 0 0 0 0 1 0 0 x
0 0 0 0 0 0 0 0 0 0 x
0 0 0 0 0 0 0 1 0 0 x
0 0 0 0 0 0 0 0 0 0 x
0 0 0 0 0 0 0 1 0 0 x
0 0 0 0 0 0 0 0 0 0 x
0 0 0 0 0 0 0 1 0 0 x
0 0 0 0 0 0 0 0 0 0 x
0 0 0 0 0 0 0 1 0 0 x
0 0 0 0 0 0 0 0 0 0 x
0 0 0 0 0 0 0 1 0 0 x
0 0 0 0 0 0 0 0 0 0 x
0 0 0 0 0 0 0 1 0 0 x
0 0 0 0 0 0 0 0 0 0 x
0 0 0 0 0 0 0 1 0 0 x
0 0 0 0 0 0 0 0 0 0 x
0 0 0 0 0 0 0 1 0 0 x
0 0 0 0 0 0 0 0 0 0 x
0 0 0 0 0 0 0 1 0 0 x
0 0 0 0 0 0 0 0 0 0 x
0 0 0 0 0 0 0 1 0 0 x
0 0 0 0 0 0 0 0 0 0 x
0 0 0 0 0 0 0 1 0 0 x
0 0 0 0 0 0 0 0 0 0 x
0 0 0 0 0 0 0 1 0 0 x
0 0 0 0 0 0 0 0 0 0 x
0 0 0 0 0 0 0 1 0 0 x
0 0 271 0 1 0 0 0 0 0 x
0 0 271 0 1 0 0 1 0 0 x
0 0 565 0 1 0 0 0 0 0 x
0 0 565 0 1 0 0 1 0 0 x
0 0 4352 0 1 0 0 0 0 0 x
0 0 4352 0 1 0 0 1 0 0 x
0 0 2819 0 1 0 0 0 0 0 x
0 0 2819 0 1 0 0 1 0 0 x
0 0 7936 0 1 0 0 0 0 0 x
0 0 7936 0 1 0 0 1 0 0 x
0 0 0 0 0 1 0 0 0 0 x
0 0 0 0 0 1 0 1 0 0 x
0 0 0 0 0 0 0 0 x 0 x
0 0 0 0 0 0 0 1 x 0 x
0 0 0 0 0 0 0 0 x 0 x
0 0 0 0 0 0 0 1 x 0 x
0 0 0 0 0 0 0 0 x 0 x
0 0 0 0 0 0 0 1 x 0 x
0 0 0 0 0 0 0 0 x 0 x
0 0 0 0 0 0 0 1 x 0 x
0 0 0 0 0 0 0 0 x 0 x
0 0 0 0 0 0 0 1 x 0 x
0 0 0 0 0 0 0 0 x 0 x
0 0 0 0 0 0 0 1 x 0 x
0 0 0 0 0 0 0 0 x 0 x
0 0 0 0 0 0 0 1 x 0 x
0 0 0 0 0 0 0 0 x 0 x
0 0 0 0 0 0 0 1 x 0 x
0 0 0 0 0 0 0 0 x 0 x
0 0 0 0 0 0 0 1 x 0 x
0 0 0 0 0 0 0 0 x 0 x
0 0 0 0 0 0 0 1 x 0 x
0 0 0 0 0 0 0 0 x 0 x
0 0 0 0 0 0 0 1 x 0 x
0 0 0 0 0 0 0 0 x 0 x
0 0 0 0 0 0 0 1 x 0 x
0 0 0 0 0 0 0 0 x 0 x
0 0 0 0 0 0 0 1 x 0 x
0 0 0 0 0 0 0 0 x 0 x
0 0 0 0 0 0 0 1 x 0 x
0 0 0 0 0 0 0 0 x 0 x
0 0 0 0 0 0 0 1 x 0 x
0 0 0 0 0 0 0 0 x 0 x
0 0 0 0 0 0 0 1 x 0 x
0 0 0 0 0 0 0 0 x 0 x
0 0 0 0 0 0 0 1 x 0 x
0 0 0 0 0 0 0 0 x 0 x
0 0 0 0 0 0 0 1 x 0 x
0 0 0 0 0 0 0 0 x 0 x
0 0 0 0 0 0 0 1 x 0 x
0 0 0 0 0 0 0 0 x 0 x
0 0 0 0 0 0 0 1 x 0 x
0 0 0 0 0 0 0 0 x 0 x
0 0 0 0 0 0 0 1 x 0 x
0 0 0 0 0 0 0 0 x 0 x
0 0 0 0 0 0 0 1 x 0 x
0 0 0 0 0 0 0 0 x 0 x
0 0 0 0 0 0 0 1 x 0 x
0 0 0 0 0 0 0 0 x 0 x
0 0 0 0 0 0 0 1 x 0 x
0 0 0 0 0 0 0 0 x 0 x
0 0 0 0 0 0 0 1 x 0 x
0 0 0 0 0 0 0 0 x 0 x
0 0 0 0 0 0 0 1 1 0 x
0 0 0 0 0 0 1 0 1 0 x
0 0 0 0 0 0 1 1 1 0 0
0 0 0 0 0 0 0 0 1 0 0
0 0 0 0 0 0 0 1 1 0 0
0 0 0 0 0 0 0 0 1 0 0
0 0 0 0 0 0 0 1 1 0 0
0 0 0 0 0 0 0 0 1 0 0
0 0 0 0 0 0 0 1 1 0 68
0 0 0 0 0 0 0 0 1 0 68
0 0 0 0 0 0 0 1 1 0 0
0 0 0 0 0 0 0 0 1 0 0
0 0 0 0 0 0 0 1 1 0 0
0 0 0 0 0 0 0 0 1 0 0
0 0 0 0 0 0 0 1 1 0 0
0 0 0 0 0 0 0 0 1 0 0
0 0 0 0 0 0 0 1 1 0 0
0 0 0 0 0 0 0 0 1 0 0
0 0 0 0 0 0 0 1 1 0 0
0 0 0 0 0 0 0 0 1 0 0
0 0 0 0 0 0 0 1 1 0 0
0 0 0 0 0 0 0 0 1 0 0
0 0 0 0 0 0 0 1 1 0 0
0 0 0 0 0 0 0 0 1 0 0
0 0 0 0 0 0 0 1 1 0 0
0 0 0 0 0 0 0 0 1 0 0
0 0 0 0 0 0 0 1 1 0 0
0 0 0 0 0 0 0 0 1 0 0
0 0 0 0 0 0 0 1 1 0 0
0 0 0 0 0 0 0 0 1 0 0
0 0 0 0 0 0 0 1 1 0 0
0 0 0 0 0 0 0 0 1 0 0
0 0 0 0 0 0 0 1 1 0 0
0 0 0 0 0 0 0 0 1 0 0
0 0 0 0 0 0 0 1 1 1 x
0 0 0 0 0 0 0 0 1 1 x
0 0 0 0 0 0 0 1 1 1 x
0 0 0 0 0 0 0 0 1 1 x
*/

/* Test case 01_P01T2:
M N progIN reset progLoad start result clk valid done output
0 0 0 0 0 0 0 0 x x x
0 0 0 0 0 0 0 1 x x x
0 0 0 1 0 0 0 0 x x x
0 0 0 1 0 0 0 1 0 0 x
0 0 0 0 0 0 0 0 0 0 x
0 0 0 0 0 0 0 1 0 0 x
0 0 0 0 0 0 0 0 0 0 x
0 0 0 0 0 0 0 1 0 0 x
0 0 0 0 0 0 0 0 0 0 x
0 0 0 0 0 0 0 1 0 0 x
0 0 0 0 0 0 0 0 0 0 x
0 0 0 0 0 0 0 1 0 0 x
0 0 0 0 0 0 0 0 0 0 x
0 0 0 0 0 0 0 1 0 0 x
0 0 0 0 0 0 0 0 0 0 x
0 0 0 0 0 0 0 1 0 0 x
0 0 0 0 0 0 0 0 0 0 x
0 0 0 0 0 0 0 1 0 0 x
0 0 0 0 0 0 0 0 0 0 x
0 0 0 0 0 0 0 1 0 0 x
0 0 0 0 0 0 0 0 0 0 x
0 0 0 0 0 0 0 1 0 0 x
0 0 0 0 0 0 0 0 0 0 x
0 0 0 0 0 0 0 1 0 0 x
0 0 0 0 0 0 0 0 0 0 x
0 0 0 0 0 0 0 1 0 0 x
0 0 0 0 0 0 0 0 0 0 x
0 0 0 0 0 0 0 1 0 0 x
0 0 0 0 0 0 0 0 0 0 x
0 0 0 0 0 0 0 1 0 0 x
0 0 0 0 0 0 0 0 0 0 x
0 0 0 0 0 0 0 1 0 0 x
0 0 0 0 0 0 0 0 0 0 x
0 0 0 0 0 0 0 1 0 0 x
0 0 0 0 0 0 0 0 0 0 x
0 0 0 0 0 0 0 1 0 0 x
0 0 0 0 0 0 0 0 0 0 x
0 0 0 0 0 0 0 1 0 0 x
0 0 0 0 0 0 0 0 0 0 x
0 0 0 0 0 0 0 1 0 0 x
0 0 0 0 0 0 0 0 0 0 x
0 0 0 0 0 0 0 1 0 0 x
0 0 271 0 1 0 0 0 0 0 x
0 0 271 0 1 0 0 1 0 0 x
0 0 565 0 1 0 0 0 0 0 x
0 0 565 0 1 0 0 1 0 0 x
0 0 4352 0 1 0 0 0 0 0 x
0 0 4352 0 1 0 0 1 0 0 x
0 0 2819 0 1 0 0 0 0 0 x
0 0 2819 0 1 0 0 1 0 0 x
0 0 7936 0 1 0 0 0 0 0 x
0 0 7936 0 1 0 0 1 0 0 x
0 0 0 0 0 1 0 0 0 0 x
0 0 0 0 0 1 0 1 0 0 x
0 0 0 0 0 0 0 0 x 0 x
0 0 0 0 0 0 0 1 x 0 x
0 0 0 0 0 0 0 0 x 0 x
0 0 0 0 0 0 0 1 x 0 x
0 0 0 0 0 0 0 0 x 0 x
0 0 0 0 0 0 0 1 x 0 x
0 0 0 0 0 0 0 0 x 0 x
0 0 0 0 0 0 0 1 x 0 x
0 0 0 0 0 0 0 0 x 0 x
0 0 0 0 0 0 0 1 x 0 x
0 0 0 0 0 0 0 0 x 0 x
0 0 0 0 0 0 0 1 x 0 x
0 0 0 0 0 0 0 0 x 0 x
0 0 0 0 0 0 0 1 x 0 x
0 0 0 0 0 0 0 0 x 0 x
0 0 0 0 0 0 0 1 x 0 x
0 0 0 0 0 0 0 0 x 0 x
0 0 0 0 0 0 0 1 x 0 x
0 0 0 0 0 0 0 0 x 0 x
0 0 0 0 0 0 0 1 x 0 x
0 0 0 0 0 0 0 0 x 0 x
0 0 0 0 0 0 0 1 x 0 x
0 0 0 0 0 0 0 0 x 0 x
0 0 0 0 0 0 0 1 x 0 x
0 0 0 0 0 0 0 0 x 0 x
0 0 0 0 0 0 0 1 x 0 x
0 0 0 0 0 0 0 0 x 0 x
0 0 0 0 0 0 0 1 x 0 x
0 0 0 0 0 0 0 0 x 0 x
0 0 0 0 0 0 0 1 x 0 x
0 0 0 0 0 0 0 0 x 0 x
0 0 0 0 0 0 0 1 x 0 x
0 0 0 0 0 0 0 0 x 0 x
0 0 0 0 0 0 0 1 x 0 x
0 0 0 0 0 0 0 0 x 0 x
0 0 0 0 0 0 0 1 x 0 x
0 0 0 0 0 0 0 0 x 0 x
0 0 0 0 0 0 0 1 x 0 x
0 0 0 0 0 0 0 0 x 0 x
0 0 0 0 0 0 0 1 x 0 x
0 0 0 0 0 0 0 0 x 0 x
0 0 0 0 0 0 0 1 x 0 x
0 0 0 0 0 0 0 0 x 0 x
0 0 0 0 0 0 0 1 x 0 x
0 0 0 0 0 0 0 0 x 0 x
0 0 0 0 0 0 0 1 x 0 x
0 0 0 0 0 0 0 0 x 0 x
0 0 0 0 0 0 0 1 x 0 x
0 0 0 0 0 0 0 0 x 0 x
0 0 0 0 0 0 0 1 x 0 x
0 0 0 0 0 0 0 0 x 0 x
0 0 0 0 0 0 0 1 1 0 x
0 0 0 0 0 0 1 0 1 0 x
0 0 0 0 0 0 1 1 1 0 0
0 0 0 0 0 0 0 0 1 0 0
0 0 0 0 0 0 0 1 1 0 0
0 0 0 0 0 0 0 0 1 0 0
0 0 0 0 0 0 0 1 1 0 0
0 0 0 0 0 0 0 0 1 0 0
0 0 0 0 0 0 0 1 1 0 68
0 0 0 0 0 0 0 0 1 0 68
0 0 0 0 0 0 0 1 1 0 0
0 0 0 0 0 0 0 0 1 0 0
0 0 0 0 0 0 0 1 1 0 0
0 0 0 0 0 0 0 0 1 0 0
0 0 0 0 0 0 0 1 1 0 0
0 0 0 0 0 0 0 0 1 0 0
0 0 0 0 0 0 0 1 1 0 0
0 0 0 0 0 0 0 0 1 0 0
0 0 0 0 0 0 0 1 1 0 0
0 0 0 0 0 0 0 0 1 0 0
0 0 0 0 0 0 0 1 1 0 0
0 0 0 0 0 0 0 0 1 0 0
0 0 0 0 0 0 0 1 1 0 0
0 0 0 0 0 0 0 0 1 0 0
0 0 0 0 0 0 0 1 1 0 0
0 0 0 0 0 0 0 0 1 0 0
0 0 0 0 0 0 0 1 1 0 0
0 0 0 0 0 0 0 0 1 0 0
0 0 0 0 0 0 0 1 1 0 0
0 0 0 0 0 0 0 0 1 0 0
0 0 0 0 0 0 0 1 1 0 0
0 0 0 0 0 0 0 0 1 0 0
0 0 0 0 0 0 0 1 1 0 0
0 0 0 0 0 0 0 0 1 0 0
0 0 0 0 0 0 0 1 1 1 x
0 0 0 0 0 0 0 0 1 1 x
0 0 0 0 0 0 0 1 1 1 x
0 0 0 0 0 0 0 0 1 1 x
0 0 0 0 0 0 0 1 1 1 x
0 0 0 0 0 0 1 0 1 X x
0 0 0 0 0 0 1 1 1 X 0
0 0 0 0 0 0 0 0 1 0 0
0 0 0 0 0 0 0 1 1 0 0
0 0 0 0 0 0 0 0 1 0 0
0 0 0 0 0 0 0 1 1 0 0
0 0 0 0 0 0 0 0 1 0 0
0 0 0 0 0 0 0 1 1 0 68
0 0 0 0 0 0 0 0 1 0 68
0 0 0 0 0 0 0 1 1 0 0
0 0 0 0 0 0 0 0 1 0 0
0 0 0 0 0 0 0 1 1 0 0
0 0 0 0 0 0 0 0 1 0 0
0 0 0 0 0 0 0 1 1 0 0
0 0 0 0 0 0 0 0 1 0 0
0 0 0 0 0 0 0 1 1 0 0
0 0 0 0 0 0 0 0 1 0 0
0 0 0 0 0 0 0 1 1 0 0
0 0 0 0 0 0 0 0 1 0 0
0 0 0 0 0 0 0 1 1 0 0
0 0 0 0 0 0 0 0 1 0 0
0 0 0 0 0 0 0 1 1 0 0
0 0 0 0 0 0 0 0 1 0 0
0 0 0 0 0 0 0 1 1 0 0
0 0 0 0 0 0 0 0 1 0 0
0 0 0 0 0 0 0 1 1 0 0
0 0 0 0 0 0 0 0 1 0 0
0 0 0 0 0 0 0 1 1 0 0
0 0 0 0 0 0 0 0 1 0 0
0 0 0 0 0 0 0 1 1 0 0
0 0 0 0 0 0 0 0 1 0 0
0 0 0 0 0 0 0 1 1 0 0
0 0 0 0 0 0 0 0 1 0 0
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*/

/* Test case 01_P01T3:
M N progIN reset progLoad start result clk valid done output
0 0 0 0 0 0 0 0 x x x
0 0 0 0 0 0 0 1 x x x
0 0 0 1 0 0 0 0 x x x
0 0 0 1 0 0 0 1 0 0 x
0 0 0 0 0 0 0 0 0 0 x
0 0 0 0 0 0 0 1 0 0 x
0 0 0 0 0 0 0 0 0 0 x
0 0 0 0 0 0 0 1 0 0 x
0 0 0 0 0 0 0 0 0 0 x
0 0 0 0 0 0 0 1 0 0 x
0 0 0 0 0 0 0 0 0 0 x
0 0 0 0 0 0 0 1 0 0 x
0 0 0 0 0 0 0 0 0 0 x
0 0 0 0 0 0 0 1 0 0 x
0 0 0 0 0 0 0 0 0 0 x
0 0 0 0 0 0 0 1 0 0 x
0 0 0 0 0 0 0 0 0 0 x
0 0 0 0 0 0 0 1 0 0 x
0 0 0 0 0 0 0 0 0 0 x
0 0 0 0 0 0 0 1 0 0 x
0 0 0 0 0 0 0 0 0 0 x
0 0 0 0 0 0 0 1 0 0 x
0 0 0 0 0 0 0 0 0 0 x
0 0 0 0 0 0 0 1 0 0 x
0 0 0 0 0 0 0 0 0 0 x
0 0 0 0 0 0 0 1 0 0 x
0 0 0 0 0 0 0 0 0 0 x
0 0 0 0 0 0 0 1 0 0 x
0 0 0 0 0 0 0 0 0 0 x
0 0 0 0 0 0 0 1 0 0 x
0 0 0 0 0 0 0 0 0 0 x
0 0 0 0 0 0 0 1 0 0 x
0 0 0 0 0 0 0 0 0 0 x
0 0 0 0 0 0 0 1 0 0 x
0 0 0 0 0 0 0 0 0 0 x
0 0 0 0 0 0 0 1 0 0 x
0 0 0 0 0 0 0 0 0 0 x
0 0 0 0 0 0 0 1 0 0 x
0 0 0 0 0 0 0 0 0 0 x
0 0 0 0 0 0 0 1 0 0 x
0 0 0 0 0 0 0 0 0 0 x
0 0 0 0 0 0 0 1 0 0 x
0 0 271 0 1 0 0 0 0 0 x
0 0 271 0 1 0 0 1 0 0 x
0 0 566 0 1 0 0 0 0 0 x
0 0 566 0 1 0 0 1 0 0 x
0 0 5888 0 1 0 0 0 0 0 x
0 0 5888 0 1 0 0 1 0 0 x
0 0 3599 0 1 0 0 0 0 0 x
0 0 3599 0 1 0 0 1 0 0 x
0 0 4110 0 1 0 0 0 0 0 x
0 0 4110 0 1 0 0 1 0 0 x
0 0 3856 0 1 0 0 0 0 0 x
0 0 3856 0 1 0 0 1 0 0 x
0 0 7936 0 1 0 0 0 0 0 x
0 0 7936 0 1 0 0 1 0 0 x
0 0 0 0 1 0 0 0 0 0 x
0 0 0 0 1 0 0 1 0 0 x
0 0 0 0 1 0 0 0 0 0 x
0 0 0 0 1 0 0 1 0 0 x
0 0 0 0 1 0 0 0 0 0 x
0 0 0 0 1 0 0 1 0 0 x
0 0 0 0 1 0 0 0 0 0 x
0 0 0 0 1 0 0 1 0 0 x
0 0 0 0 1 0 0 0 0 0 x
0 0 0 0 1 0 0 1 0 0 x
0 0 0 0 1 0 0 0 0 0 x
0 0 0 0 1 0 0 1 0 0 x
0 0 0 0 1 0 0 0 0 0 x
0 0 0 0 1 0 0 1 0 0 x
0 0 0 0 1 0 0 0 0 0 x
0 0 0 0 1 0 0 1 0 0 x
0 0 0 0 1 0 0 0 0 0 x
0 0 0 0 1 0 0 1 0 0 x
0 0 4352 0 1 0 0 0 0 0 x
0 0 4352 0 1 0 0 1 0 0 x
0 0 2819 0 1 0 0 0 0 0 x
0 0 2819 0 1 0 0 1 0 0 x
0 0 7936 0 1 0 0 0 0 0 x
0 0 7936 0 1 0 0 1 0 0 x
0 0 0 0 1 0 0 0 0 0 x
0 0 0 0 1 0 0 1 0 0 x
0 0 0 0 0 0 0 0 0 0 x
0 0 0 0 0 0 0 1 0 0 x
0 0 0 0 0 0 0 0 0 0 x
0 0 0 0 0 0 0 1 0 0 x
0 0 0 0 0 0 0 0 0 0 x
0 0 0 0 0 0 0 1 0 0 x
0 0 0 0 0 1 0 0 0 0 x
0 0 0 0 0 1 0 1 0 0 x
0 0 0 0 0 0 0 0 x 0 x
0 0 0 0 0 0 0 1 x 0 x
0 0 0 0 0 0 0 0 x 0 x
0 0 0 0 0 0 0 1 x 0 x
0 0 0 0 0 0 0 0 x 0 x
0 0 0 0 0 0 0 1 x 0 x
0 0 0 0 0 0 0 0 x 0 x
0 0 0 0 0 0 0 1 x 0 x
0 0 0 0 0 0 0 0 x 0 x
0 0 0 0 0 0 0 1 x 0 x
0 0 0 0 0 0 0 0 x 0 x
0 0 0 0 0 0 0 1 x 0 x
0 0 0 0 0 0 0 0 x 0 x
0 0 0 0 0 0 0 1 x 0 x
0 0 0 0 0 0 0 0 x 0 x
0 0 0 0 0 0 0 1 x 0 x
0 0 0 0 0 0 0 0 x 0 x
0 0 0 0 0 0 0 1 x 0 x
0 0 0 0 0 0 0 0 x 0 x
0 0 0 0 0 0 0 1 x 0 x
0 0 0 0 0 0 0 0 x 0 x
0 0 0 0 0 0 0 1 x 0 x
0 0 0 0 0 0 0 0 x 0 x
0 0 0 0 0 0 0 1 x 0 x
0 0 0 0 0 0 0 0 x 0 x
0 0 0 0 0 0 0 1 x 0 x
0 0 0 0 0 0 0 0 x 0 x
0 0 0 0 0 0 0 1 x 0 x
0 0 0 0 0 0 0 0 x 0 x
0 0 0 0 0 0 0 1 x 0 x
0 0 0 0 0 0 0 0 x 0 x
0 0 0 0 0 0 0 1 x 0 x
0 0 0 0 0 0 0 0 x 0 x
0 0 0 0 0 0 0 1 x 0 x
0 0 0 0 0 0 0 0 x 0 x
0 0 0 0 0 0 0 1 x 0 x
0 0 0 0 0 0 0 0 x 0 x
0 0 0 0 0 0 0 1 x 0 x
0 0 0 0 0 0 0 0 x 0 x
0 0 0 0 0 0 0 1 x 0 x
0 0 0 0 0 0 0 0 x 0 x
0 0 0 0 0 0 0 1 x 0 x
0 0 0 0 0 0 0 0 x 0 x
0 0 0 0 0 0 0 1 x 0 x
0 0 0 0 0 0 0 0 x 0 x
0 0 0 0 0 0 0 1 x 0 x
0 0 0 0 0 0 0 0 x 0 x
0 0 0 0 0 0 0 1 x 0 x
0 0 0 0 0 0 0 0 x 0 x
0 0 0 0 0 0 0 1 x 0 x
0 0 0 0 0 0 0 0 x 0 x
0 0 0 0 0 0 0 1 1 0 x
0 0 0 0 0 0 1 0 1 0 x
0 0 0 0 0 0 1 1 1 0 0
0 0 0 0 0 0 0 0 1 0 0
0 0 0 0 0 0 0 1 1 0 0
0 0 0 0 0 0 0 0 1 0 0
0 0 0 0 0 0 0 1 1 0 0
0 0 0 0 0 0 0 0 1 0 0
0 0 0 0 0 0 0 1 1 0 69
0 0 0 0 0 0 0 0 1 0 69
0 0 0 0 0 0 0 1 1 0 0
0 0 0 0 0 0 0 0 1 0 0
0 0 0 0 0 0 0 1 1 0 0
0 0 0 0 0 0 0 0 1 0 0
0 0 0 0 0 0 0 1 1 0 0
0 0 0 0 0 0 0 0 1 0 0
0 0 0 0 0 0 0 1 1 0 0
0 0 0 0 0 0 0 0 1 0 0
0 0 0 0 0 0 0 1 1 0 0
0 0 0 0 0 0 0 0 1 0 0
0 0 0 0 0 0 0 1 1 0 0
0 0 0 0 0 0 0 0 1 0 0
0 0 0 0 0 0 0 1 1 0 0
0 0 0 0 0 0 0 0 1 0 0
0 0 0 0 0 0 0 1 1 0 0
0 0 0 0 0 0 0 0 1 0 0
0 0 0 0 0 0 0 1 1 0 0
0 0 0 0 0 0 0 0 1 0 0
0 0 0 0 0 0 0 1 1 0 0
0 0 0 0 0 0 0 0 1 0 0
0 0 0 0 0 0 0 1 1 0 0
0 0 0 0 0 0 0 0 1 0 0
0 0 0 0 0 0 0 1 1 0 0
0 0 0 0 0 0 0 0 1 0 0
0 0 0 0 0 0 0 1 1 1 x
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*/

/* Test case 01_P01T4:
M N progIN reset progLoad start result clk valid done output
0 0 0 0 0 0 0 0 x x x
0 0 0 0 0 0 0 1 x x x
0 0 0 1 0 0 0 0 x x x
0 0 0 1 0 0 0 1 0 0 x
0 0 0 0 0 0 0 0 0 0 x
0 0 0 0 0 0 0 1 0 0 x
0 0 0 0 0 0 0 0 0 0 x
0 0 0 0 0 0 0 1 0 0 x
0 0 0 0 0 0 0 0 0 0 x
0 0 0 0 0 0 0 1 0 0 x
0 0 0 0 0 0 0 0 0 0 x
0 0 0 0 0 0 0 1 0 0 x
0 0 0 0 0 0 0 0 0 0 x
0 0 0 0 0 0 0 1 0 0 x
0 0 0 0 0 0 0 0 0 0 x
0 0 0 0 0 0 0 1 0 0 x
0 0 0 0 0 0 0 0 0 0 x
0 0 0 0 0 0 0 1 0 0 x
0 0 0 0 0 0 0 0 0 0 x
0 0 0 0 0 0 0 1 0 0 x
0 0 0 0 0 0 0 0 0 0 x
0 0 0 0 0 0 0 1 0 0 x
0 0 0 0 0 0 0 0 0 0 x
0 0 0 0 0 0 0 1 0 0 x
0 0 0 0 0 0 0 0 0 0 x
0 0 0 0 0 0 0 1 0 0 x
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*/

/* Test case 01_P01T5:
M N progIN reset progLoad start result clk valid done output
0 0 0 0 0 0 0 0 x x x
0 0 0 0 0 0 0 1 x x x
0 0 0 1 0 0 0 0 x x x
0 0 0 1 0 0 0 1 0 0 x
0 0 0 0 0 0 0 0 0 0 x
0 0 0 0 0 0 0 1 0 0 x
0 0 0 0 0 0 0 0 0 0 x
0 0 0 0 0 0 0 1 0 0 x
0 0 0 0 0 0 0 0 0 0 x
0 0 0 0 0 0 0 1 0 0 x
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*/

/* Test case 01_P01T6:
M N progIN reset progLoad start result clk valid done output
0 0 0 0 0 0 0 0 x x x
0 0 0 0 0 0 0 1 x x x
0 0 0 1 0 0 0 0 x x x
0 0 0 1 0 0 0 1 0 0 x
0 0 0 0 0 0 0 0 0 0 x
0 0 0 0 0 0 0 1 0 0 x
0 0 0 0 0 0 0 0 0 0 x
0 0 0 0 0 0 0 1 0 0 x
0 0 0 0 0 0 0 0 0 0 x
0 0 0 0 0 0 0 1 0 0 x
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*/

/* Test case 01_P01T7:
M N progIN reset progLoad start result clk valid done output
0 0 0 0 0 0 0 0 x x x
0 0 0 0 0 0 0 1 x x x
0 0 0 1 0 0 0 0 x x x
0 0 0 1 0 0 0 1 0 0 x
0 0 0 0 0 0 0 0 0 0 x
0 0 0 0 0 0 0 1 0 0 x
0 0 0 0 0 0 0 0 0 0 x
0 0 0 0 0 0 0 1 0 0 x
0 0 0 0 0 0 0 0 0 0 x
0 0 0 0 0 0 0 1 0 0 x
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*/

/* Test case 01_P01T8:
M N progIN reset progLoad start result clk valid done output
0 0 0 0 0 0 0 0 x x x
0 0 0 0 0 0 0 1 x x x
0 0 0 1 0 0 0 0 x x x
0 0 0 1 0 0 0 1 0 0 x
0 0 0 0 0 0 0 0 0 0 x
0 0 0 0 0 0 0 1 0 0 x
0 0 0 0 0 0 0 0 0 0 x
0 0 0 0 0 0 0 1 0 0 x
0 0 0 0 0 0 0 0 0 0 x
0 0 0 0 0 0 0 1 0 0 x
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*/
