// Digital circuit finalMain.dig as structural Verilog
module finalMain (
  input  [7:0] M,
  input  [7:0] N,
  input  [12:0] progIN,
  input  reset,
  input  progLoad,
  input  start,
  input  result,
  input  clk,
  output valid,
  output done,
  output [7:0] \output ,
  output [7:0] out_12,
  output [7:0] out_13,
  output [7:0] out_14,
  output [7:0] out_15,
  output [12:0] out_16,
  output [7:0] out_17
);

  wire _00, _0000, _00000, _00001, _0001, _01, _00010, _0010, _10, _00011, _0011, _11, _00100, _0100, _00101,
       _0101, _00110, _0110, _00111, _0111, _01000, _1000, _01001, _1001, _01010, _1010, _01011, _1011,
       _01100, _1100, _01101, _1101, _01110, _1110, _01111, _1111, _10000, _10001, _10010, _10011, _10100,
       _10101, _10110, _10111, _11000, _11001, _11010, _11011, _11100, _11101, _11110, _11111, ALU,
       and_1_out, and_2_out, and_3_out, and_6_out, and_7_out, and_8_out, and_9_out, and_10_out, and_11_out,
       and_12_out, and_13_out, and_14_out, and_15_out, and_16_out, and_17_out, and_18_out, and_19_out,
       and_20_out, and_21_out, and_22_out, and_24_out, and_25_out, d_ff_5_q, en_rRAM, enA, enB, enC, eq,
       eq_t, gr, gt, isPrime_d, jump, jumpOp, le, lt, move, multiplexer_25_out, multiplexer_26_out,
       multiplexer_27_out, multiplexer_28_out, multiplexer_29_out, multiplexer_30_out, multiplexer_31_out,
       multiplexer_32_out, multiplexer_34_out, not_2_out, not_3_out, not_4_out, or_1_out, or_2_out, or_3_out,
       or_4_out, or_5_out, or_6_out, or_7_out, or_8_out, or_9_out, or_10_out, or_11_out, or_15_out,
       or_17_out, or_18_out, or_19_out, or_20_out, or_21_out, or_22_out, or_23_out, or_24_out, or_25_out,
       or_26_out, or_27_out, or_28_out, or_29_out, or_30_out, P_a, P_b, Q_a, Q_b, Q_c, Q_d, r_cnt_eq_16,
       r_cnt_gt_16, r_cnt_lt_16, result_cnt_eq_16, result_cnt_gt_16, result_cnt_lt_16;
  wire [2:1] bitcount_4_out;
  wire [3:1] bitcount_2_out, bitcount_3_out;
  wire [4:0] bitcount_1_out;
  wire [7:0] A, A_B, A_lt__lt_B, AND, cnt, DIFF, DIV, MOD, MUL, multiplexer_1_out, multiplexer_2_out,
       multiplexer_3_out, multiplexer_4_out, multiplexer_5_out, multiplexer_6_out, multiplexer_7_out,
       multiplexer_8_out, multiplexer_9_out, multiplexer_10_out, multiplexer_11_out, multiplexer_12_out,
       multiplexer_13_out, multiplexer_14_out, multiplexer_15_out, multiplexer_16_out, multiplexer_17_out,
       multiplexer_18_out, multiplexer_19_out, multiplexer_22_out, multiplexer_23_out, multiplexer_24_out,
       OR, pRAM_operand, r_cnt, result_cnt, rom_1_d, rRAM_d2, rRAM_operand, rRAM_operand_1, rRAM_operand_2,
       SUM, val, XOR;
  wire [12:8] pRAM_d1;
  wire [15:0] rom_2_d, rom_3_d;

  Multiplexer #(.Selector_Bits(2), .Bits(8)) multiplexer_1 (
    .sel({en_rRAM, _01010}), .in_0(r_cnt), .in_1(out_16[7:0]), .in_2(out_16[7:0]), .in_3({8{1'b0}}),
    .out(multiplexer_1_out));
  or or_1 (or_1_out, reset, ~progLoad);  // Or
  Multiplexer #(.Bits(8)) multiplexer_2 (.sel(_11110), .in_0(multiplexer_1_out), .in_1(8'he), .out(multiplexer_2_out));
  Multiplexer #(.Selector_Bits(2), .Bits(8)) multiplexer_3 (
    .sel({en_rRAM, _01010}), .in_0(r_cnt), .in_1(out_16[7:0]), .in_2(out_16[7:0]), .in_3({8{1'b0}}),
    .out(multiplexer_3_out));
  Multiplexer #(.Selector_Bits(2), .Bits(8)) multiplexer_4 (
    .sel({en_rRAM, _01010}), .in_0(r_cnt), .in_1(out_16[7:0]), .in_2(out_16[7:0]), .in_3({8{1'b0}}),
    .out(multiplexer_4_out));
  CounterPreset #(.maxValue(256), .Bits(8)) u_cnt (
    .en(progLoad), .C(clk), .dir(1'b0), .in({8{1'b0}}), .ld(1'b0), .clr(or_1_out), .out(cnt));  // open: ovf
  or or_2 (or_2_out, _00, result);
  Multiplexer #(.Bits(8)) multiplexer_5 (.sel(_1010), .in_0(multiplexer_2_out), .in_1(8'hf), .out(multiplexer_5_out));
  Multiplexer #(.Bits(8)) multiplexer_6 (.sel(_11110), .in_0(multiplexer_3_out), .in_1(8'he), .out(multiplexer_6_out));
  Multiplexer #(.Bits(8)) multiplexer_7 (.sel(_11110), .in_0(multiplexer_4_out), .in_1(8'he), .out(multiplexer_7_out));
  Multiplexer #(.Bits(8)) multiplexer_8 (.sel(_01001), .in_0(cnt), .in_1(out_16[7:0]), .out(multiplexer_8_out));
  or or_3 (or_3_out, en_rRAM, _11110, _0011, _1010);
  Multiplexer #(.Bits(8)) multiplexer_9 (.sel(en_rRAM), .in_0({8{1'b0}}), .in_1(val), .out(multiplexer_9_out));
  Multiplexer #(.Bits(8)) multiplexer_10 (.sel(_1010), .in_0(multiplexer_6_out), .in_1(8'hf), .out(multiplexer_10_out));
  Multiplexer #(.Bits(8)) multiplexer_11 (.sel(_1010), .in_0(multiplexer_7_out), .in_1(8'hf), .out(multiplexer_11_out));
  CounterPreset #(.maxValue(256), .Bits(8)) u_r_cnt (
    .en(_0011), .C(clk), .dir(1'b0), .in({8{1'b0}}), .ld(1'b0), .clr(r_cnt_eq_16), .out(r_cnt));  // open: ovf
  Comparator #(.Bits(8)) u_r_cnt_eq_16 (.a(r_cnt), .b(8'h10), .gt(r_cnt_gt_16), .eq(r_cnt_eq_16), .lt(r_cnt_lt_16));
  Counter #(.Bits(8)) u_result_cnt (.en(_01), .C(clk), .clr(or_2_out), .out(result_cnt));  // open: ovf
  Multiplexer #(.Bits(8)) multiplexer_12 (
    .sel(_1010), .in_0(multiplexer_13_out), .in_1(rom_1_d), .out(multiplexer_12_out));
  Multiplexer #(.Bits(8)) multiplexer_13 (
    .sel(_11110), .in_0(multiplexer_9_out), .in_1(out_17), .out(multiplexer_13_out));
  or or_4 (or_4_out, en_rRAM, _11110, _0011, _1010);
  Multiplexer #(.Bits(8)) multiplexer_14 (
    .sel(_1010), .in_0(multiplexer_15_out), .in_1(rom_2_d[7:0]), .out(multiplexer_14_out));
  Multiplexer #(.Bits(8)) multiplexer_15 (
    .sel(_11110), .in_0(multiplexer_16_out), .in_1(rom_2_d[15:8]), .out(multiplexer_15_out));
  Multiplexer #(.Bits(8)) multiplexer_16 (.sel(en_rRAM), .in_0({8{1'b0}}), .in_1(val), .out(multiplexer_16_out));
  or or_5 (or_5_out, en_rRAM, _11110, _0011, _1010);
  Multiplexer #(.Bits(8)) multiplexer_17 (
    .sel(_1010), .in_0(multiplexer_18_out), .in_1(rom_3_d[7:0]), .out(multiplexer_17_out));
  Multiplexer #(.Bits(8)) multiplexer_18 (
    .sel(_11110), .in_0(multiplexer_19_out), .in_1(rom_3_d[15:8]), .out(multiplexer_18_out));
  Multiplexer #(.Bits(8)) multiplexer_19 (.sel(en_rRAM), .in_0({8{1'b0}}), .in_1(val), .out(multiplexer_19_out));
  RAMDualAccess #(.AddrBits(8), .Bits(13)) pRAM (
    .str(progLoad), .C(clk), .ld(_01001), .A1(multiplexer_8_out), .Din1(progIN), .A2(out_12),
    .D1({pRAM_d1, pRAM_operand}), .D2(out_16));
  RAMDualAccess #(.AddrBits(8), .Bits(8)) rRAM (
    .str(or_3_out), .C(clk), .ld(_01010), .A1(multiplexer_5_out), .Din1(multiplexer_12_out), .A2(result_cnt),
    .D1(rRAM_operand), .D2(rRAM_d2));
  RAMDualAccess #(.AddrBits(8), .Bits(8)) rRAM_2 (
    .str(or_4_out), .C(clk), .ld(_01010), .A1(multiplexer_10_out), .Din1(multiplexer_14_out),
    .A2({4'b0000, out_16[3:0]}), .D2(rRAM_operand_1));  // open: D1
  RAMDualAccess #(.AddrBits(8), .Bits(8)) rRAM_3 (
    .str(or_5_out), .C(clk), .ld(_01010), .A1(multiplexer_11_out), .Din1(multiplexer_17_out),
    .A2({4'b0000, out_16[7:4]}), .D2(rRAM_operand_2));  // open: D1
  or or_6 (or_6_out, reset, _11111);
  Multiplexer #(.Bits(8)) multiplexer_20 (.sel(_01), .in_0({8{1'b0}}), .in_1(rRAM_d2), .out(\output ));
  ROM #(.AddrBits(16), .Bits(16)) rom_1 (.A({rRAM_operand_1, rRAM_operand_2}), .sel(1'b1), .D({out_17, rom_1_d}));
  or or_7 (or_7_out, _0101, _0111, _1010, _0110);
  CounterPreset #(.maxValue(256), .Bits(8)) pc (
    .en(or_7_out), .C(clk), .dir(1'b0), .in(out_16[7:0]), .ld(jump), .clr(or_6_out), .out(out_12));  // open: ovf
  Comparator #(.Bits(8)) comparator_1 (
    .a(result_cnt), .b(8'h10), .gt(result_cnt_gt_16), .eq(result_cnt_eq_16), .lt(result_cnt_lt_16));
  ROM #(.AddrBits(16), .Bits(16)) rom_2 (.A({rRAM_operand_1, rRAM_operand_2}), .sel(1'b1), .D(rom_2_d));
  ROM #(.AddrBits(16), .Bits(16)) rom_3 (.A({rRAM_operand_1, rRAM_operand_2}), .sel(1'b1), .D(rom_3_d));
  Multiplexer #(.Selector_Bits(5), .Bits(8)) multiplexer_21 (
    .sel(out_16[12:8]), .in_0({8{1'b0}}), .in_1(out_16[7:0]), .in_2(out_16[7:0]), .in_3(out_14),
    .in_4(out_15), .in_5(out_15), .in_6(out_13), .in_7(M), .in_8(N), .in_9(pRAM_operand),
    .in_10(rRAM_operand), .in_11(out_15), .in_12({8{1'b0}}), .in_13({8{1'b0}}), .in_14({8{1'b0}}),
    .in_15({8{1'b0}}), .in_16({8{1'b0}}), .in_17(SUM), .in_18(DIFF), .in_19(MUL), .in_20(DIV), .in_21(MOD),
    .in_22(A_B), .in_23({8{1'b0}}), .in_24(A), .in_25(AND), .in_26(OR), .in_27(XOR), .in_28(A_lt__lt_B),
    .in_29({8{1'b0}}), .in_30({8{1'b0}}), .in_31({8{1'b0}}), .out(val));
  Multiplexer #(.Bits(8)) multiplexer_22 (.sel(reset), .in_0(val), .in_1({8{1'b0}}), .out(multiplexer_22_out));
  Register #(.Bits(8)) regC (.D(multiplexer_22_out), .C(clk), .en(enC), .Q(out_13));
  BitCount #(.Bits(16)) bitcount_1 (
    .in({_11100, _11011, _11010, _11001, _11000, _10110, _10101, _10100, _10011, _10010, _10001, _01010, _01001, _00110, _00011, _00001}),
    .out(bitcount_1_out));
  or or_8 (or_8_out, reset, start, progLoad);
  or or_9 (or_9_out, _0101, _0111);
  or or_10 (or_10_out, _00010, _00100);
  or or_11 (or_11_out, _00101, _00111, _01000);
  Multiplexer #(.Bits(8)) multiplexer_23 (.sel(reset), .in_0(val), .in_1({8{1'b0}}), .out(multiplexer_23_out));
  Register #(.Bits(8)) accB (.D(multiplexer_23_out), .C(clk), .en(enB), .Q(out_14));
  RS_FF_AS rs_ff_as_1 (.S(_11111), .R(or_8_out), .Q(valid));  // open: nQ
  and and_1 (and_1_out, bitcount_1_out[0], or_9_out);
  and and_2 (and_2_out, or_10_out, _0101);
  and and_3 (and_3_out, or_11_out, _0101);
  or or_12 (enA, and_1_out, reset);
  or or_13 (enB, reset, and_2_out);
  or or_14 (enC, reset, and_3_out);
  and and_4 (en_rRAM, _01011, _0101);
  Multiplexer #(.Bits(8)) multiplexer_24 (.sel(reset), .in_0(val), .in_1({8{1'b0}}), .out(multiplexer_24_out));
  Register #(.Bits(8)) accA (.D(multiplexer_24_out), .C(clk), .en(enA), .Q(out_15));
  or or_15 (or_15_out, reset, start, progLoad, result);
  Seven_Seg_Hex seven_seg_hex_1 (.d(\output [7:4]), .dp(1'b0));
  RS_FF_AS rs_ff_as_2 (.S(result_cnt_eq_16), .R(or_15_out), .Q(done));  // open: nQ
  assign AND = out_15 & out_14;  // And and_5, 8 bits wide
  assign OR = out_15 | out_14;  // Or or_16, 8 bits wide
  assign XOR = out_15 ^ out_14;  // XOr xor_1, 8 bits wide
  Add #(.Bits(8)) add_1 (.a(out_15), .b(out_14), .c_i(1'b0), .s(SUM));  // open: c_o
  Sub #(.Bits(8)) sub_1 (.a(out_15), .b(out_14), .c_i(1'b0), .s(DIFF));  // open: c_o
  Mul #(.Bits(4)) mul_1 (.a(out_15[3:0]), .b(out_14[3:0]), .mul(MUL));
  Div #(.Bits(8)) divide (.a(out_15), .b(out_14), .q(DIV), .r(MOD));
  assign A = ~out_15;  // Not not_1, 8 bits wide
  BarrelShifter #(.Bits(8), .barrelShifterMode("arithmetic")) barrelshifter_1 (
    .in(out_15), .shift({1'b0, out_14[2:0]}), .out(A_lt__lt_B));
  LookUpTable #(.Bits(8)) exponent (
    .in0(out_14[0]), .in1(out_14[1]), .in2(out_14[2]), .in3(out_15[0]), .in4(out_15[1]), .in5(out_15[2]),
    .out(A_B));
  Seven_Seg_Hex seven_seg_hex_2 (.d(\output [3:0]), .dp(1'b0));
  or or_17 (or_17_out, _11110, _11111);
  and and_6 (and_6_out, ~start, ~reset);  // And
  and and_7 (and_7_out, lt, _10111);
  or or_18 (or_18_out, start, progLoad, reset);
  and and_8 (and_8_out, ~reset, ~result);  // And
  or or_19 (or_19_out, start, progLoad, reset);
  Multiplexer #(.Selector_Bits(4)) multiplexer_25 (
    .sel({Q_a, Q_b, Q_c, Q_d}), .in_0(1'b0), .in_1(1'b0), .in_2(1'b0), .in_3(1'b0), .in_4(or_17_out),
    .in_5(1'b0), .in_6(1'b0), .in_7(1'b0), .in_8(1'b1), .in_9(and_6_out), .in_10(1'b0), .in_11(1'b0),
    .in_12(1'b0), .in_13(1'b0), .in_14(1'b0), .in_15(1'b0), .out(multiplexer_25_out));
  not not_2 (not_2_out, result_cnt_eq_16);
  Multiplexer multiplexer_26 (.sel(_0111), .in_0(1'b0), .in_1(and_7_out), .out(multiplexer_26_out));
  or or_20 (or_20_out, start, and_12_out);
  and and_9 (and_9_out, ~reset, multiplexer_25_out);  // And
  Multiplexer #(.Selector_Bits(2)) multiplexer_27 (
    .sel({P_a, P_b}), .in_0(1'b0), .in_1(result_cnt_eq_16), .in_2(and_8_out), .in_3(1'b0),
    .out(multiplexer_27_out));
  Multiplexer #(.Selector_Bits(2)) multiplexer_28 (
    .sel({P_a, P_b}), .in_0(result), .in_1(not_2_out), .in_2(result), .in_3(1'b0), .out(multiplexer_28_out));
  Register register_1 (.D(multiplexer_26_out), .C(clk), .en(or_20_out), .Q(le));
  Multiplexer multiplexer_29 (.sel(_0111), .in_0(1'b0), .in_1(or_22_out), .out(multiplexer_29_out));
  Register register_2 (.D(multiplexer_29_out), .C(clk), .en(or_21_out), .Q(eq_t));
  or or_21 (or_21_out, start, and_13_out);
  and and_10 (and_10_out, ~or_18_out, multiplexer_27_out);  // And
  and and_11 (and_11_out, ~or_19_out, multiplexer_28_out);  // And
  and and_12 (and_12_out, _0111, _10111);
  and and_13 (and_13_out, _0111, or_23_out);
  D_FF d_ff_1 (.D(and_9_out), .C(clk), .Q(Q_a));  // open: nQ
  or or_22 (or_22_out, and_16_out, and_15_out);
  D_FF d_ff_2 (.D(and_10_out), .C(clk), .Q(P_a));  // open: nQ
  D_FF d_ff_3 (.D(and_11_out), .C(clk), .Q(P_b));  // open: nQ
  and and_14 (and_14_out, gt, _10111);
  and and_15 (and_15_out, _11101, isPrime_d);
  and and_16 (and_16_out, eq, _10111);
  or or_23 (or_23_out, _11101, _10111);
  or or_24 (or_24_out, ALU, jumpOp, move);
  Multiplexer #(.Selector_Bits(4)) multiplexer_30 (
    .sel({Q_a, Q_b, Q_c, Q_d}), .in_0(start), .in_1(start), .in_2(1'b0), .in_3(1'b0), .in_4(or_24_out),
    .in_5(1'b1), .in_6(1'b1), .in_7(1'b1), .in_8(1'b0), .in_9(start), .in_10(1'b1), .in_11(1'b0),
    .in_12(1'b0), .in_13(1'b0), .in_14(1'b0), .in_15(1'b0), .out(multiplexer_30_out));
  Multiplexer multiplexer_31 (.sel(_0111), .in_0(1'b0), .in_1(and_14_out), .out(multiplexer_31_out));
  or or_25 (or_25_out, start, and_18_out);
  ROM #(.AddrBits(8)) isPrime (.A(out_15), .sel(1'b1), .D(isPrime_d));
  and and_17 (and_17_out, ~reset, multiplexer_30_out);  // And
  Decoder #(.Selector_Bits(2)) decoder_1 (.sel({P_a, P_b}), .out_0(_00), .out_1(_01), .out_2(_10), .out_3(_11));
  Register register_3 (.D(multiplexer_31_out), .C(clk), .en(or_25_out), .Q(gr));
  or or_26 (or_26_out, eq_t, gr);
  and and_18 (and_18_out, _0111, _10111);
  D_FF d_ff_4 (.D(and_17_out), .C(clk), .Q(Q_b));  // open: nQ
  and and_19 (and_19_out, _01101, eq_t);
  and and_20 (and_20_out, _01110, gr);
  and and_21 (and_21_out, _01111, le);
  and and_22 (and_22_out, _10000, or_26_out);
  or or_27 (or_27_out, ALU, jumpOp);
  Comparator #(.Signed("true"), .Bits(8)) comparator_2 (.a(out_15), .b(out_14), .gt(gt), .eq(eq), .lt(lt));
  or or_28 (or_28_out, _01100, and_19_out, and_20_out, and_21_out, and_22_out);
  Multiplexer #(.Selector_Bits(4)) multiplexer_32 (
    .sel({Q_a, Q_b, Q_c, Q_d}), .in_0(reset), .in_1(reset), .in_2(1'b1), .in_3(not_3_out), .in_4(or_27_out),
    .in_5(1'b0), .in_6(1'b0), .in_7(1'b0), .in_8(1'b1), .in_9(reset), .in_10(1'b0), .in_11(1'b0),
    .in_12(1'b0), .in_13(1'b0), .in_14(1'b0), .in_15(1'b0), .out(multiplexer_32_out));
  not not_3 (not_3_out, r_cnt_eq_16);
  and and_23 (jump, or_28_out, _0110);
  D_FF d_ff_5 (.D(multiplexer_32_out), .C(clk), .Q(d_ff_5_q));  // open: nQ
  Multiplexer multiplexer_33 (.sel(reset), .in_0(d_ff_5_q), .in_1(1'b1), .out(Q_c));
  or or_29 (or_29_out, ALU, _11111, move);
  not not_4 (not_4_out, r_cnt_eq_16);
  and and_24 (and_24_out, ~start, ~reset);  // And
  Multiplexer #(.Selector_Bits(4)) multiplexer_34 (
    .sel({Q_a, Q_b, Q_c, Q_d}), .in_0(progLoad), .in_1(progLoad), .in_2(1'b1), .in_3(not_4_out),
    .in_4(or_29_out), .in_5(1'b0), .in_6(1'b0), .in_7(1'b0), .in_8(1'b0), .in_9(and_24_out), .in_10(1'b0),
    .in_11(1'b0), .in_12(1'b0), .in_13(1'b0), .in_14(1'b0), .in_15(1'b0), .out(multiplexer_34_out));
  and and_25 (and_25_out, ~reset, multiplexer_34_out);  // And
  D_FF d_ff_6 (.D(and_25_out), .C(clk), .Q(Q_d));  // open: nQ
  Decoder #(.Selector_Bits(4)) decoder_2 (
    .sel({Q_a, Q_b, Q_c, Q_d}), .out_0(_0000), .out_1(_0001), .out_2(_0010), .out_3(_0011), .out_4(_0100),
    .out_5(_0101), .out_6(_0110), .out_7(_0111), .out_8(_1000), .out_9(_1001), .out_10(_1010),
    .out_11(_1011), .out_12(_1100), .out_13(_1101), .out_14(_1110), .out_15(_1111));
  or or_30 (or_30_out, _1000, _0111, _0110, _0101, _0100);
  BitCount #(.Bits(13)) bitcount_2 (
    .in({_10001, _10010, _10011, _10100, _10101, _10110, _10111, _11000, _11001, _11010, _11011, _11100, _11101}),
    .out({bitcount_2_out, ALU}));
  Demultiplexer #(.Selector_Bits(5)) demultiplexer_1 (
    .sel(out_16[12:8]), .in(or_30_out), .out_0(_00000), .out_1(_00001), .out_2(_00010), .out_3(_00011),
    .out_4(_00100), .out_5(_00101), .out_6(_00110), .out_7(_00111), .out_8(_01000), .out_9(_01001),
    .out_10(_01010), .out_11(_01011), .out_12(_01100), .out_13(_01101), .out_14(_01110), .out_15(_01111),
    .out_16(_10000), .out_17(_10001), .out_18(_10010), .out_19(_10011), .out_20(_10100), .out_21(_10101),
    .out_22(_10110), .out_23(_10111), .out_24(_11000), .out_25(_11001), .out_26(_11010), .out_27(_11011),
    .out_28(_11100), .out_29(_11101), .out_30(_11110), .out_31(_11111));
  BitCount #(.Bits(12)) bitcount_3 (
    .in({_00000, _00001, _00010, _00011, _00100, _00101, _00110, _00111, _01000, _01001, _01010, _01011}),
    .out({bitcount_3_out, move}));
  BitCount #(.Bits(5)) bitcount_4 (.in({_01100, _01101, _01110, _01111, _10000}), .out({bitcount_4_out, jumpOp}));

  // Other names for the same wires on the sheet: accA[7:0] = out_15; accB[7:0] = out_14; en_future = _11110;
  //   future = _11110; operand[7:0] = out_16[7:0]; opcode[4:0] = out_16[12:8]; pc[7:0] = out_12; regC[7:0] = out_13;
  //   stop = _11111

  // Notes on the sheet:
  //   RAMs
  //   Testcases
  //   Counters
  //   contents of rom_1 (hex, n*v repeats v):
  //   257*0,1,2,3,4,5,6,7,8,9,a,b,c,d,e,f,10,11,12,13,14,15,16,17,18
  //   ,19,1a,1b,1c,1d,1e,1f,20,21,22,23,24,25,26,27,28,29,2a,2b,2c,2d
  //   ,2e,2f,30,31,32,33,34,35,36,37,38,39,3a,3b,3c,3d,3e,3f,40,41,42
  //   ,43,44,45,46,47,48,49,4a,4b,4c,4d,4e,4f,50,51,52,53,54,55,56,57
  //   ,58,59,5a,5b,5c,5d,5e,5f,60,61,62,63,64,65,66,67,68,69,6a,6b,6c
  //   ,6d,6e,6f,70,71,72,73,74,75,76,77,78,79,7a,7b,7c,7d,7e,7f,80,81
  //   ,82,83,84,85,86,87,88,89,8a,8b,8c,8d,8e,8f,90,91,92,93,94,95,96
  //   ,97,98,99,9a,9b,9c,9d,9e,9f,a0,a1,a2,a3,a4,a5,a6,a7,a8,a9,aa,ab
  //   ,ac,ad,ae,af,b0,b1,b2,b3,b4,b5,b6,b7,b8,b9,ba,bb,bc,bd,be,bf,c0
  //   ,c1,c2,c3,c4,c5,c6,c7,c8,c9,ca,cb,cc,cd,ce,cf,d0,d1,d2,d3,d4,d5
  //   ,d6,d7,d8,d9,da,db,dc,dd,de,df,e0,e1,e2,e3,e4,e5,e6,e7,e8,e9,ea
  //   ,eb,ec,ed,ee,ef,f0,f1,f2,f3,f4,f5,f6,f7,f8,f9,fa,fb,fc,fd,fe,ff
  //   ,0,2,2,6,4,a,6,e,8,12,a,16,c,1a,e,1e,10,22,12,26,14,2a,16,2e,18
  //   ,32,1a,36,1c,3a,1e,3e,20,42,22,46,24,4a,26,4e,28,52,2a,56,2c,5a
  //   ,2e,5e,30,62,32,66,34,6a,36,6e,38,72,3a,76,3c,7a,3e,7e,40,82,42
  //   ,86,44,8a,46,8e,48,92,4a,96,4c,9a,4e,9e,50,a2,52,a6,54,aa,56,ae
  //   ,58,b2,5a,b6,5c,ba,5e,be,60,c2,62,c6,64,ca,66,ce,68,d2,6a,d6,6c
  //   ,da,6e,de,70,e2,72,e6,74,ea,76,ee,78,f2,7a,f6,7c,fa,7e,fe,80,102
  //   ,82,106,84,10a,86,10e,88,112,8a,116,8c,11a,8e,11e,90,122,92,126
  //   ,94,12a,96,12e,98,132,9a,136,9c,13a,9e,13e,a0,142,a2,146,a4,14a
  //   ,a6,14e,a8,152,aa,156,ac,15a,ae,15e,b0,162,b2,166,b4,16a,b6,16e
  //   ,b8,172,ba,176,bc,17a,be,17e,c0,182,c2,186,c4,18a,c6,18e,c8,192
  //   ,ca,196,cc,19a,ce,19e,d0,1a2,d2,1a6,d4,1aa,d6,1ae,d8,1b2,da,1b6
  //   ,dc,1ba,de,1be,e0,1c2,e2,1c6,e4,1ca,e6,1ce,e8,1d2,ea,1d6,ec,1da
  //   ,ee,1de,f0,1e2,f2,1e6,f4,1ea,f6,1ee,f8,1f2,fa,1f6,fc,1fa,fe,1fe
  //   ,0,3,6,3,c,f,6,15,18,9,1e,21,c,27,2a,f,30,33,12,39,3c,15,42,45
  //   ,18,4b,4e,1b,54,57,1e,5d,60,21,66,69,24,6f,72,27,78,7b,2a,81,84
  //   ,2d,8a,8d,30,93,96,33,9c,9f,36,a5,a8,39,ae,b1,3c,b7,ba,3f,c0,c3
  //   ,42,c9,cc,45,d2,d5,48,db,de,4b,e4,e7,4e,ed,f0,51,f6,f9,54,ff,102
  //   ,57,108,10b,5a,111,114,5d,11a,11d,60,123,126,63,12c,12f,66,135
  //   ,138,69,13e,141,6c,147,14a,6f,150,153,72,159,15c,75,162,165,78
  //   ,16b,16e,7b,174,177,7e,17d,180,81,186,189,84,18f,192,87,198,19b
  //   ,8a,1a1,1a4,8d,1aa,1ad,90,1b3,1b6,93,1bc,1bf,96,1c5,1c8,99,1ce
  //   ,1d1,9c,1d7,1da,9f,1e0,1e3,a2,1e9,1ec,a5,1f2,1f5,a8,1fb,1fe,ab
  //   ,204,207,ae,20d,210,b1,216,219,b4,21f,222,b7,228,22b,ba,231,234
  //   ,bd,23a,23d,c0,243,246,c3,24c,24f,c6,255,258,c9,25e,261,cc,267
  //   ,26a,cf,270,273,d2,279,27c,d5,282,285,d8,28b,28e,db,294,297,de
  //   ,29d,2a0,e1,2a6,2a9,e4,2af,2b2,e7,2b8,2bb,ea,2c1,2c4,ed,2ca,2cd
  //   ,f0,2d3,2d6,f3,2dc,2df,f6,2e5,2e8,f9,2ee,2f1,fc,2f7,2fa,ff,0,4,4
  //   ,c,4,14,c,1c,8,24,14,2c,c,34,1c,3c,10,44,24,4c,14,54,2c,5c,18
  //   ,64,34,6c,1c,74,3c,7c,20,84,44,8c,24,94,4c,9c,28,a4,54,ac,2c,b4
  //   ,5c,bc,30,c4,64,cc,34,d4,6c,dc,38,e4,74,ec,3c,f4,7c,fc,40,104
  //   ,84,10c,44,114,8c,11c,48,124,94,12c,4c,134,9c,13c,50,144,a4,14c
  //   ,54,154,ac,15c,58,164,b4,16c,5c,174,bc,17c,60,184,c4,18c,64,194
  //   ,cc,19c,68,1a4,d4,1ac,6c,1b4,dc,1bc,70,1c4,e4,1cc,74,1d4,ec,1dc
  //   ,78,1e4,f4,1ec,7c,1f4,fc,1fc,80,204,104,20c,84,214,10c,21c,88
  //   ,224,114,22c,8c,234,11c,23c,90,244,124,24c,94,254,12c,25c,98,264
  //   ,134,26c,9c,274,13c,27c,a0,284,144,28c,a4,294,14c,29c,a8,2a4,154
  //   ,2ac,ac,2b4,15c,2bc,b0,2c4,164,2cc,b4,2d4,16c,2dc,b8,2e4,174,2ec
  //   ,bc,2f4,17c,2fc,c0,304,184,30c,c4,314,18c,31c,c8,324,194,32c,cc
  //   ,334,19c,33c,d0,344,1a4,34c,d4,354,1ac,35c,d8,364,1b4,36c,dc,374
  //   ,1bc,37c,e0,384,1c4,38c,e4,394,1cc,39c,e8,3a4,1d4,3ac,ec,3b4,1dc
  //   ,3bc,f0,3c4,1e4,3cc,f4,3d4,1ec,3dc,f8,3e4,1f4,3ec,fc,3f4,1fc,3fc
  //   ,0,5,a,f,14,5,1e,23,28,2d,a,37,3c,41,46,f,50,55,5a,5f,14,69,6e
  //   ,73,78,19,82,87,8c,91,1e,9b,a0,a5,aa,23,b4,b9,be,c3,28,cd,d2,d7
  //   ,dc,2d,e6,eb,f0,f5,32,ff,104,109,10e,37,118,11d,122,127,3c,131
  //   ,136,13b,140,41,14a,14f,154,159,46,163,168,16d,172,4b,17c,181
  //   ,186,18b,50,195,19a,19f,1a4,55,1ae,1b3,1b8,1bd,5a,1c7,1cc,1d1
  //   ,1d6,5f,1e0,1e5,1ea,1ef,64,1f9,1fe,203,208,69,212,217,21c,221
  //   ,6e,22b,230,235,23a,73,244,249,24e,253,78,25d,262,267,26c,7d,276
  //   ,27b,280,285,82,28f,294,299,29e,87,2a8,2ad,2b2,2b7,8c,2c1,2c6
  //   ,2cb,2d0,91,2da,2df,2e4,2e9,96,2f3,2f8,2fd,302,9b,30c,311,316
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  //   contents of rom_2 (hex, n*v repeats v):
  //   257*0,1,2,3,4,5,6,7,8,9,a,b,c,d,e,f,10,11,12,13,14,15,16,17,18
  //   ,19,1a,1b,1c,1d,1e,1f,20,21,22,23,24,25,26,27,28,29,2a,2b,2c,2d
  //   ,2e,2f,30,31,32,33,34,35,36,37,38,39,3a,3b,3c,3d,3e,3f,40,41,42
  //   ,43,44,45,46,47,48,49,4a,4b,4c,4d,4e,4f,50,51,52,53,54,55,56,57
  //   ,58,59,5a,5b,5c,5d,5e,5f,60,61,62,63,64,65,66,67,68,69,6a,6b,6c
  //   ,6d,6e,6f,70,71,72,73,74,75,76,77,78,79,7a,7b,7c,7d,7e,7f,80,81
  //   ,82,83,84,85,86,87,88,89,8a,8b,8c,8d,8e,8f,90,91,92,93,94,95,96
  //   ,97,98,99,9a,9b,9c,9d,9e,9f,a0,a1,a2,a3,a4,a5,a6,a7,a8,a9,aa,ab
  //   ,ac,ad,ae,af,b0,b1,b2,b3,b4,b5,b6,b7,b8,b9,ba,bb,bc,bd,be,bf,c0
  //   ,c1,c2,c3,c4,c5,c6,c7,c8,c9,ca,cb,cc,cd,ce,cf,d0,d1,d2,d3,d4,d5
  //   ,d6,d7,d8,d9,da,db,dc,dd,de,df,e0,e1,e2,e3,e4,e5,e6,e7,e8,e9,ea
  //   ,eb,ec,ed,ee,ef,f0,f1,f2,f3,f4,f5,f6,f7,f8,f9,fa,fb,fc,fd,fe,ff
  //   ,0,2,2,6,4,a,6,e,8,12,a,16,c,1a,e,1e,10,22,12,26,14,2a,16,2e,18
  //   ,32,1a,36,1c,3a,1e,3e,20,42,22,46,24,4a,26,4e,28,52,2a,56,2c,5a
  //   ,2e,5e,30,62,32,66,34,6a,36,6e,38,72,3a,76,3c,7a,3e,7e,40,82,42
  //   ,86,44,8a,46,8e,48,92,4a,96,4c,9a,4e,9e,50,a2,52,a6,54,aa,56,ae
  //   ,58,b2,5a,b6,5c,ba,5e,be,60,c2,62,c6,64,ca,66,ce,68,d2,6a,d6,6c
  //   ,da,6e,de,70,e2,72,e6,74,ea,76,ee,78,f2,7a,f6,7c,fa,7e,fe,80,102
  //   ,82,106,84,10a,86,10e,88,112,8a,116,8c,11a,8e,11e,90,122,92,126
  //   ,94,12a,96,12e,98,132,9a,136,9c,13a,9e,13e,a0,142,a2,146,a4,14a
  //   ,a6,14e,a8,152,aa,156,ac,15a,ae,15e,b0,162,b2,166,b4,16a,b6,16e
  //   ,b8,172,ba,176,bc,17a,be,17e,c0,182,c2,186,c4,18a,c6,18e,c8,192
  //   ,ca,196,cc,19a,ce,19e,d0,1a2,d2,1a6,d4,1aa,d6,1ae,d8,1b2,da,1b6
  //   ,dc,1ba,de,1be,e0,1c2,e2,1c6,e4,1ca,e6,1ce,e8,1d2,ea,1d6,ec,1da
  //   ,ee,1de,f0,1e2,f2,1e6,f4,1ea,f6,1ee,f8,1f2,fa,1f6,fc,1fa,fe,1fe
  //   ,0,3,6,3,c,f,6,15,18,9,1e,21,c,27,2a,f,30,33,12,39,3c,15,42,45
  //   ,18,4b,4e,1b,54,57,1e,5d,60,21,66,69,24,6f,72,27,78,7b,2a,81,84
  //   ,2d,8a,8d,30,93,96,33,9c,9f,36,a5,a8,39,ae,b1,3c,b7,ba,3f,c0,c3
  //   ,42,c9,cc,45,d2,d5,48,db,de,4b,e4,e7,4e,ed,f0,51,f6,f9,54,ff,102
  //   ,57,108,10b,5a,111,114,5d,11a,11d,60,123,126,63,12c,12f,66,135
  //   ,138,69,13e,141,6c,147,14a,6f,150,153,72,159,15c,75,162,165,78
  //   ,16b,16e,7b,174,177,7e,17d,180,81,186,189,84,18f,192,87,198,19b
  //   ,8a,1a1,1a4,8d,1aa,1ad,90,1b3,1b6,93,1bc,1bf,96,1c5,1c8,99,1ce
  //   ,1d1,9c,1d7,1da,9f,1e0,1e3,a2,1e9,1ec,a5,1f2,1f5,a8,1fb,1fe,ab
  //   ,204,207,ae,20d,210,b1,216,219,b4,21f,222,b7,228,22b,ba,231,234
  //   ,bd,23a,23d,c0,243,246,c3,24c,24f,c6,255,258,c9,25e,261,cc,267
  //   ,26a,cf,270,273,d2,279,27c,d5,282,285,d8,28b,28e,db,294,297,de
  //   ,29d,2a0,e1,2a6,2a9,e4,2af,2b2,e7,2b8,2bb,ea,2c1,2c4,ed,2ca,2cd
  //   ,f0,2d3,2d6,f3,2dc,2df,f6,2e5,2e8,f9,2ee,2f1,fc,2f7,2fa,ff,0,4,4
  //   ,c,4,14,c,1c,8,24,14,2c,c,34,1c,3c,10,44,24,4c,14,54,2c,5c,18
  //   ,64,34,6c,1c,74,3c,7c,20,84,44,8c,24,94,4c,9c,28,a4,54,ac,2c,b4
  //   ,5c,bc,30,c4,64,cc,34,d4,6c,dc,38,e4,74,ec,3c,f4,7c,fc,40,104
  //   ,84,10c,44,114,8c,11c,48,124,94,12c,4c,134,9c,13c,50,144,a4,14c
  //   ,54,154,ac,15c,58,164,b4,16c,5c,174,bc,17c,60,184,c4,18c,64,194
  //   ,cc,19c,68,1a4,d4,1ac,6c,1b4,dc,1bc,70,1c4,e4,1cc,74,1d4,ec,1dc
  //   ,78,1e4,f4,1ec,7c,1f4,fc,1fc,80,204,104,20c,84,214,10c,21c,88
  //   ,224,114,22c,8c,234,11c,23c,90,244,124,24c,94,254,12c,25c,98,264
  //   ,134,26c,9c,274,13c,27c,a0,284,144,28c,a4,294,14c,29c,a8,2a4,154
  //   ,2ac,ac,2b4,15c,2bc,b0,2c4,164,2cc,b4,2d4,16c,2dc,b8,2e4,174,2ec
  //   ,bc,2f4,17c,2fc,c0,304,184,30c,c4,314,18c,31c,c8,324,194,32c,cc
  //   ,334,19c,33c,d0,344,1a4,34c,d4,354,1ac,35c,d8,364,1b4,36c,dc,374
  //   ,1bc,37c,e0,384,1c4,38c,e4,394,1cc,39c,e8,3a4,1d4,3ac,ec,3b4,1dc
  //   ,3bc,f0,3c4,1e4,3cc,f4,3d4,1ec,3dc,f8,3e4,1f4,3ec,fc,3f4,1fc,3fc
  //   ,0,5,a,f,14,5,1e,23,28,2d,a,37,3c,41,46,f,50,55,5a,5f,14,69,6e
  //   ,73,78,19,82,87,8c,91,1e,9b,a0,a5,aa,23,b4,b9,be,c3,28,cd,d2,d7
  //   ,dc,2d,e6,eb,f0,f5,32,ff,104,109,10e,37,118,11d,122,127,3c,131
  //   ,136,13b,140,41,14a,14f,154,159,46,163,168,16d,172,4b,17c,181
  //   ,186,18b,50,195,19a,19f,1a4,55,1ae,1b3,1b8,1bd,5a,1c7,1cc,1d1
  //   ,1d6,5f,1e0,1e5,1ea,1ef,64,1f9,1fe,203,208,69,212,217,21c,221
  //   ,6e,22b,230,235,23a,73,244,249,24e,253,78,25d,262,267,26c,7d,276
  //   ,27b,280,285,82,28f,294,299,29e,87,2a8,2ad,2b2,2b7,8c,2c1,2c6
  //   ,2cb,2d0,91,2da,2df,2e4,2e9,96,2f3,2f8,2fd,302,9b,30c,311,316
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  //   contents of rom_3 (hex, n*v repeats v):
  //   257*0,1,2,3,4,5,6,7,8,9,a,b,c,d,e,f,10,11,12,13,14,15,16,17,18
  //   ,19,1a,1b,1c,1d,1e,1f,20,21,22,23,24,25,26,27,28,29,2a,2b,2c,2d
  //   ,2e,2f,30,31,32,33,34,35,36,37,38,39,3a,3b,3c,3d,3e,3f,40,41,42
  //   ,43,44,45,46,47,48,49,4a,4b,4c,4d,4e,4f,50,51,52,53,54,55,56,57
  //   ,58,59,5a,5b,5c,5d,5e,5f,60,61,62,63,64,65,66,67,68,69,6a,6b,6c
  //   ,6d,6e,6f,70,71,72,73,74,75,76,77,78,79,7a,7b,7c,7d,7e,7f,80,81
  //   ,82,83,84,85,86,87,88,89,8a,8b,8c,8d,8e,8f,90,91,92,93,94,95,96
  //   ,97,98,99,9a,9b,9c,9d,9e,9f,a0,a1,a2,a3,a4,a5,a6,a7,a8,a9,aa,ab
  //   ,ac,ad,ae,af,b0,b1,b2,b3,b4,b5,b6,b7,b8,b9,ba,bb,bc,bd,be,bf,c0
  //   ,c1,c2,c3,c4,c5,c6,c7,c8,c9,ca,cb,cc,cd,ce,cf,d0,d1,d2,d3,d4,d5
  //   ,d6,d7,d8,d9,da,db,dc,dd,de,df,e0,e1,e2,e3,e4,e5,e6,e7,e8,e9,ea
  //   ,eb,ec,ed,ee,ef,f0,f1,f2,f3,f4,f5,f6,f7,f8,f9,fa,fb,fc,fd,fe,ff
  //   ,0,2,2,6,4,a,6,e,8,12,a,16,c,1a,e,1e,10,22,12,26,14,2a,16,2e,18
  //   ,32,1a,36,1c,3a,1e,3e,20,42,22,46,24,4a,26,4e,28,52,2a,56,2c,5a
  //   ,2e,5e,30,62,32,66,34,6a,36,6e,38,72,3a,76,3c,7a,3e,7e,40,82,42
  //   ,86,44,8a,46,8e,48,92,4a,96,4c,9a,4e,9e,50,a2,52,a6,54,aa,56,ae
  //   ,58,b2,5a,b6,5c,ba,5e,be,60,c2,62,c6,64,ca,66,ce,68,d2,6a,d6,6c
  //   ,da,6e,de,70,e2,72,e6,74,ea,76,ee,78,f2,7a,f6,7c,fa,7e,fe,80,102
  //   ,82,106,84,10a,86,10e,88,112,8a,116,8c,11a,8e,11e,90,122,92,126
  //   ,94,12a,96,12e,98,132,9a,136,9c,13a,9e,13e,a0,142,a2,146,a4,14a
  //   ,a6,14e,a8,152,aa,156,ac,15a,ae,15e,b0,162,b2,166,b4,16a,b6,16e
  //   ,b8,172,ba,176,bc,17a,be,17e,c0,182,c2,186,c4,18a,c6,18e,c8,192
  //   ,ca,196,cc,19a,ce,19e,d0,1a2,d2,1a6,d4,1aa,d6,1ae,d8,1b2,da,1b6
  //   ,dc,1ba,de,1be,e0,1c2,e2,1c6,e4,1ca,e6,1ce,e8,1d2,ea,1d6,ec,1da
  //   ,ee,1de,f0,1e2,f2,1e6,f4,1ea,f6,1ee,f8,1f2,fa,1f6,fc,1fa,fe,1fe
  //   ,0,3,6,3,c,f,6,15,18,9,1e,21,c,27,2a,f,30,33,12,39,3c,15,42,45
  //   ,18,4b,4e,1b,54,57,1e,5d,60,21,66,69,24,6f,72,27,78,7b,2a,81,84
  //   ,2d,8a,8d,30,93,96,33,9c,9f,36,a5,a8,39,ae,b1,3c,b7,ba,3f,c0,c3
  //   ,42,c9,cc,45,d2,d5,48,db,de,4b,e4,e7,4e,ed,f0,51,f6,f9,54,ff,102
  //   ,57,108,10b,5a,111,114,5d,11a,11d,60,123,126,63,12c,12f,66,135
  //   ,138,69,13e,141,6c,147,14a,6f,150,153,72,159,15c,75,162,165,78
  //   ,16b,16e,7b,174,177,7e,17d,180,81,186,189,84,18f,192,87,198,19b
  //   ,8a,1a1,1a4,8d,1aa,1ad,90,1b3,1b6,93,1bc,1bf,96,1c5,1c8,99,1ce
  //   ,1d1,9c,1d7,1da,9f,1e0,1e3,a2,1e9,1ec,a5,1f2,1f5,a8,1fb,1fe,ab
  //   ,204,207,ae,20d,210,b1,216,219,b4,21f,222,b7,228,22b,ba,231,234
  //   ,bd,23a,23d,c0,243,246,c3,24c,24f,c6,255,258,c9,25e,261,cc,267
  //   ,26a,cf,270,273,d2,279,27c,d5,282,285,d8,28b,28e,db,294,297,de
  //   ,29d,2a0,e1,2a6,2a9,e4,2af,2b2,e7,2b8,2bb,ea,2c1,2c4,ed,2ca,2cd
  //   ,f0,2d3,2d6,f3,2dc,2df,f6,2e5,2e8,f9,2ee,2f1,fc,2f7,2fa,ff,0,4,4
  //   ,c,4,14,c,1c,8,24,14,2c,c,34,1c,3c,10,44,24,4c,14,54,2c,5c,18
  //   ,64,34,6c,1c,74,3c,7c,20,84,44,8c,24,94,4c,9c,28,a4,54,ac,2c,b4
  //   ,5c,bc,30,c4,64,cc,34,d4,6c,dc,38,e4,74,ec,3c,f4,7c,fc,40,104
  //   ,84,10c,44,114,8c,11c,48,124,94,12c,4c,134,9c,13c,50,144,a4,14c
  //   ,54,154,ac,15c,58,164,b4,16c,5c,174,bc,17c,60,184,c4,18c,64,194
  //   ,cc,19c,68,1a4,d4,1ac,6c,1b4,dc,1bc,70,1c4,e4,1cc,74,1d4,ec,1dc
  //   ,78,1e4,f4,1ec,7c,1f4,fc,1fc,80,204,104,20c,84,214,10c,21c,88
  //   ,224,114,22c,8c,234,11c,23c,90,244,124,24c,94,254,12c,25c,98,264
  //   ,134,26c,9c,274,13c,27c,a0,284,144,28c,a4,294,14c,29c,a8,2a4,154
  //   ,2ac,ac,2b4,15c,2bc,b0,2c4,164,2cc,b4,2d4,16c,2dc,b8,2e4,174,2ec
  //   ,bc,2f4,17c,2fc,c0,304,184,30c,c4,314,18c,31c,c8,324,194,32c,cc
  //   ,334,19c,33c,d0,344,1a4,34c,d4,354,1ac,35c,d8,364,1b4,36c,dc,374
  //   ,1bc,37c,e0,384,1c4,38c,e4,394,1cc,39c,e8,3a4,1d4,3ac,ec,3b4,1dc
  //   ,3bc,f0,3c4,1e4,3cc,f4,3d4,1ec,3dc,f8,3e4,1f4,3ec,fc,3f4,1fc,3fc
  //   ,0,5,a,f,14,5,1e,23,28,2d,a,37,3c,41,46,f,50,55,5a,5f,14,69,6e
  //   ,73,78,19,82,87,8c,91,1e,9b,a0,a5,aa,23,b4,b9,be,c3,28,cd,d2,d7
  //   ,dc,2d,e6,eb,f0,f5,32,ff,104,109,10e,37,118,11d,122,127,3c,131
  //   ,136,13b,140,41,14a,14f,154,159,46,163,168,16d,172,4b,17c,181
  //   ,186,18b,50,195,19a,19f,1a4,55,1ae,1b3,1b8,1bd,5a,1c7,1cc,1d1
  //   ,1d6,5f,1e0,1e5,1ea,1ef,64,1f9,1fe,203,208,69,212,217,21c,221
  //   ,6e,22b,230,235,23a,73,244,249,24e,253,78,25d,262,267,26c,7d,276
  //   ,27b,280,285,82,28f,294,299,29e,87,2a8,2ad,2b2,2b7,8c,2c1,2c6
  //   ,2cb,2d0,91,2da,2df,2e4,2e9,96,2f3,2f8,2fd,302,9b,30c,311,316
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  //   I/O
  //   LoadValue
  //   Registers
  //   ALU
  //   contents of exponent (hex, n*v repeats v):
  //   1,0,a0000,a00000,0,40000,0,0,9*1,2,4,8,10,20,40,80,1,3,9,1b,51
  //   ,f3,d9,8b,1,4,10,40,4*0,1,5,19,7d,71,35,9,2d,1,6,24,d8,10,60,40
  //   ,80,1,7,31,57,61,a7,91,f7,0,0,0,1,0,0,0,1,0,1,5*0,1,0,0,0,1,5*0
  //   ,1,7*0,1,0,0,0,1,0,1,0,0,0,1,0,1,0,0,0,1,13*0,1,0,0,0,1,5*0,1
  //   ,0,1,9*0,1,0,1,5*0,1,5*0,1,0,0,0,1,5*0,1,5*0,1,0,1,9*0,1,0,1,0,0,0
  //   ,1,0,1,11*0,1,11*0,1,0,0,0,1,0,1,0,0,0,1,5*0,1,0,1,9*0,1
  //   Processing States
  //   Result Showing States
  //   Flags
  //   contents of isPrime (hex, n*v repeats v):
  //   0,0,1,1,0,1,0,1,0,0,0,1,0,1,0,0,0,1,0,1,0,0,0,1,5*0,1,0,1,5*0
  //   ,1,0,0,0,1,0,1,0,0,0,1,5*0,1,5*0,1,0,1,5*0,1,0,0,0,1,0,1,5*0,1
  //   ,0,0,0,1,5*0,1,7*0,1,0,0,0,1,0,1,0,0,0,1,0,1,0,0,0,1,13*0,1,0,0,0
  //   ,1,5*0,1,0,1,9*0,1,0,1,5*0,1,5*0,1,0,0,0,1,5*0,1,5*0,1,0,1,9*0
  //   ,1,0,1,0,0,0,1,0,1,11*0,1,11*0,1,0,0,0,1,0,1,0,0,0,1,5*0,1,0,1
  //   ,9*0,1
  //   Team - Minecraft Enjoyer
  //   6733285921	อนรรฆวี ชูจินดา (ผู้พัฒนาวงจรหลัก)
  //   6733143421 ป้อมบุญ ป้อมบุญมี (ผู้พัฒนาวงจรหลัก)
  //   6733050721	ชิติพัฒน์ ภู่ทอง
  //   6733013521 กฤษฎา ลิ้มศรีประพันธ์
endmodule

/* Test case 01_P01T01:
M N progIN reset progLoad start result clk valid done output
0 0 0 0 0 0 0 0 x x x
0 0 0 0 0 0 0 1 x x x
0 0 0 1 0 0 0 0 x x x
0 0 0 1 0 0 0 1 0 0 x
0 0 0 0 0 0 0 0 0 0 x
0 0 0 0 0 0 0 1 0 0 x
0 0 0 0 0 0 0 0 0 0 x
0 0 0 0 0 0 0 1 0 0 x
0 0 0 0 0 0 0 0 0 0 x
0 0 0 0 0 0 0 1 0 0 x
0 0 0 0 0 0 0 0 0 0 x
0 0 0 0 0 0 0 1 0 0 x
0 0 0 0 0 0 0 0 0 0 x
0 0 0 0 0 0 0 1 0 0 x
0 0 0 0 0 0 0 0 0 0 x
0 0 0 0 0 0 0 1 0 0 x
0 0 0 0 0 0 0 0 0 0 x
0 0 0 0 0 0 0 1 0 0 x
0 0 0 0 0 0 0 0 0 0 x
0 0 0 0 0 0 0 1 0 0 x
0 0 0 0 0 0 0 0 0 0 x
0 0 0 0 0 0 0 1 0 0 x
0 0 0 0 0 0 0 0 0 0 x
0 0 0 0 0 0 0 1 0 0 x
0 0 0 0 0 0 0 0 0 0 x
0 0 0 0 0 0 0 1 0 0 x
0 0 0 0 0 0 0 0 0 0 x
0 0 0 0 0 0 0 1 0 0 x
0 0 0 0 0 0 0 0 0 0 x
0 0 0 0 0 0 0 1 0 0 x
0 0 0 0 0 0 0 0 0 0 x
0 0 0 0 0 0 0 1 0 0 x
0 0 0 0 0 0 0 0 0 0 x
0 0 0 0 0 0 0 1 0 0 x
0 0 0 0 0 0 0 0 0 0 x
0 0 0 0 0 0 0 1 0 0 x
0 0 0 0 0 0 0 0 0 0 x
0 0 0 0 0 0 0 1 0 0 x
0 0 0 0 0 0 0 0 0 0 x
0 0 0 0 0 0 0 1 0 0 x
0 0 0 0 0 0 0 0 0 0 x
0 0 0 0 0 0 0 1 0 0 x
0 0 271 0 1 0 0 0 0 0 x
0 0 271 0 1 0 0 1 0 0 x
0 0 565 0 1 0 0 0 0 0 x
0 0 565 0 1 0 0 1 0 0 x
0 0 4352 0 1 0 0 0 0 0 x
0 0 4352 0 1 0 0 1 0 0 x
0 0 2819 0 1 0 0 0 0 0 x
0 0 2819 0 1 0 0 1 0 0 x
0 0 7936 0 1 0 0 0 0 0 x
0 0 7936 0 1 0 0 1 0 0 x
0 0 0 0 0 1 0 0 0 0 x
0 0 0 0 0 1 0 1 0 0 x
0 0 0 0 0 0 0 0 x 0 x
0 0 0 0 0 0 0 1 x 0 x
0 0 0 0 0 0 0 0 x 0 x
0 0 0 0 0 0 0 1 x 0 x
0 0 0 0 0 0 0 0 x 0 x
0 0 0 0 0 0 0 1 x 0 x
0 0 0 0 0 0 0 0 x 0 x
0 0 0 0 0 0 0 1 x 0 x
0 0 0 0 0 0 0 0 x 0 x
0 0 0 0 0 0 0 1 x 0 x
0 0 0 0 0 0 0 0 x 0 x
0 0 0 0 0 0 0 1 x 0 x
0 0 0 0 0 0 0 0 x 0 x
0 0 0 0 0 0 0 1 x 0 x
0 0 0 0 0 0 0 0 x 0 x
0 0 0 0 0 0 0 1 x 0 x
0 0 0 0 0 0 0 0 x 0 x
0 0 0 0 0 0 0 1 x 0 x
0 0 0 0 0 0 0 0 x 0 x
0 0 0 0 0 0 0 1 x 0 x
0 0 0 0 0 0 0 0 x 0 x
0 0 0 0 0 0 0 1 x 0 x
0 0 0 0 0 0 0 0 x 0 x
0 0 0 0 0 0 0 1 x 0 x
0 0 0 0 0 0 0 0 x 0 x
0 0 0 0 0 0 0 1 x 0 x
0 0 0 0 0 0 0 0 x 0 x
0 0 0 0 0 0 0 1 x 0 x
0 0 0 0 0 0 0 0 x 0 x
0 0 0 0 0 0 0 1 x 0 x
0 0 0 0 0 0 0 0 x 0 x
0 0 0 0 0 0 0 1 x 0 x
0 0 0 0 0 0 0 0 x 0 x
0 0 0 0 0 0 0 1 x 0 x
0 0 0 0 0 0 0 0 x 0 x
0 0 0 0 0 0 0 1 x 0 x
0 0 0 0 0 0 0 0 x 0 x
0 0 0 0 0 0 0 1 x 0 x
0 0 0 0 0 0 0 0 x 0 x
0 0 0 0 0 0 0 1 x 0 x
0 0 0 0 0 0 0 0 x 0 x
0 0 0 0 0 0 0 1 x 0 x
0 0 0 0 0 0 0 0 x 0 x
0 0 0 0 0 0 0 1 x 0 x
0 0 0 0 0 0 0 0 x 0 x
0 0 0 0 0 0 0 1 x 0 x
0 0 0 0 0 0 0 0 x 0 x
0 0 0 0 0 0 0 1 x 0 x
0 0 0 0 0 0 0 0 x 0 x
0 0 0 0 0 0 0 1 x 0 x
0 0 0 0 0 0 0 0 x 0 x
0 0 0 0 0 0 0 1 1 0 x
0 0 0 0 0 0 1 0 1 0 x
0 0 0 0 0 0 1 1 1 0 0
0 0 0 0 0 0 0 0 1 0 0
0 0 0 0 0 0 0 1 1 0 0
0 0 0 0 0 0 0 0 1 0 0
0 0 0 0 0 0 0 1 1 0 0
0 0 0 0 0 0 0 0 1 0 0
0 0 0 0 0 0 0 1 1 0 68
0 0 0 0 0 0 0 0 1 0 68
0 0 0 0 0 0 0 1 1 0 0
0 0 0 0 0 0 0 0 1 0 0
0 0 0 0 0 0 0 1 1 0 0
0 0 0 0 0 0 0 0 1 0 0
0 0 0 0 0 0 0 1 1 0 0
0 0 0 0 0 0 0 0 1 0 0
0 0 0 0 0 0 0 1 1 0 0
0 0 0 0 0 0 0 0 1 0 0
0 0 0 0 0 0 0 1 1 0 0
0 0 0 0 0 0 0 0 1 0 0
0 0 0 0 0 0 0 1 1 0 0
0 0 0 0 0 0 0 0 1 0 0
0 0 0 0 0 0 0 1 1 0 0
0 0 0 0 0 0 0 0 1 0 0
0 0 0 0 0 0 0 1 1 0 0
0 0 0 0 0 0 0 0 1 0 0
0 0 0 0 0 0 0 1 1 0 0
0 0 0 0 0 0 0 0 1 0 0
0 0 0 0 0 0 0 1 1 0 0
0 0 0 0 0 0 0 0 1 0 0
0 0 0 0 0 0 0 1 1 0 0
0 0 0 0 0 0 0 0 1 0 0
0 0 0 0 0 0 0 1 1 0 0
0 0 0 0 0 0 0 0 1 0 0
0 0 0 0 0 0 0 1 1 1 x
0 0 0 0 0 0 0 0 1 1 x
0 0 0 0 0 0 0 1 1 1 x
0 0 0 0 0 0 0 0 1 1 x
*/

/* Test case 07_P06T02:
M N progIN reset progLoad start result clk valid done output
0 0 0 0 0 0 0 0 x x x
0 0 0 0 0 0 0 1 x x x
0 0 0 1 0 0 0 0 x x x
0 0 0 1 0 0 0 1 0 0 x
0 0 0 0 0 0 0 0 0 0 x
0 0 0 0 0 0 0 1 0 0 x
0 0 0 0 0 0 0 0 0 0 x
0 0 0 0 0 0 0 1 0 0 x
0 0 0 0 0 0 0 0 0 0 x
0 0 0 0 0 0 0 1 0 0 x
0 0 0 0 0 0 0 0 0 0 x
0 0 0 0 0 0 0 1 0 0 x
0 0 0 0 0 0 0 0 0 0 x
0 0 0 0 0 0 0 1 0 0 x
0 0 0 0 0 0 0 0 0 0 x
0 0 0 0 0 0 0 1 0 0 x
0 0 0 0 0 0 0 0 0 0 x
0 0 0 0 0 0 0 1 0 0 x
0 0 0 0 0 0 0 0 0 0 x
0 0 0 0 0 0 0 1 0 0 x
0 0 0 0 0 0 0 0 0 0 x
0 0 0 0 0 0 0 1 0 0 x
0 0 0 0 0 0 0 0 0 0 x
0 0 0 0 0 0 0 1 0 0 x
0 0 0 0 0 0 0 0 0 0 x
0 0 0 0 0 0 0 1 0 0 x
0 0 0 0 0 0 0 0 0 0 x
0 0 0 0 0 0 0 1 0 0 x
0 0 0 0 0 0 0 0 0 0 x
0 0 0 0 0 0 0 1 0 0 x
0 0 0 0 0 0 0 0 0 0 x
0 0 0 0 0 0 0 1 0 0 x
0 0 0 0 0 0 0 0 0 0 x
0 0 0 0 0 0 0 1 0 0 x
0 0 0 0 0 0 0 0 0 0 x
0 0 0 0 0 0 0 1 0 0 x
0 0 0 0 0 0 0 0 0 0 x
0 0 0 0 0 0 0 1 0 0 x
0 0 0 0 0 0 0 0 0 0 x
0 0 0 0 0 0 0 1 0 0 x
0 0 0 0 0 0 0 0 0 0 x
0 0 0 0 0 0 0 1 0 0 x
0 0 1792 0 1 0 0 0 0 0 x
0 0 1792 0 1 0 0 1 0 0 x
0 0 1536 0 1 0 0 0 0 0 x
0 0 1536 0 1 0 0 1 0 0 x
0 0 2817 0 1 0 0 0 0 0 x
0 0 2817 0 1 0 0 1 0 0 x
0 0 2048 0 1 0 0 0 0 0 x
0 0 2048 0 1 0 0 1 0 0 x
0 0 1536 0 1 0 0 0 0 0 x
0 0 1536 0 1 0 0 1 0 0 x
0 0 2818 0 1 0 0 0 0 0 x
0 0 2818 0 1 0 0 1 0 0 x
0 0 1024 0 1 0 0 0 0 0 x
0 0 1024 0 1 0 0 1 0 0 x
0 0 2561 0 1 0 0 0 0 0 x
0 0 2561 0 1 0 0 1 0 0 x
0 0 4864 0 1 0 0 0 0 0 x
0 0 4864 0 1 0 0 1 0 0 x
0 0 2819 0 1 0 0 0 0 0 x
0 0 2819 0 1 0 0 1 0 0 x
0 0 2561 0 1 0 0 0 0 0 x
0 0 2561 0 1 0 0 1 0 0 x
0 0 5120 0 1 0 0 0 0 0 x
0 0 5120 0 1 0 0 1 0 0 x
0 0 2820 0 1 0 0 0 0 0 x
0 0 2820 0 1 0 0 1 0 0 x
0 0 7936 0 1 0 0 0 0 0 x
0 0 7936 0 1 0 0 1 0 0 x
15 7 0 0 0 1 0 0 0 0 x
15 7 0 0 0 1 0 1 0 0 x
15 7 0 0 0 0 0 0 x 0 x
15 7 0 0 0 0 0 1 x 0 x
15 7 0 0 0 0 0 0 x 0 x
15 7 0 0 0 0 0 1 x 0 x
15 7 0 0 0 0 0 0 x 0 x
15 7 0 0 0 0 0 1 x 0 x
15 7 0 0 0 0 0 0 x 0 x
15 7 0 0 0 0 0 1 x 0 x
15 7 0 0 0 0 0 0 x 0 x
15 7 0 0 0 0 0 1 x 0 x
15 7 0 0 0 0 0 0 x 0 x
15 7 0 0 0 0 0 1 x 0 x
15 7 0 0 0 0 0 0 x 0 x
15 7 0 0 0 0 0 1 x 0 x
15 7 0 0 0 0 0 0 x 0 x
15 7 0 0 0 0 0 1 x 0 x
15 7 0 0 0 0 0 0 x 0 x
15 7 0 0 0 0 0 1 x 0 x
15 7 0 0 0 0 0 0 x 0 x
15 7 0 0 0 0 0 1 x 0 x
15 7 0 0 0 0 0 0 x 0 x
15 7 0 0 0 0 0 1 x 0 x
15 7 0 0 0 0 0 0 x 0 x
15 7 0 0 0 0 0 1 x 0 x
15 7 0 0 0 0 0 0 x 0 x
15 7 0 0 0 0 0 1 x 0 x
15 7 0 0 0 0 0 0 x 0 x
15 7 0 0 0 0 0 1 x 0 x
15 7 0 0 0 0 0 0 x 0 x
15 7 0 0 0 0 0 1 x 0 x
15 7 0 0 0 0 0 0 x 0 x
15 7 0 0 0 0 0 1 x 0 x
15 7 0 0 0 0 0 0 x 0 x
15 7 0 0 0 0 0 1 x 0 x
15 7 0 0 0 0 0 0 x 0 x
15 7 0 0 0 0 0 1 x 0 x
15 7 0 0 0 0 0 0 x 0 x
15 7 0 0 0 0 0 1 x 0 x
15 7 0 0 0 0 0 0 x 0 x
0 0 0 0 0 0 0 1 x 0 x
0 0 0 0 0 0 0 0 x 0 x
0 0 0 0 0 0 0 1 x 0 x
0 0 0 0 0 0 0 0 x 0 x
0 0 0 0 0 0 0 1 x 0 x
0 0 0 0 0 0 0 0 x 0 x
0 0 0 0 0 0 0 1 x 0 x
0 0 0 0 0 0 0 0 x 0 x
0 0 0 0 0 0 0 1 x 0 x
0 0 0 0 0 0 0 0 x 0 x
0 0 0 0 0 0 0 1 x 0 x
0 0 0 0 0 0 0 0 x 0 x
0 0 0 0 0 0 0 1 1 0 x
0 0 0 0 0 0 1 0 1 0 0
0 0 0 0 0 0 1 1 1 0 0
0 0 0 0 0 0 0 0 1 0 0
0 0 0 0 0 0 0 1 1 0 15
0 0 0 0 0 0 0 0 1 0 15
0 0 0 0 0 0 0 1 1 0 7
0 0 0 0 0 0 0 0 1 0 7
0 0 0 0 0 0 0 1 1 0 105
0 0 0 0 0 0 0 0 1 0 105
0 0 0 0 0 0 0 1 1 0 2
0 0 0 0 0 0 0 0 1 0 2
0 0 0 0 0 0 0 1 1 0 0
0 0 0 0 0 0 0 0 1 0 0
0 0 0 0 0 0 0 1 1 0 0
0 0 0 0 0 0 0 0 1 0 0
0 0 0 0 0 0 0 1 1 0 0
0 0 0 0 0 0 0 0 1 0 0
0 0 0 0 0 0 0 1 1 0 0
0 0 0 0 0 0 0 0 1 0 0
0 0 0 0 0 0 0 1 1 0 0
0 0 0 0 0 0 0 0 1 0 0
0 0 0 0 0 0 0 1 1 0 0
0 0 0 0 0 0 0 0 1 0 0
0 0 0 0 0 0 0 1 1 0 0
0 0 0 0 0 0 0 0 1 0 0
0 0 0 0 0 0 0 1 1 0 0
0 0 0 0 0 0 0 0 1 0 0
0 0 0 0 0 0 0 1 1 0 0
0 0 0 0 0 0 0 0 1 0 0
0 0 0 0 0 0 0 1 1 0 0
0 0 0 0 0 0 0 0 1 0 0
0 0 0 0 0 0 0 1 1 0 0
0 0 0 0 0 0 0 0 1 0 0
0 0 0 0 0 0 0 1 1 1 x
0 0 0 0 0 0 0 0 1 1 x
0 0 0 0 0 0 0 1 1 1 x
0 0 0 0 0 0 0 0 1 1 x
*/

/* Test case 02_P01T2:
M N progIN reset progLoad start result clk valid done output
0 0 0 0 0 0 0 0 x x x
0 0 0 0 0 0 0 1 x x x
0 0 0 1 0 0 0 0 x x x
0 0 0 1 0 0 0 1 0 0 x
0 0 0 0 0 0 0 0 0 0 x
0 0 0 0 0 0 0 1 0 0 x
0 0 0 0 0 0 0 0 0 0 x
0 0 0 0 0 0 0 1 0 0 x
0 0 0 0 0 0 0 0 0 0 x
0 0 0 0 0 0 0 1 0 0 x
0 0 0 0 0 0 0 0 0 0 x
0 0 0 0 0 0 0 1 0 0 x
0 0 0 0 0 0 0 0 0 0 x
0 0 0 0 0 0 0 1 0 0 x
0 0 0 0 0 0 0 0 0 0 x
0 0 0 0 0 0 0 1 0 0 x
0 0 0 0 0 0 0 0 0 0 x
0 0 0 0 0 0 0 1 0 0 x
0 0 0 0 0 0 0 0 0 0 x
0 0 0 0 0 0 0 1 0 0 x
0 0 0 0 0 0 0 0 0 0 x
0 0 0 0 0 0 0 1 0 0 x
0 0 0 0 0 0 0 0 0 0 x
0 0 0 0 0 0 0 1 0 0 x
0 0 0 0 0 0 0 0 0 0 x
0 0 0 0 0 0 0 1 0 0 x
0 0 0 0 0 0 0 0 0 0 x
0 0 0 0 0 0 0 1 0 0 x
0 0 0 0 0 0 0 0 0 0 x
0 0 0 0 0 0 0 1 0 0 x
0 0 0 0 0 0 0 0 0 0 x
0 0 0 0 0 0 0 1 0 0 x
0 0 0 0 0 0 0 0 0 0 x
0 0 0 0 0 0 0 1 0 0 x
0 0 0 0 0 0 0 0 0 0 x
0 0 0 0 0 0 0 1 0 0 x
0 0 0 0 0 0 0 0 0 0 x
0 0 0 0 0 0 0 1 0 0 x
0 0 0 0 0 0 0 0 0 0 x
0 0 0 0 0 0 0 1 0 0 x
0 0 0 0 0 0 0 0 0 0 x
0 0 0 0 0 0 0 1 0 0 x
0 0 271 0 1 0 0 0 0 0 x
0 0 271 0 1 0 0 1 0 0 x
0 0 565 0 1 0 0 0 0 0 x
0 0 565 0 1 0 0 1 0 0 x
0 0 4352 0 1 0 0 0 0 0 x
0 0 4352 0 1 0 0 1 0 0 x
0 0 2819 0 1 0 0 0 0 0 x
0 0 2819 0 1 0 0 1 0 0 x
0 0 7936 0 1 0 0 0 0 0 x
0 0 7936 0 1 0 0 1 0 0 x
0 0 0 0 0 1 0 0 0 0 x
0 0 0 0 0 1 0 1 0 0 x
0 0 0 0 0 0 0 0 x 0 x
0 0 0 0 0 0 0 1 x 0 x
0 0 0 0 0 0 0 0 x 0 x
0 0 0 0 0 0 0 1 x 0 x
0 0 0 0 0 0 0 0 x 0 x
0 0 0 0 0 0 0 1 x 0 x
0 0 0 0 0 0 0 0 x 0 x
0 0 0 0 0 0 0 1 x 0 x
0 0 0 0 0 0 0 0 x 0 x
0 0 0 0 0 0 0 1 x 0 x
0 0 0 0 0 0 0 0 x 0 x
0 0 0 0 0 0 0 1 x 0 x
0 0 0 0 0 0 0 0 x 0 x
0 0 0 0 0 0 0 1 x 0 x
0 0 0 0 0 0 0 0 x 0 x
0 0 0 0 0 0 0 1 x 0 x
0 0 0 0 0 0 0 0 x 0 x
0 0 0 0 0 0 0 1 x 0 x
0 0 0 0 0 0 0 0 x 0 x
0 0 0 0 0 0 0 1 x 0 x
0 0 0 0 0 0 0 0 x 0 x
0 0 0 0 0 0 0 1 x 0 x
0 0 0 0 0 0 0 0 x 0 x
0 0 0 0 0 0 0 1 x 0 x
0 0 0 0 0 0 0 0 x 0 x
0 0 0 0 0 0 0 1 x 0 x
0 0 0 0 0 0 0 0 x 0 x
0 0 0 0 0 0 0 1 x 0 x
0 0 0 0 0 0 0 0 x 0 x
0 0 0 0 0 0 0 1 x 0 x
0 0 0 0 0 0 0 0 x 0 x
0 0 0 0 0 0 0 1 x 0 x
0 0 0 0 0 0 0 0 x 0 x
0 0 0 0 0 0 0 1 x 0 x
0 0 0 0 0 0 0 0 x 0 x
0 0 0 0 0 0 0 1 x 0 x
0 0 0 0 0 0 0 0 x 0 x
0 0 0 0 0 0 0 1 x 0 x
0 0 0 0 0 0 0 0 x 0 x
0 0 0 0 0 0 0 1 x 0 x
0 0 0 0 0 0 0 0 x 0 x
0 0 0 0 0 0 0 1 x 0 x
0 0 0 0 0 0 0 0 x 0 x
0 0 0 0 0 0 0 1 x 0 x
0 0 0 0 0 0 0 0 x 0 x
0 0 0 0 0 0 0 1 x 0 x
0 0 0 0 0 0 0 0 x 0 x
0 0 0 0 0 0 0 1 x 0 x
0 0 0 0 0 0 0 0 x 0 x
0 0 0 0 0 0 0 1 x 0 x
0 0 0 0 0 0 0 0 x 0 x
0 0 0 0 0 0 0 1 1 0 x
0 0 0 0 0 0 1 0 1 0 x
0 0 0 0 0 0 1 1 1 0 0
0 0 0 0 0 0 0 0 1 0 0
0 0 0 0 0 0 0 1 1 0 0
0 0 0 0 0 0 0 0 1 0 0
0 0 0 0 0 0 0 1 1 0 0
0 0 0 0 0 0 0 0 1 0 0
0 0 0 0 0 0 0 1 1 0 68
0 0 0 0 0 0 0 0 1 0 68
0 0 0 0 0 0 0 1 1 0 0
0 0 0 0 0 0 0 0 1 0 0
0 0 0 0 0 0 0 1 1 0 0
0 0 0 0 0 0 0 0 1 0 0
0 0 0 0 0 0 0 1 1 0 0
0 0 0 0 0 0 0 0 1 0 0
0 0 0 0 0 0 0 1 1 0 0
0 0 0 0 0 0 0 0 1 0 0
0 0 0 0 0 0 0 1 1 0 0
0 0 0 0 0 0 0 0 1 0 0
0 0 0 0 0 0 0 1 1 0 0
0 0 0 0 0 0 0 0 1 0 0
0 0 0 0 0 0 0 1 1 0 0
0 0 0 0 0 0 0 0 1 0 0
0 0 0 0 0 0 0 1 1 0 0
0 0 0 0 0 0 0 0 1 0 0
0 0 0 0 0 0 0 1 1 0 0
0 0 0 0 0 0 0 0 1 0 0
0 0 0 0 0 0 0 1 1 0 0
0 0 0 0 0 0 0 0 1 0 0
0 0 0 0 0 0 0 1 1 0 0
0 0 0 0 0 0 0 0 1 0 0
0 0 0 0 0 0 0 1 1 0 0
0 0 0 0 0 0 0 0 1 0 0
0 0 0 0 0 0 0 1 1 1 x
0 0 0 0 0 0 0 0 1 1 x
0 0 0 0 0 0 0 1 1 1 x
0 0 0 0 0 0 0 0 1 1 x
0 0 0 0 0 0 0 1 1 1 x
0 0 0 0 0 0 1 0 1 X x
0 0 0 0 0 0 1 1 1 X 0
0 0 0 0 0 0 0 0 1 0 0
0 0 0 0 0 0 0 1 1 0 0
0 0 0 0 0 0 0 0 1 0 0
0 0 0 0 0 0 0 1 1 0 0
0 0 0 0 0 0 0 0 1 0 0
0 0 0 0 0 0 0 1 1 0 68
0 0 0 0 0 0 0 0 1 0 68
0 0 0 0 0 0 0 1 1 0 0
0 0 0 0 0 0 0 0 1 0 0
0 0 0 0 0 0 0 1 1 0 0
0 0 0 0 0 0 0 0 1 0 0
0 0 0 0 0 0 0 1 1 0 0
0 0 0 0 0 0 0 0 1 0 0
0 0 0 0 0 0 0 1 1 0 0
0 0 0 0 0 0 0 0 1 0 0
0 0 0 0 0 0 0 1 1 0 0
0 0 0 0 0 0 0 0 1 0 0
0 0 0 0 0 0 0 1 1 0 0
0 0 0 0 0 0 0 0 1 0 0
0 0 0 0 0 0 0 1 1 0 0
0 0 0 0 0 0 0 0 1 0 0
0 0 0 0 0 0 0 1 1 0 0
0 0 0 0 0 0 0 0 1 0 0
0 0 0 0 0 0 0 1 1 0 0
0 0 0 0 0 0 0 0 1 0 0
0 0 0 0 0 0 0 1 1 0 0
0 0 0 0 0 0 0 0 1 0 0
0 0 0 0 0 0 0 1 1 0 0
0 0 0 0 0 0 0 0 1 0 0
0 0 0 0 0 0 0 1 1 0 0
0 0 0 0 0 0 0 0 1 0 0
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*/

/* Test case 08_P06T2:
M N progIN reset progLoad start result clk valid done output
0 0 0 0 0 0 0 0 x x x
0 0 0 0 0 0 0 1 x x x
0 0 0 1 0 0 0 0 x x x
0 0 0 1 0 0 0 1 0 0 x
0 0 0 0 0 0 0 0 0 0 x
0 0 0 0 0 0 0 1 0 0 x
0 0 0 0 0 0 0 0 0 0 x
0 0 0 0 0 0 0 1 0 0 x
0 0 0 0 0 0 0 0 0 0 x
0 0 0 0 0 0 0 1 0 0 x
0 0 0 0 0 0 0 0 0 0 x
0 0 0 0 0 0 0 1 0 0 x
0 0 0 0 0 0 0 0 0 0 x
0 0 0 0 0 0 0 1 0 0 x
0 0 0 0 0 0 0 0 0 0 x
0 0 0 0 0 0 0 1 0 0 x
0 0 0 0 0 0 0 0 0 0 x
0 0 0 0 0 0 0 1 0 0 x
0 0 0 0 0 0 0 0 0 0 x
0 0 0 0 0 0 0 1 0 0 x
0 0 0 0 0 0 0 0 0 0 x
0 0 0 0 0 0 0 1 0 0 x
0 0 0 0 0 0 0 0 0 0 x
0 0 0 0 0 0 0 1 0 0 x
0 0 0 0 0 0 0 0 0 0 x
0 0 0 0 0 0 0 1 0 0 x
0 0 0 0 0 0 0 0 0 0 x
0 0 0 0 0 0 0 1 0 0 x
0 0 0 0 0 0 0 0 0 0 x
0 0 0 0 0 0 0 1 0 0 x
0 0 0 0 0 0 0 0 0 0 x
0 0 0 0 0 0 0 1 0 0 x
0 0 0 0 0 0 0 0 0 0 x
0 0 0 0 0 0 0 1 0 0 x
0 0 0 0 0 0 0 0 0 0 x
0 0 0 0 0 0 0 1 0 0 x
0 0 0 0 0 0 0 0 0 0 x
0 0 0 0 0 0 0 1 0 0 x
0 0 0 0 0 0 0 0 0 0 x
0 0 0 0 0 0 0 1 0 0 x
0 0 0 0 0 0 0 0 0 0 x
0 0 0 0 0 0 0 1 0 0 x
0 0 1792 0 1 0 0 0 0 0 x
0 0 1792 0 1 0 0 1 0 0 x
0 0 1536 0 1 0 0 0 0 0 x
0 0 1536 0 1 0 0 1 0 0 x
0 0 2817 0 1 0 0 0 0 0 x
0 0 2817 0 1 0 0 1 0 0 x
0 0 2048 0 1 0 0 0 0 0 x
0 0 2048 0 1 0 0 1 0 0 x
0 0 1536 0 1 0 0 0 0 0 x
0 0 1536 0 1 0 0 1 0 0 x
0 0 2818 0 1 0 0 0 0 0 x
0 0 2818 0 1 0 0 1 0 0 x
0 0 1024 0 1 0 0 0 0 0 x
0 0 1024 0 1 0 0 1 0 0 x
0 0 2561 0 1 0 0 0 0 0 x
0 0 2561 0 1 0 0 1 0 0 x
0 0 4864 0 1 0 0 0 0 0 x
0 0 4864 0 1 0 0 1 0 0 x
0 0 2819 0 1 0 0 0 0 0 x
0 0 2819 0 1 0 0 1 0 0 x
0 0 2561 0 1 0 0 0 0 0 x
0 0 2561 0 1 0 0 1 0 0 x
0 0 5120 0 1 0 0 0 0 0 x
0 0 5120 0 1 0 0 1 0 0 x
0 0 2820 0 1 0 0 0 0 0 x
0 0 2820 0 1 0 0 1 0 0 x
0 0 7936 0 1 0 0 0 0 0 x
0 0 7936 0 1 0 0 1 0 0 x
15 7 0 0 0 1 0 0 0 0 x
15 7 0 0 0 1 0 1 0 0 x
15 7 0 0 0 0 0 0 x 0 x
15 7 0 0 0 0 0 1 x 0 x
15 7 0 0 0 0 0 0 x 0 x
15 7 0 0 0 0 0 1 x 0 x
15 7 0 0 0 0 0 0 x 0 x
15 7 0 0 0 0 0 1 x 0 x
15 7 0 0 0 0 0 0 x 0 x
15 7 0 0 0 0 0 1 x 0 x
15 7 0 0 0 0 0 0 x 0 x
15 7 0 0 0 0 0 1 x 0 x
15 7 0 0 0 0 0 0 x 0 x
15 7 0 0 0 0 0 1 x 0 x
15 7 0 0 0 0 0 0 x 0 x
15 7 0 0 0 0 0 1 x 0 x
15 7 0 0 0 0 0 0 x 0 x
15 7 0 0 0 0 0 1 x 0 x
15 7 0 0 0 0 0 0 x 0 x
15 7 0 0 0 0 0 1 x 0 x
15 7 0 0 0 0 0 0 x 0 x
15 7 0 0 0 0 0 1 x 0 x
15 7 0 0 0 0 0 0 x 0 x
15 7 0 0 0 0 0 1 x 0 x
15 7 0 0 0 0 0 0 x 0 x
15 7 0 0 0 0 0 1 x 0 x
15 7 0 0 0 0 0 0 x 0 x
15 7 0 0 0 0 0 1 x 0 x
15 7 0 0 0 0 0 0 x 0 x
15 7 0 0 0 0 0 1 x 0 x
15 7 0 0 0 0 0 0 x 0 x
15 7 0 0 0 0 0 1 x 0 x
15 7 0 0 0 0 0 0 x 0 x
15 7 0 0 0 0 0 1 x 0 x
15 7 0 0 0 0 0 0 x 0 x
15 7 0 0 0 0 0 1 x 0 x
15 7 0 0 0 0 0 0 x 0 x
15 7 0 0 0 0 0 1 x 0 x
15 7 0 0 0 0 0 0 x 0 x
15 7 0 0 0 0 0 1 x 0 x
15 7 0 0 0 0 0 0 x 0 x
0 0 0 0 0 0 0 1 x 0 x
0 0 0 0 0 0 0 0 x 0 x
0 0 0 0 0 0 0 1 x 0 x
0 0 0 0 0 0 0 0 x 0 x
0 0 0 0 0 0 0 1 x 0 x
0 0 0 0 0 0 0 0 x 0 x
0 0 0 0 0 0 0 1 x 0 x
0 0 0 0 0 0 0 0 x 0 x
0 0 0 0 0 0 0 1 x 0 x
0 0 0 0 0 0 0 0 x 0 x
0 0 0 0 0 0 0 1 x 0 x
0 0 0 0 0 0 0 0 x 0 x
0 0 0 0 0 0 0 1 1 0 x
0 0 0 0 0 0 1 0 1 0 0
0 0 0 0 0 0 1 1 1 0 0
0 0 0 0 0 0 0 0 1 0 0
0 0 0 0 0 0 0 1 1 0 15
0 0 0 0 0 0 0 0 1 0 15
0 0 0 0 0 0 0 1 1 0 7
0 0 0 0 0 0 0 0 1 0 7
0 0 0 0 0 0 0 1 1 0 105
0 0 0 0 0 0 0 0 1 0 105
0 0 0 0 0 0 0 1 1 0 2
0 0 0 0 0 0 0 0 1 0 2
0 0 0 0 0 0 0 1 1 0 0
0 0 0 0 0 0 0 0 1 0 0
0 0 0 0 0 0 0 1 1 0 0
0 0 0 0 0 0 0 0 1 0 0
0 0 0 0 0 0 0 1 1 0 0
0 0 0 0 0 0 0 0 1 0 0
0 0 0 0 0 0 0 1 1 0 0
0 0 0 0 0 0 0 0 1 0 0
0 0 0 0 0 0 0 1 1 0 0
0 0 0 0 0 0 0 0 1 0 0
0 0 0 0 0 0 0 1 1 0 0
0 0 0 0 0 0 0 0 1 0 0
0 0 0 0 0 0 0 1 1 0 0
0 0 0 0 0 0 0 0 1 0 0
0 0 0 0 0 0 0 1 1 0 0
0 0 0 0 0 0 0 0 1 0 0
0 0 0 0 0 0 0 1 1 0 0
0 0 0 0 0 0 0 0 1 0 0
0 0 0 0 0 0 0 1 1 0 0
0 0 0 0 0 0 0 0 1 0 0
0 0 0 0 0 0 0 1 1 0 0
0 0 0 0 0 0 0 0 1 0 0
0 0 0 0 0 0 0 1 1 1 x
0 0 0 0 0 0 0 0 1 1 x
0 0 0 0 0 0 0 1 1 1 x
0 0 0 0 0 0 0 0 1 1 x
0 0 0 0 0 0 0 1 1 1 x
0 0 0 1 0 0 0 0 x x x
0 0 0 1 0 0 0 1 0 0 x
0 0 0 0 0 0 0 0 0 0 x
0 0 0 0 0 0 0 1 0 0 x
0 0 0 0 0 0 0 0 0 0 x
0 0 0 0 0 0 0 1 0 0 x
0 0 0 0 0 0 0 0 0 0 x
0 0 0 0 0 0 0 1 0 0 x
0 0 0 0 0 0 0 0 0 0 x
0 0 0 0 0 0 0 1 0 0 x
0 0 0 0 0 0 0 0 0 0 x
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*/

/* Test case 03_P02T01:
M N progIN reset progLoad start result clk valid done output
0 0 0 0 0 0 0 0 x x x
0 0 0 0 0 0 0 1 x x x
0 0 0 1 0 0 0 0 x x x
0 0 0 1 0 0 0 1 0 0 x
0 0 0 0 0 0 0 0 0 0 x
0 0 0 0 0 0 0 1 0 0 x
0 0 0 0 0 0 0 0 0 0 x
0 0 0 0 0 0 0 1 0 0 x
0 0 0 0 0 0 0 0 0 0 x
0 0 0 0 0 0 0 1 0 0 x
0 0 0 0 0 0 0 0 0 0 x
0 0 0 0 0 0 0 1 0 0 x
0 0 0 0 0 0 0 0 0 0 x
0 0 0 0 0 0 0 1 0 0 x
0 0 0 0 0 0 0 0 0 0 x
0 0 0 0 0 0 0 1 0 0 x
0 0 0 0 0 0 0 0 0 0 x
0 0 0 0 0 0 0 1 0 0 x
0 0 0 0 0 0 0 0 0 0 x
0 0 0 0 0 0 0 1 0 0 x
0 0 0 0 0 0 0 0 0 0 x
0 0 0 0 0 0 0 1 0 0 x
0 0 0 0 0 0 0 0 0 0 x
0 0 0 0 0 0 0 1 0 0 x
0 0 0 0 0 0 0 0 0 0 x
0 0 0 0 0 0 0 1 0 0 x
0 0 0 0 0 0 0 0 0 0 x
0 0 0 0 0 0 0 1 0 0 x
0 0 0 0 0 0 0 0 0 0 x
0 0 0 0 0 0 0 1 0 0 x
0 0 0 0 0 0 0 0 0 0 x
0 0 0 0 0 0 0 1 0 0 x
0 0 0 0 0 0 0 0 0 0 x
0 0 0 0 0 0 0 1 0 0 x
0 0 0 0 0 0 0 0 0 0 x
0 0 0 0 0 0 0 1 0 0 x
0 0 0 0 0 0 0 0 0 0 x
0 0 0 0 0 0 0 1 0 0 x
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*/

/* Test case 08_P06T3:
M N progIN reset progLoad start result clk valid done output
0 0 0 0 0 0 0 0 x x x
0 0 0 0 0 0 0 1 x x x
0 0 0b0000100000111 0 1 0 0 0 0 0 x
0 0 0b0000100000111 0 1 0 0 1 0 0 x
0 0 0b0001000000100 0 1 0 0 0 0 0 x
0 0 0b0001000000100 0 1 0 0 1 0 0 x
0 0 0b0000000000100 0 1 0 0 0 0 0 x
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*/

/* Test case 04_P03T01:
M N progIN reset progLoad start result clk valid done output
0 0 0 0 0 0 0 0 x x x
0 0 0 0 0 0 0 1 x x x
0 0 0 1 0 0 0 0 x x x
0 0 0 1 0 0 0 1 0 0 x
0 0 0 0 0 0 0 0 0 0 x
0 0 0 0 0 0 0 1 0 0 x
0 0 0 0 0 0 0 0 0 0 x
0 0 0 0 0 0 0 1 0 0 x
0 0 0 0 0 0 0 0 0 0 x
0 0 0 0 0 0 0 1 0 0 x
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*/

/* Test case 1:
M N progIN reset progLoad start result clk valid done output
0 0 0 0 0 0 0 0 0 0 x
0 0 0 0 0 0 0 1 0 0 x
0 0 0 0 0 0 0 0 0 0 x
0 0 0 0 0 0 0 1 0 0 x
0 0 0 0 0 0 0 0 0 0 x
0 0 0 0 0 0 0 1 0 0 x
0 0 0 0 0 0 0 0 0 0 x
0 0 0 0 0 0 0 1 0 0 x
0 0 0 0 0 0 0 0 0 0 x
0 0 0 0 0 0 0 1 0 0 x
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*/

/* Test case 05_P04T01:
M N progIN reset progLoad start result clk valid done output
0 0 0 0 0 0 0 0 x x x
0 0 0 0 0 0 0 1 x x x
0 0 0 1 0 0 0 0 x x x
0 0 0 1 0 0 0 1 0 0 x
0 0 0 0 0 0 0 0 0 0 x
0 0 0 0 0 0 0 1 0 0 x
0 0 0 0 0 0 0 0 0 0 x
0 0 0 0 0 0 0 1 0 0 x
0 0 0 0 0 0 0 0 0 0 x
0 0 0 0 0 0 0 1 0 0 x
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*/

/* Test case 2:
M N progIN reset progLoad start result clk valid done output
0 0 0 0 0 0 0 0 x x x
0 0 0 0 0 0 0 1 x x x
0 0 0 1 0 0 0 0 x x x
0 0 0 1 0 0 0 1 0 0 x
0 0 0 0 0 0 0 0 0 0 x
0 0 0 0 0 0 0 1 0 0 x
0 0 0 0 0 0 0 0 0 0 x
0 0 0 0 0 0 0 1 0 0 x
0 0 0 0 0 0 0 0 0 0 x
0 0 0 0 0 0 0 1 0 0 x
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*/

/* Test case 06_P05T01:
M N progIN reset progLoad start result clk valid done output
0 0 0 0 0 0 0 0 x x x
0 0 0 0 0 0 0 1 x x x
0 0 0 1 0 0 0 0 x x x
0 0 0 1 0 0 0 1 0 0 x
0 0 0 0 0 0 0 0 0 0 x
0 0 0 0 0 0 0 1 0 0 x
0 0 0 0 0 0 0 0 0 0 x
0 0 0 0 0 0 0 1 0 0 x
0 0 0 0 0 0 0 0 0 0 x
0 0 0 0 0 0 0 1 0 0 x
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*/
