// Digital circuit Template.dig as structural Verilog
module Template (
  input  K,
  input  J,
  input  Clear,
  input  Clock,
  output Q,
  output Q_2
);

  wire and_1_out, and_2_out, and_3_out, and_4_out, multiplexer_1_out, multiplexer_2_out, multiplexer_3_out,
       nor_1_out, nor_2_out, not_1_out;

  and and_1 (and_1_out, Q, K, Clock);
  and and_2 (and_2_out, Clock, J, Q_2);
  nor nor_1 (nor_1_out, and_1_out, nor_2_out);
  nor nor_2 (nor_2_out, nor_1_out, and_2_out);
  not not_1 (not_1_out, Clock);
  Multiplexer multiplexer_1 (.sel(Clear), .in_0(nor_1_out), .in_1(1'b0), .out(multiplexer_1_out));
  Multiplexer multiplexer_2 (.sel(Clear), .in_0(not_1_out), .in_1(1'b1), .out(multiplexer_2_out));
  Multiplexer multiplexer_3 (.sel(Clear), .in_0(nor_2_out), .in_1(1'b1), .out(multiplexer_3_out));
  and and_3 (and_3_out, multiplexer_2_out, multiplexer_3_out);
  and and_4 (and_4_out, multiplexer_1_out, multiplexer_2_out);
  nor nor_3 (Q, and_3_out, Q_2);
  nor nor_4 (Q_2, Q, and_4_out);
endmodule

/* Test case:
K J \Clear Clock Q \Q
0 0 1 0 0 1
0 0 1 1 0 1
0 1 0 0 0 1
0 1 0 1 0 1
0 1 0 0 1 0
1 0 0 1 1 0
1 0 0 0 0 1
0 0 0 1 0 1
0 0 0 0 0 1
0 1 0 1 0 1
0 1 0 0 1 0
*/
