// Digital circuit Template.dig as structural Verilog
module Template (
  input  D,
  input  Clear,
  input  Clock,
  output Q,
  output Q_2
);

  wire multiplexer_1_out, nor_1_out, nor_2_out, nor_3_out, nor_4_out;

  Multiplexer multiplexer_1 (.sel(Clear), .in_0(D), .in_1(1'b0), .out(multiplexer_1_out));
  nor nor_1 (nor_1_out, nor_4_out, nor_2_out);
  nor nor_2 (nor_2_out, nor_1_out, Clock);
  nor nor_3 (nor_3_out, nor_2_out, Clock, nor_4_out);
  nor nor_4 (nor_4_out, nor_3_out, multiplexer_1_out);
  nor nor_5 (Q, nor_2_out, Q_2);
  nor nor_6 (Q_2, Q, nor_3_out);
endmodule
