// Digital circuit Template.dig as structural Verilog
module Template (
  input  T,
  input  Clock,
  output Q,
  output Q_2
);

  wire and_1_out, and_2_out, nor_2_out;

  not not_1 (Q, Q_2);
  and and_1 (and_1_out, T, Q_2, Clock);
  and and_2 (and_2_out, Clock, nor_2_out, T);
  nor nor_1 (Q_2, and_1_out, nor_2_out);
  nor nor_2 (nor_2_out, Q_2, and_2_out);

  // Other names for the same wires on the sheet: Q_n = Q_2

  // Notes on the sheet:
  //   Clock: Hz: 2
endmodule
