// Digital circuit item2.dig as structural Verilog
module item2 (
  input  [2:0] in0,
  input  [2:0] in1,
  input  addsubtract,
  output [2:0] out
);

  wire a0, a1, add_4_c_o, add_6_c_o, add_7_c_o, b0, b1, not_1_out, not_2_out;
  wire [2:0] add_3_s, add_5_s;

  Add add_1 (.a(in0[0]), .b(in0[1]), .c_i(in0[2]), .s(a0), .c_o(a1));
  not not_1 (not_1_out, b1);
  not not_2 (not_2_out, b0);
  Add add_2 (.a(in1[0]), .b(in1[1]), .c_i(in1[2]), .s(b0), .c_o(b1));
  Add add_3 (.a(b1), .b(a1), .c_i(add_4_c_o), .s(add_3_s[1]), .c_o(add_3_s[2]));
  Add add_4 (.a(b0), .b(a0), .c_i(1'b0), .s(add_3_s[0]), .c_o(add_4_c_o));
  Add add_5 (.a(1'b0), .b(1'b1), .c_i(add_6_c_o), .s(add_5_s[2]));  // open: c_o
  Add add_6 (.a(a1), .b(not_1_out), .c_i(add_7_c_o), .s(add_5_s[1]), .c_o(add_6_c_o));
  Add add_7 (.a(a0), .b(not_2_out), .c_i(1'b1), .s(add_5_s[0]), .c_o(add_7_c_o));
  Multiplexer #(.Bits(3)) multiplexer_1 (.sel(addsubtract), .in_0(add_3_s), .in_1(add_5_s), .out(out));
endmodule
